// Logisim project 2-1MUX.circ as structural Verilog: 1 circuit, main circuit main
module main (
  input  D0,
  input  D1,
  input  X,
  output Y
);

  wire and_1_out, and_2_out, not_1_out;

  not not_1 (not_1_out, X);
  // Probe on X
  // Probe on not_1_out
  and and_1 (and_1_out, D0, not_1_out);
  and and_2 (and_2_out, D1, X);
  or or_1 (Y, and_1_out, and_2_out);
endmodule
