// Logisim project 4-1MUX.circ as structural Verilog: 2 circuits, main circuit main
// 2-1MUX
module main (
  input  D0,
  input  D1,
  input  D2,
  input  D3,
  input  S0,
  input  S1,
  output Y
);

  wire _2_1MUX_2_y, _2_1MUX_y;

  _2 _2_1MUX (.D0(D0), .D1(D1), .X(S0), .Y(_2_1MUX_y));
  _2 _2_1MUX_2 (.D0(D2), .D1(D3), .X(S0), .Y(_2_1MUX_2_y));
  _2 _2_1MUX_3 (.D0(_2_1MUX_y), .D1(_2_1MUX_2_y), .X(S1), .Y(Y));
endmodule

module _2 (
  input  D0,
  input  D1,
  input  X,
  output Y
);

  wire and_1_out, and_2_out, not_1_out;

  not not_1 (not_1_out, X);
  and and_1 (and_1_out, D0, not_1_out);
  and and_2 (and_2_out, D1, X);
  or or_1 (Y, and_1_out, and_2_out);
endmodule
