// Logisim project checkcode.circ as structural Verilog: 1 circuit, main circuit main
module main (
  input  in_1,
  input  in_2,
  input  in_3,
  input  in_4,
  output out_5
);

  wire xor_1_out, xor_2_out;

  xor xor_1 (xor_1_out, in_1, in_2);
  xor xor_2 (xor_2_out, in_3, in_4);
  xor xor_3 (out_5, xor_1_out, xor_2_out);

  // Notes on the sheet:
  //   偶校验：使得原码中+校验位中1的个数为偶，奇校验在最后加一个 非门 即可
endmodule
