// Logisim project cmos_or.circ as structural Verilog: 1 circuit, main circuit cmos_or
module cmos_or (
  input  X,
  input  Y,
  output Z
);

  wire transistor_1_out, transistor_2_out;

  Transistor transistor_1 (.in(1'b1), .out(transistor_1_out), .gate(X));
  Transistor transistor_2 (.in(transistor_1_out), .out(transistor_2_out), .gate(Y));
  Transistor #(.\type ("n")) transistor_3 (.in(1'b0), .out(transistor_2_out), .gate(X));
  Transistor transistor_4 (.in(1'b1), .out(Z), .gate(transistor_2_out));
  Transistor #(.\type ("n")) transistor_5 (.in(1'b0), .out(Z), .gate(transistor_2_out));
  Transistor #(.\type ("n")) transistor_6 (.in(1'b0), .out(transistor_2_out), .gate(Y));

  // Notes on the sheet:
  //   P1
  //   P2
  //   N1
  //   或门实现电路
  //   P3
  //   N3
  //   N2
endmodule
