// Logisim project thinking2.circ as structural Verilog: 3 circuits, main circuit Main
module temp (
  input  [3:0] DATA,
  input  [1:0] S,
  output out_3
);

  wire _2MUX_2_y, _2MUX_y;

  _2mux _2MUX (.D0(DATA[0]), .D1(DATA[1]), .X(S[0]), .Y(_2MUX_y));
  _2mux _2MUX_2 (.D0(DATA[2]), .D1(DATA[3]), .X(S[0]), .Y(_2MUX_2_y));
  _2mux _2MUX_3 (.D0(_2MUX_y), .D1(_2MUX_2_y), .X(S[1]), .Y(out_3));

  // Notes on the sheet:
  //   构造4个DATA，DATA_i用于存放四个DATA的第i位
endmodule

module _2mux (
  input  D0,
  input  D1,
  input  X,
  output Y
);

  wire and_1_out, and_2_out, not_1_out;

  not not_1 (not_1_out, X);
  and and_1 (and_1_out, D0, not_1_out);
  and and_2 (and_2_out, D1, X);
  or or_1 (Y, and_1_out, and_2_out);
endmodule

module Main (
  input  in_1,
  input  in_2,
  input  input1,
  input  in_4,
  input  in_5,
  input  in_6,
  input  input2,
  input  in_8,
  input  in_9,
  input  in_10,
  input  input3,
  input  in_12,
  input  in_13,
  input  in_14,
  input  input4,
  input  in_16,
  input  [1:0] S,
  output [3:0] out_18
);

  temp temp_1 (.DATA({in_13, in_9, in_5, in_1}), .S(S), .out_3(out_18[3]));
  temp temp_2 (.DATA({in_14, in_10, in_6, in_2}), .S(S), .out_3(out_18[2]));
  temp temp_3 (.DATA({input4, input3, input2, input1}), .S(S), .out_3(out_18[1]));
  temp temp_4 (.DATA({in_16, in_12, in_8, in_4}), .S(S), .out_3(out_18[0]));

  // Notes on the sheet:
  //   存放每个input的第0位
  //   存放每个input的第3位
  //   存放每个input的第1位
  //   存放每个input的第2位
endmodule
