// Logisim project thinking3.circ as structural Verilog: 1 circuit, main circuit main
module main (
  input  in_1,
  input  in_2,
  input  in_3,
  input  in_4,
  output \校验位 
);

  wire xor_1_out, xor_2_out;

  xor xor_1 (xor_1_out, in_1, in_2);
  xor xor_2 (xor_2_out, in_3, in_4);
  xor xor_3 (\校验位 , xor_1_out, xor_2_out);

  // Notes on the sheet:
  //   偶校验：使得码中1个数位偶数
  //   奇校验的实现就在最后加一个非门就行
endmodule
