// Logisim project MOVE.circ as structural Verilog: 7 circuits, main circuit 8move
module _8move (
  input  [7:0] in_1,
  input  [2:0] in_2,
  input  \_0右移1左移 ,
  input  \_0逻辑1算数 ,
  output [7:0] out_5,
  output [7:0] out_6
);

  wire [7:0] left1_1_out_2, left2_1_out_2, left4_1_out_2, multiplexer_1_out, multiplexer_2_out,
       right1_1_out_3, right2_1_out_3, right4_1_out_3;

  RIGHT1 right1_1 (.in_1(in_1), .A_L(\_0逻辑1算数 ), .out_3(right1_1_out_3));
  LEFT1 left1_1 (.in_1(in_1), .out_2(left1_1_out_2));
  Multiplexer #(.select(2), .width(8), .enable("false")) multiplexer_1 (
    .in0(in_1), .in1(in_1), .in2(right1_1_out_3), .in3(left1_1_out_2), .out(multiplexer_1_out),
    .sel({in_2[0], \_0右移1左移 }));
  Multiplexer #(.select(2), .width(8), .enable("false")) multiplexer_2 (
    .in0(multiplexer_1_out), .in1(multiplexer_1_out), .in2(right2_1_out_3), .in3(left2_1_out_2),
    .out(multiplexer_2_out), .sel({in_2[1], \_0右移1左移 }));
  RIGHT2 right2_1 (.in_1(multiplexer_1_out), .A_L(\_0逻辑1算数 ), .out_3(right2_1_out_3));
  LEFT2 left2_1 (.in_1(multiplexer_1_out), .out_2(left2_1_out_2));
  RIGHT4 right4_1 (.in_1(multiplexer_2_out), .A_L(\_0逻辑1算数 ), .out_3(right4_1_out_3));
  LEFT4 left4_1 (.in_1(multiplexer_2_out), .out_2(left4_1_out_2));
  Multiplexer #(.select(2), .width(8), .enable("false")) multiplexer_3 (
    .in0(multiplexer_2_out), .in1(multiplexer_2_out), .in2(right4_1_out_3), .in3(left4_1_out_2), .out(out_5),
    .sel({in_2[2], \_0右移1左移 }));

  assign out_6 = out_5;

  // Other names for the same wires on the sheet: SHAMT[2:0] = in_2; L_R = \_0右移1左移 ; A_L = \_0逻辑1算数 ;
  //   INPUT[7:0] = in_1; OUTPUT[7:0] = out_5
endmodule

module LEFT4 (
  input  [7:0] in_1,
  output [7:0] out_2
);


  assign out_2 = {in_1[3:0], 4'b0000};
endmodule

module LEFT2 (
  input  [7:0] in_1,
  output [7:0] out_2
);


  assign out_2 = {in_1[5:0], 2'b00};
endmodule

module LEFT1 (
  input  [7:0] in_1,
  output [7:0] out_2
);


  assign out_2 = {in_1[6:0], 1'b0};
endmodule

module RIGHT4 (
  input  [7:0] in_1,
  input  A_L,
  output [7:0] out_3
);

  and and_1 (out_3[7], in_1[7], A_L);

  assign out_3[6:0] = {{3{out_3[7]}}, in_1[7:4]};
endmodule

module RIGHT2 (
  input  [7:0] in_1,
  input  A_L,
  output [7:0] out_3
);

  and and_1 (out_3[7], in_1[7], A_L);

  assign out_3[6:0] = {out_3[7], in_1[7:2]};
endmodule

module RIGHT1 (
  input  [7:0] in_1,
  input  A_L,
  output [7:0] out_3
);

  and and_1 (out_3[7], in_1[7], A_L);

  assign out_3[6:0] = in_1[7:1];
endmodule
