// Logisim project NJU.circ as structural Verilog: 1 circuit, main circuit main
module main (
);

  DotMatrix #(.matrixcols(16), .matrixrows(16)) dotmatrix_1 (
    .col0({16{1'b0}}), .col1(16'h1fe), .col2(16'h100), .col3(16'h548), .col4(16'h528), .col5(16'hf3e),
    .col6(16'h528), .col7(16'h548), .col8(16'h100), .col9(16'h1fe), .col10({16{1'b0}}), .col11(16'h10c),
    .col12(16'h130), .col13(16'h7c0), .col14(16'h130), .col15(16'h10c));
endmodule
