// Logisim project THINKING3_32BIT.circ as structural Verilog: 11 circuits, main circuit main
module main (
  input  [31:0] in_1,
  input  in_2,
  input  in_3,
  input  [4:0] in_4,
  output [31:0] out_5
);

  wire [31:0] l1_1_out_2, l2_1_out_2, l4_1_out_2, l8_1_out_2, l16_1_out_2, multiplexer_1_out,
       multiplexer_2_out, multiplexer_3_out, multiplexer_4_out, r1_1_out_3, r2_1_out_3, r4_1_out_3,
       r8_1_out_3, r16_1_out_3;

  R1 r1_1 (.in_1(in_1), .in_2(in_3), .out_3(r1_1_out_3));
  L1 l1_1 (.in_1(in_1), .out_2(l1_1_out_2));
  Multiplexer #(.select(2), .width(32), .enable("false")) multiplexer_1 (
    .in0(in_1), .in1(in_1), .in2(r1_1_out_3), .in3(l1_1_out_2), .out(multiplexer_1_out), .sel({in_4[0], in_2}));
  R2 r2_1 (.in_1(multiplexer_1_out), .in_2(in_3), .out_3(r2_1_out_3));
  L2 l2_1 (.in_1(multiplexer_1_out), .out_2(l2_1_out_2));
  Multiplexer #(.select(2), .width(32), .enable("false")) multiplexer_2 (
    .in0(multiplexer_1_out), .in1(multiplexer_1_out), .in2(r2_1_out_3), .in3(l2_1_out_2),
    .out(multiplexer_2_out), .sel({in_4[1], in_2}));
  R4 r4_1 (.in_1(multiplexer_2_out), .in_2(in_3), .out_3(r4_1_out_3));
  L4 l4_1 (.in_1(multiplexer_2_out), .out_2(l4_1_out_2));
  Multiplexer #(.select(2), .width(32), .enable("false")) multiplexer_3 (
    .in0(multiplexer_2_out), .in1(multiplexer_2_out), .in2(r4_1_out_3), .in3(l4_1_out_2),
    .out(multiplexer_3_out), .sel({in_4[2], in_2}));
  R8 r8_1 (.in_1(multiplexer_3_out), .in_2(in_3), .out_3(r8_1_out_3));
  L8 l8_1 (.in_1(multiplexer_3_out), .out_2(l8_1_out_2));
  Multiplexer #(.select(2), .width(32), .enable("false")) multiplexer_4 (
    .in0(multiplexer_3_out), .in1(multiplexer_3_out), .in2(r8_1_out_3), .in3(l8_1_out_2),
    .out(multiplexer_4_out), .sel({in_4[3], in_2}));
  R16 r16_1 (.in_1(multiplexer_4_out), .in_2(in_3), .out_3(r16_1_out_3));
  L16 l16_1 (.in_1(multiplexer_4_out), .out_2(l16_1_out_2));
  Multiplexer #(.select(2), .width(32), .enable("false")) multiplexer_5 (
    .in0(multiplexer_4_out), .in1(multiplexer_4_out), .in2(r16_1_out_3), .in3(l16_1_out_2), .out(out_5),
    .sel({in_4[4], in_2}));

  // Other names for the same wires on the sheet: SHAMT[4:0] = in_4; L_R = in_2; A_L = in_3; INPUT[31:0] = in_1;
  //   OUTPUT[31:0] = out_5
endmodule

module L1 (
  input  [31:0] in_1,
  output [31:0] out_2
);


  assign out_2 = {in_1[30:0], 1'b0};
endmodule

module L2 (
  input  [31:0] in_1,
  output [31:0] out_2
);


  assign out_2 = {in_1[29:0], 2'b00};
endmodule

module L4 (
  input  [31:0] in_1,
  output [31:0] out_2
);


  assign out_2 = {in_1[27:0], 4'b0000};
endmodule

module L8 (
  input  [31:0] in_1,
  output [31:0] out_2
);


  assign out_2 = {in_1[23:0], {8{1'b0}}};
endmodule

module L16 (
  input  [31:0] in_1,
  output [31:0] out_2
);


  assign out_2 = {in_1[15:0], {16{1'b0}}};
endmodule

module R1 (
  input  [31:0] in_1,
  input  in_2,
  output [31:0] out_3
);

  and and_1 (out_3[31], in_1[31], in_2);

  assign out_3[30:0] = in_1[31:1];
endmodule

module R2 (
  input  [31:0] in_1,
  input  in_2,
  output [31:0] out_3
);

  and and_1 (out_3[31], in_1[31], in_2);

  assign out_3[30:0] = {out_3[31], in_1[31:2]};
endmodule

module R4 (
  input  [31:0] in_1,
  input  in_2,
  output [31:0] out_3
);

  and and_1 (out_3[31], in_1[31], in_2);

  assign out_3[30:0] = {{3{out_3[31]}}, in_1[31:4]};
endmodule

module R8 (
  input  [31:0] in_1,
  input  in_2,
  output [31:0] out_3
);

  and and_1 (out_3[31], in_1[31], in_2);

  assign out_3[30:0] = {{7{out_3[31]}}, in_1[31:8]};
endmodule

module R16 (
  input  [31:0] in_1,
  input  in_2,
  output [31:0] out_3
);

  and and_1 (out_3[31], in_1[31], in_2);

  assign out_3[30:0] = {{15{out_3[31]}}, in_1[31:16]};
endmodule
