// Logisim project adder.circ as structural Verilog: 2 circuits, main circuit main
module main (
  input  in_1,
  input  [3:0] X,
  input  [3:0] Y,
  output [3:0] out_4,
  output out_5,
  output out_6,
  output \溢出标志OF ,
  output out_8
);

  wire \fulladder_1_cout_进位输出 , \fulladder_2_cout_进位输出 , \fulladder_3_cout_进位输出 , \fulladder_4_cout_进位输出 ;
  wire [3:0] xor_1_out;

  xor xor_1 (xor_1_out[0], Y[0], in_1);
  xor xor_2 (xor_1_out[1], Y[1], in_1);
  xor xor_3 (xor_1_out[2], Y[2], in_1);
  xor xor_4 (xor_1_out[3], Y[3], in_1);
  and and_1 (out_6, in_1, out_5);
  Hex_Digit_Display hex_digit_display_1 (.value(X));  // open: dp
  Hex_Digit_Display hex_digit_display_2 (.value(Y));  // open: dp
  fulladder fulladder_1 (
    .A(X[0]), .B(xor_1_out[0]), .Cin(in_1), .\F_本位 (out_4[0]), .\Cout_进位输出 (\fulladder_1_cout_进位输出 ));
  Hex_Digit_Display hex_digit_display_3 (.value({3'b000, out_5}));  // open: dp
  fulladder fulladder_2 (
    .A(X[1]), .B(xor_1_out[1]), .Cin(\fulladder_1_cout_进位输出 ), .\F_本位 (out_4[1]),
    .\Cout_进位输出 (\fulladder_2_cout_进位输出 ));
  Hex_Digit_Display hex_digit_display_4 (.value(out_4));  // open: dp
  fulladder fulladder_3 (
    .A(X[2]), .B(xor_1_out[2]), .Cin(\fulladder_2_cout_进位输出 ), .\F_本位 (out_4[2]),
    .\Cout_进位输出 (\fulladder_3_cout_进位输出 ));
  fulladder fulladder_4 (
    .A(X[3]), .B(xor_1_out[3]), .Cin(\fulladder_3_cout_进位输出 ), .\F_本位 (out_4[3]),
    .\Cout_进位输出 (\fulladder_4_cout_进位输出 ));
  xor xor_5 (out_5, \fulladder_4_cout_进位输出 , in_1);
  nand nand_1 (out_8, out_4[0], out_4[1], out_4[2], out_4[3], out_5);

  assign \溢出标志OF  = out_5;

  // Other names for the same wires on the sheet: COUT = out_5; C = in_1; OUTPUT[3:0] = out_4

  // Notes on the sheet:
  //   符号标志SF
  //   输出为1代表负数，输出为0代表正数
  //   输出为0代表没有溢出
  //   +/-
  //   output1
  //   =
  //   进位标志CF
  //   output3
  //   output4
  //   0标志位ZF
  //   不进位且输出位0，输出位1代表是0
endmodule

module fulladder (
  input  A,
  input  B,
  input  Cin,
  output \F_本位 ,
  output \Cout_进位输出 
);

  wire A_B_out, A_Cin_out, B_Cin_out;

  xor xor_1 (\F_本位 , A, Cin, B);
  and A_B (A_B_out, A, B);
  and B_Cin (B_Cin_out, B, Cin);
  and A_Cin (A_Cin_out, A, Cin);
  or or_1 (\Cout_进位输出 , A_B_out, B_Cin_out, A_Cin_out);
endmodule
