// Logisim project hm_code.circ as structural Verilog: 2 circuits, main circuit main
module main (
  input  [6:0] P1P2M1P3M2M3M4,
  input  G1,
  input  G2A_L,
  input  G2B_L,
  input  in_5,
  output out_6,
  output out_7,
  output [6:0] out_8
);

  wire n3_8_1_y1_l, n3_8_1_y2_l, n3_8_1_y3_l, n3_8_1_y4_l, n3_8_1_y5_l, n3_8_1_y6_l, n3_8_1_y7_l;
  wire [2:0] _1357_out;

  xor _1357 (_1357_out[0], P1P2M1P3M2M3M4[0], P1P2M1P3M2M3M4[2], P1P2M1P3M2M3M4[4], P1P2M1P3M2M3M4[6]);
  xor _2367 (_1357_out[1], P1P2M1P3M2M3M4[1], P1P2M1P3M2M3M4[2], P1P2M1P3M2M3M4[5], P1P2M1P3M2M3M4[6]);
  xor _4567 (_1357_out[2], P1P2M1P3M2M3M4[3], P1P2M1P3M2M3M4[4], P1P2M1P3M2M3M4[5], P1P2M1P3M2M3M4[6]);
  Hex_Digit_Display hex_digit_display_1 (.value({in_5, _1357_out}));  // open: dp
  not not_1 (out_6, out_7);
  _3_8 u_3_8_1 (
    .G1(G1), .G2A_L(G2A_L), .G2B_L(G2B_L), .A(_1357_out[0]), .B(_1357_out[1]), .C(_1357_out[2]),
    .Y0_L(out_7), .Y1_L(n3_8_1_y1_l), .Y2_L(n3_8_1_y2_l), .Y3_L(n3_8_1_y3_l), .Y4_L(n3_8_1_y4_l),
    .Y5_L(n3_8_1_y5_l), .Y6_L(n3_8_1_y6_l), .Y7_L(n3_8_1_y7_l));
  xor xor_1 (out_8[0], P1P2M1P3M2M3M4[0], ~n3_8_1_y1_l);  // XOR_Gate
  xor xor_2 (out_8[1], P1P2M1P3M2M3M4[1], ~n3_8_1_y2_l);  // XOR_Gate
  xor xor_3 (out_8[2], P1P2M1P3M2M3M4[2], ~n3_8_1_y3_l);  // XOR_Gate
  xor xor_4 (out_8[3], P1P2M1P3M2M3M4[3], ~n3_8_1_y4_l);  // XOR_Gate
  xor xor_5 (out_8[4], P1P2M1P3M2M3M4[4], ~n3_8_1_y5_l);  // XOR_Gate
  xor xor_6 (out_8[5], P1P2M1P3M2M3M4[5], ~n3_8_1_y6_l);  // XOR_Gate
  xor xor_7 (out_8[6], P1P2M1P3M2M3M4[6], ~n3_8_1_y7_l);  // XOR_Gate

  // Other names for the same wires on the sheet: ERROR = out_7; INPUT[6:0] = P1P2M1P3M2M3M4; OK = out_6;
  //   OUTPUT[6:0] = out_8

  // Notes on the sheet:
  //   校验位：原数据求偶校验码
  //   纠错：如果校验位和原码的个数是偶数，那就正常，否则这一位校验码对应的值们有问题
endmodule

module _3_8 (
  input  G1,
  input  G2A_L,
  input  G2B_L,
  input  A,
  input  B,
  input  C,
  output Y0_L,
  output Y1_L,
  output Y2_L,
  output Y3_L,
  output Y4_L,
  output Y5_L,
  output Y6_L,
  output Y7_L
);

  wire and_1_out, not_1_out, not_2_out, not_3_out, not_4_out, not_5_out, not_6_out, not_7_out;

  not not_1 (not_1_out, G1);
  and and_1 (and_1_out, ~not_1_out, ~G2A_L, ~G2B_L);  // AND_Gate
  not not_2 (not_2_out, A);
  not not_3 (not_3_out, B);
  not not_4 (not_4_out, C);
  not not_5 (not_5_out, not_2_out);
  not not_6 (not_6_out, not_3_out);
  not not_7 (not_7_out, not_4_out);
  nand nand_1 (Y0_L, not_2_out, not_3_out, not_4_out, and_1_out);
  nand nand_2 (Y1_L, not_3_out, not_4_out, not_5_out, and_1_out);
  nand nand_3 (Y2_L, not_2_out, not_4_out, not_6_out, and_1_out);
  nand nand_4 (Y3_L, not_4_out, not_5_out, not_6_out, and_1_out);
  nand nand_5 (Y4_L, not_2_out, not_3_out, not_7_out, and_1_out);
  nand nand_6 (Y5_L, not_3_out, not_5_out, not_7_out, and_1_out);
  nand nand_7 (Y6_L, not_2_out, not_6_out, not_7_out, and_1_out);
  nand nand_8 (Y7_L, and_1_out, not_6_out, not_7_out, not_5_out);
endmodule
