// Logisim project 实验三全部电路_许霁烨.circ as structural Verilog: 9 circuits, main circuit 数字时钟
module \计数器  (
  input  LD,
  input  CLR,
  input  D0,
  input  D1,
  input  D2,
  input  D3,
  input  ENP,
  input  ENT,
  output out_9,
  output out_10,
  output out_11,
  output out_12,
  output out_13
);

  wire and_1_out, and_2_out, and_3_out, and_4_out, and_5_out, and_6_out, and_7_out, and_8_out, and_9_out,
       and_10_out, and_11_out, and_12_out, and_13_out, and_14_out, and_15_out, and_16_out, buffer_1_out,
       clock_1_out, d_ff_1_qn, d_ff_2_qn, d_ff_3_qn, d_ff_4_qn, not_1_out, not_2_out, not_3_out, not_4_out,
       not_5_out, not_6_out, not_7_out, or_1_out, or_2_out, or_3_out, or_4_out, xor_1_out, xor_2_out,
       xor_3_out, xor_4_out;

  Clock clock_1 (.out(clock_1_out));
  buf buffer_1 (buffer_1_out, CLR);
  not not_1 (not_1_out, clock_1_out);
  not not_2 (not_2_out, d_ff_1_qn);
  and and_1 (and_1_out, ~d_ff_1_qn, ~d_ff_2_qn);  // AND_Gate
  and and_2 (and_2_out, ~d_ff_1_qn, ~d_ff_2_qn, ~d_ff_3_qn);  // AND_Gate
  and and_3 (and_3_out, ENP, ENT);
  not not_3 (not_3_out, ENT);
  xor xor_1 (xor_1_out, and_3_out, ~d_ff_1_qn);  // XOR_Gate
  and and_4 (and_4_out, not_2_out, and_3_out);
  xor xor_2 (xor_2_out, and_4_out, ~d_ff_2_qn);  // XOR_Gate
  and and_5 (and_5_out, and_1_out, and_3_out);
  and and_6 (and_6_out, and_2_out, and_3_out);
  and and_7 (and_7_out, LD, ~buffer_1_out);  // AND_Gate
  and and_8 (and_8_out, ~and_7_out, ~buffer_1_out);  // AND_Gate
  and and_9 (and_9_out, and_7_out, D0);
  and and_10 (and_10_out, and_8_out, xor_1_out);
  and and_11 (and_11_out, and_7_out, D1);
  and and_12 (and_12_out, and_8_out, xor_2_out);
  and and_13 (and_13_out, and_7_out, D2);
  and and_14 (and_14_out, and_8_out, xor_3_out);
  xor xor_3 (xor_3_out, and_5_out, ~d_ff_3_qn);  // XOR_Gate
  and and_15 (and_15_out, and_7_out, D3);
  and and_16 (and_16_out, and_8_out, xor_4_out);
  xor xor_4 (xor_4_out, and_6_out, ~d_ff_4_qn);  // XOR_Gate
  and and_17 (out_13, ~d_ff_4_qn, ~d_ff_3_qn, ~d_ff_2_qn, ~d_ff_1_qn, ~not_3_out);  // AND_Gate
  or or_1 (or_1_out, and_9_out, and_10_out);
  or or_2 (or_2_out, and_11_out, and_12_out);
  or or_3 (or_3_out, and_13_out, and_14_out);
  or or_4 (or_4_out, and_15_out, and_16_out);
  not not_4 (not_4_out, not_1_out);
  not not_5 (not_5_out, not_1_out);
  not not_6 (not_6_out, not_1_out);
  not not_7 (not_7_out, not_1_out);
  D_Flip_Flop #(.Pre_Clr_Positions("LEGACY"), .enable("true")) d_ff_1 (
    .clk(not_4_out), .D(or_1_out), .Q(out_9), .Qn(d_ff_1_qn));  // open: preset, en, reset
  D_Flip_Flop #(.Pre_Clr_Positions("LEGACY"), .enable("true")) d_ff_2 (
    .clk(not_5_out), .D(or_2_out), .Q(out_10), .Qn(d_ff_2_qn));  // open: preset, en, reset
  D_Flip_Flop #(.Pre_Clr_Positions("LEGACY"), .enable("true")) d_ff_3 (
    .clk(not_6_out), .D(or_3_out), .Q(out_11), .Qn(d_ff_3_qn));  // open: preset, en, reset
  D_Flip_Flop #(.Pre_Clr_Positions("LEGACY"), .enable("true")) d_ff_4 (
    .clk(not_7_out), .D(or_4_out), .Q(out_12), .Qn(d_ff_4_qn));  // open: preset, en, reset
endmodule

module \数字时钟  (
  input  in_1,
  input  in_2,
  input  [3:0] in_3,
  input  [3:0] in_4,
  input  [3:0] in_5,
  input  [3:0] in_6,
  input  [3:0] in_7,
  input  [3:0] in_8,
  input  in_9
);

  wire and_1_out, and_2_out, and_3_out, and_4_out, and_5_out, and_6_out, and_7_out, and_8_out, and_9_out,
       and_10_out, and_11_out, and_12_out, and_13_out, and_15_out, and_16_out, and_17_out, and_18_out,
       and_19_out, and_20_out, comparator_1_eq, comparator_2_eq, comparator_3_eq, comparator_4_eq,
       comparator_5_eq, comparator_6_eq, LED, multiplexer_1_out, multiplexer_2_out, multiplexer_3_out,
       multiplexer_4_out, multiplexer_5_out, register_1_q, register_2_q, register_3_q, register_4_q,
       register_5_q, register_6_q, T, \蜂鸣使能 ;
  wire [3:0] H1, H2, M1, M2, S1, S2;

  // Buzzer buzzer_1: pin names not known; wires that end beside it: 14'h1000, \蜂鸣使能 , 7'b0110000
  Multiplexer #(.enable("false")) multiplexer_1 (.in0(and_4_out), .in1(T), .out(multiplexer_1_out), .sel(in_1));
  LED led_1 (.in(LED));
  Hex_Digit_Display hex_digit_display_1 (.value(H1));  // open: dp
  and and_1 (and_1_out, and_5_out, ~in_1);  // AND_Gate
  counter_no_clk counter_no_clk_1 (
    .CLK(T), .LD(in_1), .CLR(and_1_out), .D0(in_3[0]), .D1(in_3[1]), .D2(in_3[2]), .D3(in_3[3]), .ENP(in_9),
    .ENT(in_2), .out_10(S2[0]), .out_11(S2[1]), .out_12(S2[2]), .out_13(S2[3]));  // open: out_14
  and and_2 (and_2_out, and_6_out, ~in_1);  // AND_Gate
  counter_no_clk counter_no_clk_2 (
    .CLK(multiplexer_1_out), .LD(in_1), .CLR(and_2_out), .D0(in_4[0]), .D1(in_4[1]), .D2(in_4[2]),
    .D3(in_4[3]), .ENP(in_9), .ENT(in_2), .out_10(S1[0]), .out_11(S1[1]), .out_12(S1[2]), .out_13(S1[3]));  // open: out_14
  Register #(.width(1), .Select("low")) register_1 (.D(and_2_out), .Q(register_1_q), .clk(T));  // open: en, clr
  Register #(.width(1), .Select("low")) register_2 (.D(and_1_out), .Q(register_2_q), .clk(T));  // open: en, clr
  Hex_Digit_Display hex_digit_display_2 (.value(H2), .dp(1'b1));
  Hex_Digit_Display hex_digit_display_3 (.value(M1));  // open: dp
  and and_3 (and_3_out, register_1_q, register_2_q);
  Comparator #(.width(4)) comparator_1 (.a(H2), .b(4'b0001), .eq(comparator_1_eq));  // open: gt, lt
  Comparator #(.width(4)) comparator_2 (.a(H1), .b(4'b0001), .eq(comparator_2_eq));  // open: gt, lt
  Comparator #(.width(4)) comparator_3 (.a(M2), .b(4'b0001), .eq(comparator_3_eq));  // open: gt, lt
  Comparator #(.width(4)) comparator_4 (.a(M1), .b(4'b0001), .eq(comparator_4_eq));  // open: gt, lt
  Comparator #(.width(4)) comparator_5 (.a(S2), .b(4'b0001), .eq(comparator_5_eq));  // open: gt, lt
  Comparator #(.width(4)) comparator_6 (.a(S1), .b(4'b0001), .eq(comparator_6_eq));  // open: gt, lt
  Hex_Digit_Display hex_digit_display_4 (.value(S1));  // open: dp
  Hex_Digit_Display hex_digit_display_5 (.value(M2), .dp(1'b1));
  and and_4 (and_4_out, ~S2[0], ~S2[1], ~S2[2], ~S2[3]);  // AND_Gate
  and and_5 (and_5_out, S2[0], ~S2[1], ~S2[2], S2[3]);  // AND_Gate
  and and_6 (and_6_out, S1[0], ~S1[1], S1[2], ~S1[3]);  // AND_Gate
  Hex_Digit_Display hex_digit_display_6 (.value(S2), .dp(1'b1));
  and and_7 (and_7_out, comparator_1_eq, comparator_2_eq, comparator_3_eq, comparator_4_eq, comparator_5_eq, comparator_6_eq);
  Clock clock_1 (.out(T));
  // Buzzer buzzer_2: pin names not known; wires that end beside it: 14'h1000, and_7_out, 7'b0110000
  Multiplexer #(.enable("false")) multiplexer_2 (.in0(and_3_out), .in1(T), .out(multiplexer_2_out), .sel(in_1));
  Multiplexer #(.enable("false")) multiplexer_3 (.in0(and_12_out), .in1(T), .out(multiplexer_3_out), .sel(in_1));
  and and_8 (and_8_out, and_10_out, ~in_1);  // AND_Gate
  counter_no_clk counter_no_clk_3 (
    .CLK(multiplexer_2_out), .LD(in_1), .CLR(and_8_out), .D0(in_5[0]), .D1(in_5[1]), .D2(in_5[2]),
    .D3(in_5[3]), .ENP(in_9), .ENT(in_2), .out_10(M2[0]), .out_11(M2[1]), .out_12(M2[2]), .out_13(M2[3]));  // open: out_14
  and and_9 (and_9_out, and_11_out, ~in_1);  // AND_Gate
  counter_no_clk counter_no_clk_4 (
    .CLK(multiplexer_3_out), .LD(in_1), .CLR(and_9_out), .D0(in_6[0]), .D1(in_6[1]), .D2(in_6[2]),
    .D3(in_6[3]), .ENP(in_9), .ENT(in_2), .out_10(M1[0]), .out_11(M1[1]), .out_12(M1[2]), .out_13(M1[3]));  // open: out_14
  Register #(.width(1), .Select("low")) register_3 (.D(and_9_out), .Q(register_3_q), .clk(T));  // open: en, clr
  Register #(.width(1), .Select("low")) register_4 (.D(and_8_out), .Q(register_4_q), .clk(T));  // open: en, clr
  and and_10 (and_10_out, M2[0], ~M2[1], ~M2[2], M2[3]);  // AND_Gate
  and and_11 (and_11_out, M1[0], ~M1[1], M1[2], ~M1[3]);  // AND_Gate
  and and_12 (and_12_out, ~M2[0], ~M2[1], ~M2[2], ~M2[3]);  // AND_Gate
  and and_13 (and_13_out, register_3_q, register_4_q);
  and and_14 (LED, and_3_out, and_13_out);
  and and_15 (and_15_out, and_17_out, ~in_1);  // AND_Gate
  Multiplexer #(.enable("false")) multiplexer_4 (.in0(LED), .in1(T), .out(multiplexer_4_out), .sel(in_1));
  Multiplexer #(.enable("false")) multiplexer_5 (.in0(and_20_out), .in1(T), .out(multiplexer_5_out), .sel(in_1));
  counter_no_clk counter_no_clk_5 (
    .CLK(multiplexer_4_out), .LD(in_1), .CLR(and_15_out), .D0(in_7[0]), .D1(in_7[1]), .D2(in_7[2]),
    .D3(in_7[3]), .ENP(in_9), .ENT(in_2), .out_10(H2[0]), .out_11(H2[1]), .out_12(H2[2]), .out_13(H2[3]));  // open: out_14
  and and_16 (and_16_out, and_18_out, ~in_1);  // AND_Gate
  counter_no_clk counter_no_clk_6 (
    .CLK(multiplexer_5_out), .LD(in_1), .CLR(and_16_out), .D0(in_8[0]), .D1(in_8[1]), .D2(in_8[2]),
    .D3(in_8[3]), .ENP(in_9), .ENT(in_2), .out_10(H1[0]), .out_11(H1[1]), .out_12(H1[2]), .out_13(H1[3]));  // open: out_14
  Register #(.width(1), .Select("low")) register_5 (.D(and_16_out), .Q(register_5_q), .clk(T));  // open: en, clr
  Register #(.width(1), .Select("low")) register_6 (.D(and_15_out), .Q(register_6_q), .clk(T));  // open: en, clr
  and and_17 (and_17_out, H2[0], H2[1], ~H2[2], ~H2[3]);  // AND_Gate
  and and_18 (and_18_out, ~H1[0], H1[1], ~H1[2], ~H1[3]);  // AND_Gate
  and and_19 (and_19_out, register_5_q, register_6_q);
  and and_20 (and_20_out, ~H2[0], ~H2[1], ~H2[2], ~H2[3]);  // AND_Gate
  and and_21 (\蜂鸣使能 , and_19_out, LED);

  // Other names for the same wires on the sheet: ENP = in_9; ENT = in_2; LOAD = in_1; 分低位[3:0] = in_5;
  //   分高位[3:0] = in_6; 时低位[3:0] = in_7; 时高位[3:0] = in_8; 秒低位[3:0] = in_3; 秒高位[3:0] = in_4

  // Notes on the sheet:
  //   闹钟
endmodule

module counter_no_clk (
  input  CLK,
  input  LD,
  input  CLR,
  input  D0,
  input  D1,
  input  D2,
  input  D3,
  input  ENP,
  input  ENT,
  output out_10,
  output out_11,
  output out_12,
  output out_13,
  output out_14
);

  wire and_1_out, and_2_out, and_3_out, and_4_out, and_5_out, and_6_out, and_7_out, and_8_out, and_9_out,
       and_10_out, and_11_out, and_12_out, and_13_out, and_14_out, and_15_out, and_16_out, buffer_1_out,
       d_ff_1_qn, d_ff_2_qn, d_ff_3_qn, d_ff_4_qn, not_1_out, not_2_out, not_3_out, not_4_out, not_5_out,
       not_6_out, not_7_out, or_1_out, or_2_out, or_3_out, or_4_out, xor_1_out, xor_2_out, xor_3_out,
       xor_4_out;

  buf buffer_1 (buffer_1_out, CLR);
  not not_1 (not_1_out, CLK);
  not not_2 (not_2_out, d_ff_1_qn);
  and and_1 (and_1_out, ~d_ff_1_qn, ~d_ff_2_qn);  // AND_Gate
  and and_2 (and_2_out, ~d_ff_1_qn, ~d_ff_2_qn, ~d_ff_3_qn);  // AND_Gate
  and and_3 (and_3_out, ENP, ENT);
  not not_3 (not_3_out, ENT);
  xor xor_1 (xor_1_out, and_3_out, ~d_ff_1_qn);  // XOR_Gate
  and and_4 (and_4_out, not_2_out, and_3_out);
  xor xor_2 (xor_2_out, and_4_out, ~d_ff_2_qn);  // XOR_Gate
  and and_5 (and_5_out, and_1_out, and_3_out);
  and and_6 (and_6_out, and_2_out, and_3_out);
  and and_7 (and_7_out, LD, ~buffer_1_out);  // AND_Gate
  and and_8 (and_8_out, ~and_7_out, ~buffer_1_out);  // AND_Gate
  and and_9 (and_9_out, and_7_out, D0);
  and and_10 (and_10_out, and_8_out, xor_1_out);
  and and_11 (and_11_out, and_7_out, D1);
  and and_12 (and_12_out, and_8_out, xor_2_out);
  and and_13 (and_13_out, and_7_out, D2);
  and and_14 (and_14_out, and_8_out, xor_3_out);
  xor xor_3 (xor_3_out, and_5_out, ~d_ff_3_qn);  // XOR_Gate
  and and_15 (and_15_out, and_7_out, D3);
  and and_16 (and_16_out, and_8_out, xor_4_out);
  xor xor_4 (xor_4_out, and_6_out, ~d_ff_4_qn);  // XOR_Gate
  and and_17 (out_14, ~d_ff_4_qn, ~d_ff_3_qn, ~d_ff_2_qn, ~d_ff_1_qn, ~not_3_out);  // AND_Gate
  or or_1 (or_1_out, and_9_out, and_10_out);
  or or_2 (or_2_out, and_11_out, and_12_out);
  or or_3 (or_3_out, and_13_out, and_14_out);
  or or_4 (or_4_out, and_15_out, and_16_out);
  not not_4 (not_4_out, not_1_out);
  not not_5 (not_5_out, not_1_out);
  not not_6 (not_6_out, not_1_out);
  not not_7 (not_7_out, not_1_out);
  D_Flip_Flop #(.Pre_Clr_Positions("LEGACY"), .enable("true")) d_ff_1 (
    .clk(not_4_out), .D(or_1_out), .Q(out_10), .Qn(d_ff_1_qn));  // open: preset, en, reset
  D_Flip_Flop #(.Pre_Clr_Positions("LEGACY"), .enable("true")) d_ff_2 (
    .clk(not_5_out), .D(or_2_out), .Q(out_11), .Qn(d_ff_2_qn));  // open: preset, en, reset
  D_Flip_Flop #(.Pre_Clr_Positions("LEGACY"), .enable("true")) d_ff_3 (
    .clk(not_6_out), .D(or_3_out), .Q(out_12), .Qn(d_ff_3_qn));  // open: preset, en, reset
  D_Flip_Flop #(.Pre_Clr_Positions("LEGACY"), .enable("true")) d_ff_4 (
    .clk(not_7_out), .D(or_4_out), .Q(out_13), .Qn(d_ff_4_qn));  // open: preset, en, reset
endmodule

module \无符号乘法  (
  input  [3:0] in_1,
  input  [3:0] D0D1D2D3,
  input  [3:0] in_3,
  input  in_4,
  input  LD,
  input  CLR,
  output [7:0] out_7
);

  wire and_1_out, clock_1_out, clock_2_out, counter_no_clk_1_out_10, counter_no_clk_1_out_11,
       counter_no_clk_1_out_12, index, multiplexer_1_out, multiplexer_2_out, or_1_out, or_2_out, RST, STOP;
  wire [0:0] adder_1_out;
  wire [3:0] adder_1_cout, multiplexer_3_out, multiplexer_4_out, multiplexer_5_out;

  Hex_Digit_Display hex_digit_display_1 (.value(in_1));  // open: dp
  Clock clock_1 (.out(clock_1_out));
  and and_1 (and_1_out, ~STOP, in_4);  // AND_Gate
  Hex_Digit_Display hex_digit_display_2 (.value(in_3));  // open: dp
  Multiplexer #(.enable("false")) multiplexer_1 (
    .in0(1'b1), .in1(clock_1_out), .out(multiplexer_1_out), .sel(and_1_out));
  Clock clock_2 (.out(clock_2_out));
  Hex_Digit_Display hex_digit_display_3 (.value(out_7[3:0]));  // open: dp
  Hex_Digit_Display hex_digit_display_4 (.value(out_7[7:4]));  // open: dp
  Multiplexer #(.enable("false")) multiplexer_2 (
    .in0(multiplexer_1_out), .in1(clock_2_out), .out(multiplexer_2_out), .sel(RST));
  or or_1 (or_1_out, index, RST);
  Register #(.width(4), .Select("low")) register_1 (
    .D(multiplexer_3_out), .Q(out_7[7:4]), .clk(multiplexer_2_out));  // open: en, clr
  Multiplexer #(.width(4), .enable("false")) multiplexer_3 (
    .in0(adder_1_cout), .in1(4'b0000), .out(multiplexer_3_out), .sel(or_1_out));
  Multiplexer #(.width(4), .enable("false")) multiplexer_4 (
    .in0(4'b0000), .in1(in_1), .out(multiplexer_4_out), .sel(out_7[0]));
  Adder #(.width(4)) adder_1 (
    .a(out_7[7:4]), .b(multiplexer_4_out), .out({adder_1_cout[2:0], adder_1_out[0]}), .cin(1'b0),
    .cout(adder_1_cout[3]));
  Multiplexer #(.width(4), .enable("false")) multiplexer_5 (
    .in0({adder_1_out[0], out_7[3:1]}), .in1(in_3), .out(multiplexer_5_out), .sel(or_2_out));
  or or_2 (or_2_out, index, RST);
  Register #(.width(4), .Select("low")) register_2 (
    .D(multiplexer_5_out), .Q(out_7[3:0]), .clk(multiplexer_2_out));  // open: en, clr
  Button button_1 (.out(RST));
  LED led_1 (.in(STOP));
  and and_2 (index, ~counter_no_clk_1_out_10, ~counter_no_clk_1_out_11, ~counter_no_clk_1_out_12);  // AND_Gate
  and and_3 (STOP, counter_no_clk_1_out_10, ~counter_no_clk_1_out_11, counter_no_clk_1_out_12);  // AND_Gate
  counter_no_clk counter_no_clk_1 (
    .CLK(multiplexer_2_out), .LD(LD), .CLR(RST), .D0(D0D1D2D3[0]), .D1(D0D1D2D3[1]), .D2(D0D1D2D3[2]),
    .D3(D0D1D2D3[3]), .ENP(1'b1), .ENT(1'b1), .out_10(counter_no_clk_1_out_10),
    .out_11(counter_no_clk_1_out_11), .out_12(counter_no_clk_1_out_12));  // open: out_13, out_14

  // Other names for the same wires on the sheet: DIN[3:0] = D0D1D2D3; LOAD = in_4; X[3:0] = in_1; Y[3:0] = in_3;
  //   Z[7:0] = out_7

  // Notes on the sheet:
  //   ×
  //   =
endmodule

module \_8位移位器  (
  input  not_CLR,
  input  Rin,
  input  D3,
  input  D2,
  input  D1,
  input  D0,
  input  Lin,
  input  S1,
  input  S0,
  output out_10,
  output out_11,
  output out_12,
  output out_13
);

  wire _00_2_out, _00_3_out, _00_4_out, _00_out, _01_2_out, _01_3_out, _01_4_out, _01_out, _10_2_out,
       _10_3_out, _10_4_out, _10_out, _11_2_out, _11_3_out, _11_4_out, _11_out, buffer_1_out, buffer_2_out,
       clock_1_out, not_1_out, not_2_out, not_3_out, not_4_out, not_5_out, not_6_out, not_7_out, not_8_out,
       not_9_out, not_10_out, not_11_out, not_12_out, not_13_out, not_14_out, not_15_out, or_1_out, or_2_out,
       or_3_out, or_4_out;

  Clock clock_1 (.out(clock_1_out));
  not not_1 (not_1_out, S1);
  not not_2 (not_2_out, S0);
  not not_3 (not_3_out, clock_1_out);
  not not_4 (not_4_out, not_5_out);
  not not_5 (not_5_out, not_CLR);
  not not_6 (not_6_out, not_1_out);
  buf buffer_1 (buffer_1_out, not_6_out);
  buf buffer_2 (buffer_2_out, not_7_out);
  not not_7 (not_7_out, not_2_out);
  and _10 (_10_out, Rin, buffer_1_out, not_2_out);
  and _00 (_00_out, out_10, not_1_out, not_2_out);
  and _11 (_11_out, D3, buffer_1_out, buffer_2_out);
  and _01 (_01_out, out_11, not_1_out, buffer_2_out);
  and _10_2 (_10_2_out, out_10, buffer_1_out, not_2_out);
  and _00_2 (_00_2_out, out_11, not_1_out, not_2_out);
  and _11_2 (_11_2_out, D2, buffer_1_out, buffer_2_out);
  and _01_2 (_01_2_out, out_12, not_1_out, buffer_2_out);
  and _10_3 (_10_3_out, out_11, buffer_1_out, not_2_out);
  and _00_3 (_00_3_out, out_12, not_1_out, not_2_out);
  and _11_3 (_11_3_out, D1, buffer_1_out, buffer_2_out);
  and _01_3 (_01_3_out, out_13, not_1_out, buffer_2_out);
  and _10_4 (_10_4_out, out_12, buffer_1_out, not_2_out);
  and _00_4 (_00_4_out, out_13, not_1_out, not_2_out);
  and _11_4 (_11_4_out, D0, buffer_1_out, buffer_2_out);
  and _01_4 (_01_4_out, Lin, not_1_out, buffer_2_out);
  or or_1 (or_1_out, _10_out, _00_out, _11_out, _01_out);
  or or_2 (or_2_out, _10_2_out, _00_2_out, _11_2_out, _01_2_out);
  or or_3 (or_3_out, _10_3_out, _00_3_out, _11_3_out, _01_3_out);
  or or_4 (or_4_out, _10_4_out, _00_4_out, _11_4_out, _01_4_out);
  not not_8 (not_8_out, not_3_out);
  not not_9 (not_9_out, not_4_out);
  not not_10 (not_10_out, not_3_out);
  not not_11 (not_11_out, not_4_out);
  not not_12 (not_12_out, not_3_out);
  not not_13 (not_13_out, not_4_out);
  not not_14 (not_14_out, not_3_out);
  not not_15 (not_15_out, not_4_out);
  Register #(.width(1), .Select("low")) register_1 (
    .D(or_1_out), .Q(out_10), .clk(not_8_out), .clr(not_9_out));  // open: en
  Register #(.width(1), .Select("low")) register_2 (
    .D(or_2_out), .Q(out_11), .clk(not_10_out), .clr(not_11_out));  // open: en
  Register #(.width(1), .Select("low")) register_3 (
    .D(or_3_out), .Q(out_12), .clk(not_12_out), .clr(not_13_out));  // open: en
  Register #(.width(1), .Select("low")) register_4 (
    .D(or_4_out), .Q(out_13), .clk(not_14_out), .clr(not_15_out));  // open: en
endmodule

module \_32位寄存器堆  (
  input  in_1,
  input  [4:0] in_2,
  input  [31:0] in_3,
  input  [4:0] in_4,
  input  [4:0] in_5,
  output [31:0] out_6,
  output [31:0] out_7
);

  wire and_1_out, and_2_out, and_3_out, and_4_out, and_5_out, and_6_out, and_7_out, and_8_out, and_9_out,
       and_10_out, and_11_out, and_12_out, and_13_out, and_14_out, and_15_out, and_16_out, and_17_out,
       and_18_out, and_19_out, and_20_out, and_21_out, and_22_out, and_23_out, and_24_out, and_25_out,
       and_26_out, and_27_out, and_28_out, and_29_out, and_30_out, and_31_out, and_32_out, CLK,
       decoder_1_out0, decoder_1_out1, decoder_1_out2, decoder_1_out3, decoder_1_out4, decoder_1_out5,
       decoder_1_out6, decoder_1_out7, decoder_1_out8, decoder_1_out9, decoder_1_out10, decoder_1_out11,
       decoder_1_out12, decoder_1_out13, decoder_1_out14, decoder_1_out15, decoder_1_out16, decoder_1_out17,
       decoder_1_out18, decoder_1_out19, decoder_1_out20, decoder_1_out21, decoder_1_out22, decoder_1_out23,
       decoder_1_out24, decoder_1_out25, decoder_1_out26, decoder_1_out27, decoder_1_out28, decoder_1_out29,
       decoder_1_out30, decoder_1_out31;
  wire [31:0] register_1_q, register_2_q, register_3_q, register_4_q, register_5_q, register_6_q,
       register_7_q, register_8_q, register_9_q, register_10_q, register_11_q, register_12_q, register_13_q,
       register_14_q, register_15_q, register_16_q, register_17_q, register_18_q, register_19_q,
       register_20_q, register_21_q, register_22_q, register_23_q, register_24_q, register_25_q,
       register_26_q, register_27_q, register_28_q, register_29_q, register_30_q, register_31_q,
       register_32_q;

  Clock clock_1 (.out(CLK));
  Decoder #(.select(5), .enable("false")) decoder_1 (
    .out0(decoder_1_out0), .out1(decoder_1_out1), .out2(decoder_1_out2), .out3(decoder_1_out3),
    .out4(decoder_1_out4), .out5(decoder_1_out5), .out6(decoder_1_out6), .out7(decoder_1_out7),
    .out8(decoder_1_out8), .out9(decoder_1_out9), .out10(decoder_1_out10), .out11(decoder_1_out11),
    .out12(decoder_1_out12), .out13(decoder_1_out13), .out14(decoder_1_out14), .out15(decoder_1_out15),
    .out16(decoder_1_out16), .out17(decoder_1_out17), .out18(decoder_1_out18), .out19(decoder_1_out19),
    .out20(decoder_1_out20), .out21(decoder_1_out21), .out22(decoder_1_out22), .out23(decoder_1_out23),
    .out24(decoder_1_out24), .out25(decoder_1_out25), .out26(decoder_1_out26), .out27(decoder_1_out27),
    .out28(decoder_1_out28), .out29(decoder_1_out29), .out30(decoder_1_out30), .out31(decoder_1_out31),
    .sel(in_5));
  and and_1 (and_1_out, decoder_1_out0, CLK, in_1);
  and and_2 (and_2_out, decoder_1_out1, CLK, in_1);
  and and_3 (and_3_out, decoder_1_out2, CLK, in_1);
  and and_4 (and_4_out, decoder_1_out3, CLK, in_1);
  and and_5 (and_5_out, decoder_1_out4, CLK, in_1);
  and and_6 (and_6_out, decoder_1_out5, CLK, in_1);
  and and_7 (and_7_out, decoder_1_out6, CLK, in_1);
  and and_8 (and_8_out, decoder_1_out7, CLK, in_1);
  and and_9 (and_9_out, decoder_1_out8, CLK, in_1);
  and and_10 (and_10_out, decoder_1_out9, CLK, in_1);
  and and_11 (and_11_out, decoder_1_out10, CLK, in_1);
  and and_12 (and_12_out, decoder_1_out11, CLK, in_1);
  and and_13 (and_13_out, decoder_1_out12, CLK, in_1);
  and and_14 (and_14_out, decoder_1_out13, CLK, in_1);
  and and_15 (and_15_out, decoder_1_out14, CLK, in_1);
  and and_16 (and_16_out, decoder_1_out15, CLK, in_1);
  and and_17 (and_17_out, decoder_1_out16, CLK, in_1);
  and and_18 (and_18_out, decoder_1_out17, CLK, in_1);
  and and_19 (and_19_out, decoder_1_out18, CLK, in_1);
  and and_20 (and_20_out, decoder_1_out19, CLK, in_1);
  and and_21 (and_21_out, decoder_1_out20, CLK, in_1);
  and and_22 (and_22_out, decoder_1_out21, CLK, in_1);
  and and_23 (and_23_out, decoder_1_out22, CLK, in_1);
  and and_24 (and_24_out, decoder_1_out23, CLK, in_1);
  and and_25 (and_25_out, decoder_1_out24, CLK, in_1);
  and and_26 (and_26_out, decoder_1_out25, CLK, in_1);
  and and_27 (and_27_out, decoder_1_out26, CLK, in_1);
  and and_28 (and_28_out, decoder_1_out27, CLK, in_1);
  and and_29 (and_29_out, decoder_1_out28, CLK, in_1);
  and and_30 (and_30_out, decoder_1_out29, CLK, in_1);
  and and_31 (and_31_out, decoder_1_out30, CLK, in_1);
  and and_32 (and_32_out, decoder_1_out31, CLK, in_1);
  Register #(.width(32), .Select("low")) register_1 (.D(in_3), .Q(register_1_q), .clk(and_1_out));  // open: en, clr
  Register #(.width(32), .Select("low")) register_2 (.D(in_3), .Q(register_2_q), .clk(and_2_out));  // open: en, clr
  Register #(.width(32), .Select("low")) register_3 (.D(in_3), .Q(register_3_q), .clk(and_3_out));  // open: en, clr
  Register #(.width(32), .Select("low")) register_4 (.D(in_3), .Q(register_4_q), .clk(and_4_out));  // open: en, clr
  Register #(.width(32), .Select("low")) register_5 (.D(in_3), .Q(register_5_q), .clk(and_5_out));  // open: en, clr
  Register #(.width(32), .Select("low")) register_6 (.D(in_3), .Q(register_6_q), .clk(and_6_out));  // open: en, clr
  Register #(.width(32), .Select("low")) register_7 (.D(in_3), .Q(register_7_q), .clk(and_7_out));  // open: en, clr
  Register #(.width(32), .Select("low")) register_8 (.D(in_3), .Q(register_8_q), .clk(and_8_out));  // open: en, clr
  Register #(.width(32), .Select("low")) register_9 (.D(in_3), .Q(register_9_q), .clk(and_9_out));  // open: en, clr
  Register #(.width(32), .Select("low")) register_10 (.D(in_3), .Q(register_10_q), .clk(and_10_out));  // open: en, clr
  Register #(.width(32), .Select("low")) register_11 (.D(in_3), .Q(register_11_q), .clk(and_11_out));  // open: en, clr
  Register #(.width(32), .Select("low")) register_12 (.D(in_3), .Q(register_12_q), .clk(and_12_out));  // open: en, clr
  Register #(.width(32), .Select("low")) register_13 (.D(in_3), .Q(register_13_q), .clk(and_13_out));  // open: en, clr
  Register #(.width(32), .Select("low")) register_14 (.D(in_3), .Q(register_14_q), .clk(and_14_out));  // open: en, clr
  Register #(.width(32), .Select("low")) register_15 (.D(in_3), .Q(register_15_q), .clk(and_15_out));  // open: en, clr
  Register #(.width(32), .Select("low")) register_16 (.D(in_3), .Q(register_16_q), .clk(and_16_out));  // open: en, clr
  Register #(.width(32), .Select("low")) register_17 (.D(in_3), .Q(register_17_q), .clk(and_17_out));  // open: en, clr
  Register #(.width(32), .Select("low")) register_18 (.D(in_3), .Q(register_18_q), .clk(and_18_out));  // open: en, clr
  Register #(.width(32), .Select("low")) register_19 (.D(in_3), .Q(register_19_q), .clk(and_19_out));  // open: en, clr
  Register #(.width(32), .Select("low")) register_20 (.D(in_3), .Q(register_20_q), .clk(and_20_out));  // open: en, clr
  Register #(.width(32), .Select("low")) register_21 (.D(in_3), .Q(register_21_q), .clk(and_21_out));  // open: en, clr
  Register #(.width(32), .Select("low")) register_22 (.D(in_3), .Q(register_22_q), .clk(and_22_out));  // open: en, clr
  Register #(.width(32), .Select("low")) register_23 (.D(in_3), .Q(register_23_q), .clk(and_23_out));  // open: en, clr
  Register #(.width(32), .Select("low")) register_24 (.D(in_3), .Q(register_24_q), .clk(and_24_out));  // open: en, clr
  Register #(.width(32), .Select("low")) register_25 (.D(in_3), .Q(register_25_q), .clk(and_25_out));  // open: en, clr
  Register #(.width(32), .Select("low")) register_26 (.D(in_3), .Q(register_26_q), .clk(and_26_out));  // open: en, clr
  Register #(.width(32), .Select("low")) register_27 (.D(in_3), .Q(register_27_q), .clk(and_27_out));  // open: en, clr
  Register #(.width(32), .Select("low")) register_28 (.D(in_3), .Q(register_28_q), .clk(and_28_out));  // open: en, clr
  Register #(.width(32), .Select("low")) register_29 (.D(in_3), .Q(register_29_q), .clk(and_29_out));  // open: en, clr
  Register #(.width(32), .Select("low")) register_30 (.D(in_3), .Q(register_30_q), .clk(and_30_out));  // open: en, clr
  Register #(.width(32), .Select("low")) register_31 (.D(in_3), .Q(register_31_q), .clk(and_31_out));  // open: en, clr
  Register #(.width(32), .Select("low")) register_32 (.D(in_3), .Q(register_32_q), .clk(and_32_out));  // open: en, clr
  Multiplexer #(.select(5), .width(32), .enable("false")) multiplexer_1 (
    .in0(register_1_q), .in1(register_2_q), .in2(register_3_q), .in3(register_4_q), .in4(register_5_q),
    .in5(register_6_q), .in6(register_7_q), .in7(register_8_q), .in8(register_9_q), .in9(register_10_q),
    .in10(register_11_q), .in11(register_12_q), .in12(register_13_q), .in13(register_14_q),
    .in14(register_15_q), .in15(register_16_q), .in16(register_17_q), .in17(register_18_q),
    .in18(register_19_q), .in19(register_20_q), .in20(register_21_q), .in21(register_22_q),
    .in22(register_23_q), .in23(register_24_q), .in24(register_25_q), .in25(register_26_q),
    .in26(register_27_q), .in27(register_28_q), .in28(register_29_q), .in29(register_30_q),
    .in30(register_31_q), .in31(register_32_q), .out(out_7), .sel(in_4));
  Multiplexer #(.select(5), .width(32), .enable("false")) multiplexer_2 (
    .in0(register_1_q), .in1(register_2_q), .in2(register_3_q), .in3(register_4_q), .in4(register_5_q),
    .in5(register_6_q), .in6(register_7_q), .in7(register_8_q), .in8(register_9_q), .in9(register_10_q),
    .in10(register_11_q), .in11(register_12_q), .in12(register_13_q), .in13(register_14_q),
    .in14(register_15_q), .in15(register_16_q), .in16(register_17_q), .in17(register_18_q),
    .in18(register_19_q), .in19(register_20_q), .in20(register_21_q), .in21(register_22_q),
    .in22(register_23_q), .in23(register_24_q), .in24(register_25_q), .in25(register_26_q),
    .in26(register_27_q), .in27(register_28_q), .in28(register_29_q), .in29(register_30_q),
    .in30(register_31_q), .in31(register_32_q), .out(out_6), .sel(in_2));

  // Other names for the same wires on the sheet: BUSA[31:0] = out_6; BUSB[31:0] = out_7; RA[4:0] = in_2;
  //   RB[4:0] = in_4; RW[4:0] = in_5; WE = in_1; WRITE[31:0] = in_3
endmodule

module \_8位移位器_有示波器  (
  input  not_CLR,
  input  Rin,
  input  D3,
  input  D2,
  input  D1,
  input  D0,
  input  Lin,
  input  S1,
  input  S0,
  output out_10,
  output out_11,
  output out_12,
  output out_13
);

  wire _00_2_out, _00_3_out, _00_4_out, _00_out, _01_2_out, _01_3_out, _01_4_out, _01_out, _10_2_out,
       _10_3_out, _10_4_out, _10_out, _11_2_out, _11_3_out, _11_4_out, _11_out, buffer_1_out, buffer_2_out,
       clock_1_out, not_1_out, not_2_out, not_3_out, not_4_out, not_5_out, not_6_out, not_7_out, not_8_out,
       not_9_out, not_10_out, not_11_out, not_12_out, not_13_out, not_14_out, not_15_out, or_1_out, or_2_out,
       or_3_out, or_4_out, xor_1_out;

  Clock clock_1 (.out(clock_1_out));
  not not_1 (not_1_out, S1);
  not not_2 (not_2_out, S0);
  not not_3 (not_3_out, clock_1_out);
  not not_4 (not_4_out, not_CLR);
  not not_5 (not_5_out, not_4_out);
  buf buffer_1 (buffer_1_out, not_6_out);
  not not_6 (not_6_out, not_1_out);
  not not_7 (not_7_out, not_2_out);
  buf buffer_2 (buffer_2_out, not_7_out);
  and _10 (_10_out, xor_1_out, buffer_1_out, not_2_out);
  and _00 (_00_out, out_10, not_1_out, not_2_out);
  and _11 (_11_out, D3, buffer_1_out, buffer_2_out);
  and _01 (_01_out, out_11, not_1_out, buffer_2_out);
  and _10_2 (_10_2_out, out_10, buffer_1_out, not_2_out);
  and _00_2 (_00_2_out, out_11, not_1_out, not_2_out);
  and _11_2 (_11_2_out, D2, buffer_1_out, buffer_2_out);
  and _01_2 (_01_2_out, out_12, not_1_out, buffer_2_out);
  and _10_3 (_10_3_out, out_11, buffer_1_out, not_2_out);
  and _00_3 (_00_3_out, out_12, not_1_out, not_2_out);
  and _11_3 (_11_3_out, D1, buffer_1_out, buffer_2_out);
  and _01_3 (_01_3_out, out_13, not_1_out, buffer_2_out);
  and _10_4 (_10_4_out, out_12, buffer_1_out, not_2_out);
  and _00_4 (_00_4_out, out_13, not_1_out, not_2_out);
  and _11_4 (_11_4_out, D0, buffer_1_out, buffer_2_out);
  and _01_4 (_01_4_out, Lin, not_1_out, buffer_2_out);
  or or_1 (or_1_out, _10_out, _00_out, _11_out, _01_out);
  or or_2 (or_2_out, _10_2_out, _00_2_out, _11_2_out, _01_2_out);
  or or_3 (or_3_out, _10_3_out, _00_3_out, _11_3_out, _01_3_out);
  or or_4 (or_4_out, _10_4_out, _00_4_out, _11_4_out, _01_4_out);
  not not_8 (not_8_out, not_3_out);
  not not_9 (not_9_out, not_5_out);
  not not_10 (not_10_out, not_3_out);
  not not_11 (not_11_out, not_5_out);
  not not_12 (not_12_out, not_3_out);
  not not_13 (not_13_out, not_5_out);
  not not_14 (not_14_out, not_3_out);
  not not_15 (not_15_out, not_5_out);
  Register #(.width(1), .Select("low")) register_1 (
    .D(or_1_out), .Q(out_10), .clk(not_8_out), .clr(not_9_out));  // open: en
  Register #(.width(1), .Select("low")) register_2 (
    .D(or_2_out), .Q(out_11), .clk(not_10_out), .clr(not_11_out));  // open: en
  Register #(.width(1), .Select("low")) register_3 (
    .D(or_3_out), .Q(out_12), .clk(not_12_out), .clr(not_13_out));  // open: en
  Register #(.width(1), .Select("low")) register_4 (
    .D(or_4_out), .Q(out_13), .clk(not_14_out), .clr(not_15_out));  // open: en
  // Digital_Oscilloscope #(.nState(20)) digital_oscilloscope_1: pin names not known; wires that end beside it: not_3_out, out_13, out_12
  xor xor_1 (xor_1_out, out_12, out_13);
endmodule

module \无符号除法  (
  input  [3:0] in_1,
  input  [3:0] D0D1D2D3,
  input  [3:0] in_3,
  input  in_4,
  input  LD,
  input  CLR,
  output [7:0] out_7
);

  wire and_1_out, clock_1_out, clock_2_out, counter_no_clk_1_out_10, counter_no_clk_1_out_11,
       counter_no_clk_1_out_12, index, multiplexer_1_out, multiplexer_2_out, or_1_out, RST, STOP,
       subtractor_1_bout;
  wire [0:0] not_1_out;
  wire [3:0] multiplexer_6_out, \余数 , \商 ;
  wire [7:0] bit_extender_1_out, multiplexer_3_out, multiplexer_4_out, multiplexer_5_out, register_1_q,
       shifter_1_out, subtractor_1_out;
  wire [7:4] register_2_q;

  Hex_Digit_Display hex_digit_display_1 (.value(in_1));  // open: dp
  Hex_Digit_Display hex_digit_display_2 (.value(in_3));  // open: dp
  Clock clock_1 (.out(clock_1_out));
  and and_1 (and_1_out, ~STOP, in_4);  // AND_Gate
  Hex_Digit_Display hex_digit_display_3 (.value(\商 ));  // open: dp
  Shifter #(.shift("lr")) shifter_1 (.in(multiplexer_4_out), .\dist (3'b001), .out(shifter_1_out));
  or or_1 (or_1_out, index, RST);
  Multiplexer #(.enable("false")) multiplexer_1 (
    .in0(1'b1), .in1(clock_1_out), .out(multiplexer_1_out), .sel(and_1_out));
  Clock clock_2 (.out(clock_2_out));
  assign bit_extender_1_out = {{4{1'b0}}, in_1};  // Bit_Extender bit_extender_1
  // Probe on bit_extender_1_out
  Register #(.Select("low")) register_1 (
    .D(shifter_1_out), .Q(register_1_q), .clk(multiplexer_2_out));  // open: en, clr
  Multiplexer #(.enable("false")) multiplexer_2 (
    .in0(multiplexer_1_out), .in1(clock_2_out), .out(multiplexer_2_out), .sel(RST));
  Hex_Digit_Display hex_digit_display_4 (.value(\余数 ));  // open: dp
  Multiplexer #(.width(8), .enable("false")) multiplexer_3 (
    .in0(multiplexer_5_out), .in1(bit_extender_1_out), .out(multiplexer_3_out), .sel(or_1_out));
  Multiplexer #(.width(8), .enable("false")) multiplexer_4 (
    .in0(register_1_q), .in1({in_3, 4'b0000}), .out(multiplexer_4_out), .sel(or_1_out));
  // Probe on {register_2_q, \余数 }
  Register #(.Select("low")) register_2 (
    .D(multiplexer_3_out), .Q({register_2_q, \余数 }), .clk(multiplexer_2_out));  // open: en, clr
  // Probe on multiplexer_4_out
  Subtractor subtractor_1 (
    .a({register_2_q, \余数 }), .b(multiplexer_4_out), .out(subtractor_1_out), .bout(subtractor_1_bout));  // open: bin
  Button button_1 (.out(RST));
  Multiplexer #(.width(8), .enable("false")) multiplexer_5 (
    .in0(subtractor_1_out), .in1({register_2_q, \余数 }), .out(multiplexer_5_out), .sel(subtractor_1_bout));
  not not_1 (not_1_out[0], subtractor_1_bout);
  Multiplexer #(.width(4), .enable("false")) multiplexer_6 (
    .in0(\商 ), .in1(4'b0000), .out(multiplexer_6_out), .sel(or_1_out));
  LED led_1 (.in(STOP));
  // Probe on \商 
  Register #(.width(4), .Select("low")) register_3 (
    .D({multiplexer_6_out[2:0], not_1_out[0]}), .Q(\商 ), .clk(multiplexer_2_out));  // open: en, clr
  and and_2 (index, ~counter_no_clk_1_out_10, ~counter_no_clk_1_out_11, ~counter_no_clk_1_out_12);  // AND_Gate
  and and_3 (STOP, counter_no_clk_1_out_10, ~counter_no_clk_1_out_11, counter_no_clk_1_out_12);  // AND_Gate
  counter_no_clk counter_no_clk_1 (
    .CLK(multiplexer_2_out), .LD(LD), .CLR(RST), .D0(D0D1D2D3[0]), .D1(D0D1D2D3[1]), .D2(D0D1D2D3[2]),
    .D3(D0D1D2D3[3]), .ENP(1'b1), .ENT(1'b1), .out_10(counter_no_clk_1_out_10),
    .out_11(counter_no_clk_1_out_11), .out_12(counter_no_clk_1_out_12));  // open: out_13, out_14

  // Other names for the same wires on the sheet: 除数[3:0] = in_3; DIN[3:0] = D0D1D2D3; LOAD = in_4; Z[7:0] = out_7;
  //   被除数[3:0] = in_1

  // Notes on the sheet:
  //   ÷
  //   =
  //   余
endmodule

module \booth_乘法  (
  input  [3:0] in_1,
  input  [3:0] D0D1D2D3,
  input  [3:0] in_3,
  input  in_4,
  input  LD,
  input  CLR,
  output [7:0] out_7
);

  wire and_1_out, clock_1_out, clock_2_out, counter_no_clk_1_out_10, counter_no_clk_1_out_11,
       counter_no_clk_1_out_12, index, multiplexer_1_out, multiplexer_2_out, or_1_out, or_2_out,
       register_3_q, RST, STOP;
  wire [0:0] multiplexer_6_out;
  wire [3:0] adder_2_out, \minus_X补 , multiplexer_3_out, multiplexer_4_out, multiplexer_5_out, not_1_out,
       shifter_1_out;

  not not_1 (not_1_out[0], in_1[0]);
  not not_2 (not_1_out[1], in_1[1]);
  not not_3 (not_1_out[2], in_1[2]);
  not not_4 (not_1_out[3], in_1[3]);
  // Probe on in_1
  Clock clock_1 (.out(clock_1_out));
  Adder #(.width(4)) adder_1 (.a(4'b0001), .b(not_1_out), .out(\minus_X补 ), .cin(1'b0));  // open: cout
  // Probe on \minus_X补 
  Multiplexer #(.enable("false")) multiplexer_1 (
    .in0(1'b1), .in1(clock_1_out), .out(multiplexer_1_out), .sel(and_1_out));
  Clock clock_2 (.out(clock_2_out));
  and and_1 (and_1_out, ~STOP, in_4);  // AND_Gate
  Hex_Digit_Display hex_digit_display_1 (.value(in_1));  // open: dp
  Multiplexer #(.enable("false")) multiplexer_2 (
    .in0(multiplexer_1_out), .in1(clock_2_out), .out(multiplexer_2_out), .sel(RST));
  Hex_Digit_Display hex_digit_display_2 (.value(in_3));  // open: dp
  Hex_Digit_Display hex_digit_display_3 (.value(out_7[7:4]));  // open: dp
  Multiplexer #(.width(4), .enable("false")) multiplexer_3 (
    .in0(shifter_1_out), .in1(4'b0000), .out(multiplexer_3_out), .sel(or_1_out));
  or or_1 (or_1_out, index, RST);
  Multiplexer #(.select(2), .width(4), .enable("false")) multiplexer_4 (
    .in0(4'b0000), .in1(in_1), .in2(\minus_X补 ), .in3(4'b0000), .out(multiplexer_4_out),
    .sel({out_7[0], multiplexer_6_out[0]}));
  // Probe on multiplexer_4_out
  Hex_Digit_Display hex_digit_display_4 (.value(out_7[3:0]));  // open: dp
  Register #(.width(4), .Select("low")) register_1 (
    .D(multiplexer_3_out), .Q(out_7[7:4]), .clk(multiplexer_2_out));  // open: en, clr
  // Probe on out_7[7:4]
  Adder #(.width(4)) adder_2 (.a(out_7[7:4]), .b(multiplexer_4_out), .out(adder_2_out), .cin(1'b0));  // open: cout
  Shifter #(.width(4), .shift("ar")) shifter_1 (.in(adder_2_out), .\dist (2'b01), .out(shifter_1_out));
  Multiplexer #(.width(4), .enable("false")) multiplexer_5 (
    .in0({adder_2_out[0], out_7[3:1]}), .in1(in_3), .out(multiplexer_5_out), .sel(or_2_out));
  or or_2 (or_2_out, index, RST);
  Register #(.width(4), .Select("low")) register_2 (
    .D(multiplexer_5_out), .Q(out_7[3:0]), .clk(multiplexer_2_out));  // open: en, clr
  // Probe on out_7[3:0]
  Register #(.width(1), .Select("low")) register_3 (
    .D(out_7[0]), .Q(register_3_q), .clk(multiplexer_2_out));  // open: en, clr
  Multiplexer #(.enable("false")) multiplexer_6 (
    .in0(register_3_q), .in1(1'b0), .out(multiplexer_6_out[0]), .sel(index));
  Button button_1 (.out(RST));
  LED led_1 (.in(STOP));
  and and_2 (index, ~counter_no_clk_1_out_10, ~counter_no_clk_1_out_11, ~counter_no_clk_1_out_12);  // AND_Gate
  and and_3 (STOP, counter_no_clk_1_out_10, ~counter_no_clk_1_out_11, counter_no_clk_1_out_12);  // AND_Gate
  counter_no_clk counter_no_clk_1 (
    .CLK(multiplexer_2_out), .LD(LD), .CLR(RST), .D0(D0D1D2D3[0]), .D1(D0D1D2D3[1]), .D2(D0D1D2D3[2]),
    .D3(D0D1D2D3[3]), .ENP(1'b1), .ENT(1'b1), .out_10(counter_no_clk_1_out_10),
    .out_11(counter_no_clk_1_out_11), .out_12(counter_no_clk_1_out_12));  // open: out_13, out_14

  // Other names for the same wires on the sheet: DIN[3:0] = D0D1D2D3; LOAD = in_4; X[3:0] = in_1; Y[3:0] = in_3;
  //   Z[7:0] = out_7

  // Notes on the sheet:
  //   ×
  //   =
endmodule
