// Logisim project 实验4.circ as structural Verilog: 11 circuits, main circuit 4位快速加法器CLA
module \_4位快速加法器CLA  (
  input  [3:0] in_1,
  input  [3:0] in_2,
  input  in_3,
  output [3:0] out_4,
  output out_5,
  output out_6,
  output COUT
);

  wire C1, C2, C3, \全加器_1_g_ab , \全加器_1_p_a_b , \全加器_2_g_ab , \全加器_2_p_a_b , \全加器_3_g_ab , \全加器_3_p_a_b ,
       \全加器_4_g_ab , \全加器_4_p_a_b ;

  Hex_Digit_Display hex_digit_display_1 (.value(in_1));  // open: dp
  \全加器  \u_全加器_1  (.A(in_2[3]), .B(in_1[3]), .Cin(C3), .F(out_4[3]), .G_AB(\全加器_1_g_ab ), .P_A_B(\全加器_1_p_a_b ));
  Hex_Digit_Display hex_digit_display_2 (.value(in_2));  // open: dp
  \全加器  \u_全加器_2  (.A(in_2[2]), .B(in_1[2]), .Cin(C2), .F(out_4[2]), .G_AB(\全加器_2_g_ab ), .P_A_B(\全加器_2_p_a_b ));
  Hex_Digit_Display hex_digit_display_3 (.value(out_4));  // open: dp
  \全加器  \u_全加器_3  (.A(in_2[1]), .B(in_1[1]), .Cin(C1), .F(out_4[1]), .G_AB(\全加器_3_g_ab ), .P_A_B(\全加器_3_p_a_b ));
  \_4位先行进位加法器CLA  \u_4位先行进位加法器cla_1  (
    .in_1(\全加器_4_p_a_b ), .in_2(\全加器_4_g_ab ), .out_10(C1), .in_3(in_3), .in_4(\全加器_3_p_a_b ),
    .in_5(\全加器_3_g_ab ), .out_11(C2), .out_12(out_5), .in_6(\全加器_2_p_a_b ), .in_7(\全加器_2_g_ab ), .out_13(C3),
    .out_14(out_6), .in_8(\全加器_1_p_a_b ), .in_9(\全加器_1_g_ab ), .out_15(COUT));
  \全加器  \u_全加器_4  (.A(in_2[0]), .B(in_1[0]), .Cin(in_3), .F(out_4[0]), .G_AB(\全加器_4_g_ab ), .P_A_B(\全加器_4_p_a_b ));

  // Other names for the same wires on the sheet: C4 = COUT; Cin = in_3; Gg = out_6; Pg = out_5; X[3:0] = in_1;
  //   Y[3:0] = in_2; F1 = out_4[0]; Z[3:0] = out_4; F2 = out_4[1]; F3 = out_4[2]; F4 = out_4[3]

  // Notes on the sheet:
  //   +
  //   =
endmodule

module \_4位先行进位加法器CLA  (
  input  in_1,
  input  in_2,
  input  in_3,
  input  in_4,
  input  in_5,
  input  in_6,
  input  in_7,
  input  in_8,
  input  in_9,
  output out_10,
  output out_11,
  output out_12,
  output out_13,
  output out_14,
  output out_15
);

  wire P0C0_out, P1G0_out, P1P0C0_out, P2G1_out, P2P1G0_out, P2P1P0C0_out, P3G2_out, P3P2G1_out,
       P3P2P1G0_out, P3P2P1P0C0_out;

  or or_1 (out_14, P3P2P1G0_out, P3P2G1_out, P3G2_out, in_9);
  and and_1 (out_12, in_1, in_4, in_6, in_8);
  and P3P2G1 (P3P2G1_out, in_8, in_6, in_5);
  and P3G2 (P3G2_out, in_8, in_7);
  or or_2 (out_15, in_9, P3G2_out, P3P2G1_out, P3P2P1G0_out, P3P2P1P0C0_out);
  and P3P2P1G0 (P3P2P1G0_out, in_8, in_6, in_4, in_2);
  and P3P2P1P0C0 (P3P2P1P0C0_out, in_8, in_6, in_4, in_1, in_3);
  or or_3 (out_13, in_7, P2G1_out, P2P1G0_out, P2P1P0C0_out);
  and P2P1G0 (P2P1G0_out, in_6, in_4, in_2);
  and P2G1 (P2G1_out, in_6, in_5);
  and P2P1P0C0 (P2P1P0C0_out, in_6, in_4, in_1, in_3);
  or or_4 (out_11, in_5, P1G0_out, P1P0C0_out);
  and P1G0 (P1G0_out, in_4, in_2);
  and P1P0C0 (P1P0C0_out, in_4, in_1, in_3);
  or or_5 (out_10, in_2, P0C0_out);
  and P0C0 (P0C0_out, in_3, in_1);

  // Other names for the same wires on the sheet: C0 = in_3; C1 = out_10; C2 = out_11; C3 = out_13; C4 = out_15;
  //   Cg = out_14; G0 = in_2; G1 = in_5; G2 = in_7; G3 = in_9; P0 = in_1; P1 = in_4; P2 = in_6; P3 = in_8;
  //   Pg = out_12
endmodule

module \全加器  (
  input  A,
  input  B,
  input  Cin,
  output F,
  output G_AB,
  output P_A_B
);

  xor xor_1 (F, A, B, Cin);
  and and_1 (G_AB, A, B);
  or or_1 (P_A_B, B, A);
endmodule

module \_16位两级先行进位加法器实验  (
  input  in_1,
  input  [15:0] in_2,
  input  [15:0] in_3,
  output out_4,
  output out_5,
  output out_6,
  output [15:0] out_7
);

  wire C1, C2, C3, C4, \n4位快速加法器cla_1_out_5 , \n4位快速加法器cla_1_out_6 , \n4位快速加法器cla_2_out_5 ,
       \n4位快速加法器cla_2_out_6 , \n4位快速加法器cla_3_out_5 , \n4位快速加法器cla_3_out_6 , \n4位快速加法器cla_4_out_5 ,
       \n4位快速加法器cla_4_out_6 ;

  \_4位快速加法器CLA  \u_4位快速加法器cla_1  (
    .in_1(in_2[15:12]), .out_4(out_7[15:12]), .out_5(\n4位快速加法器cla_1_out_5 ), .in_2(in_3[15:12]),
    .out_6(\n4位快速加法器cla_1_out_6 ), .in_3(C3), .COUT(out_4));
  \_4位快速加法器CLA  \u_4位快速加法器cla_2  (
    .in_1(in_2[11:8]), .out_4(out_7[11:8]), .out_5(\n4位快速加法器cla_2_out_5 ), .in_2(in_3[11:8]),
    .out_6(\n4位快速加法器cla_2_out_6 ), .in_3(C2));  // open: COUT
  \_4位快速加法器CLA  \u_4位快速加法器cla_3  (
    .in_1(in_2[7:4]), .out_4(out_7[7:4]), .out_5(\n4位快速加法器cla_3_out_5 ), .in_2(in_3[7:4]),
    .out_6(\n4位快速加法器cla_3_out_6 ), .in_3(C1));  // open: COUT
  \_4位先行进位加法器CLA  \u_4位先行进位加法器cla_1  (
    .in_1(\n4位快速加法器cla_4_out_5 ), .in_2(\n4位快速加法器cla_4_out_6 ), .out_10(C1), .in_3(in_1),
    .in_4(\n4位快速加法器cla_3_out_5 ), .in_5(\n4位快速加法器cla_3_out_6 ), .out_11(C2), .out_12(out_5),
    .in_6(\n4位快速加法器cla_2_out_5 ), .in_7(\n4位快速加法器cla_2_out_6 ), .out_13(C3), .out_14(out_6),
    .in_8(\n4位快速加法器cla_1_out_5 ), .in_9(\n4位快速加法器cla_1_out_6 ), .out_15(C4));
  \_4位快速加法器CLA  \u_4位快速加法器cla_4  (
    .in_1(in_2[3:0]), .out_4(out_7[3:0]), .out_5(\n4位快速加法器cla_4_out_5 ), .in_2(in_3[3:0]),
    .out_6(\n4位快速加法器cla_4_out_6 ), .in_3(in_1));  // open: COUT
  // Probe on in_2
  // Probe on in_3
  // Probe on out_7

  // Other names for the same wires on the sheet: C0 = in_1; C16 = out_4; Gg = out_6; Pg = out_5; S[15:0] = out_7;
  //   S0[3:0] = out_7[3:0]; S1[3:0] = out_7[7:4]; S2[3:0] = out_7[11:8]; S3[3:0] = out_7[15:12]; X[15:0] = in_2;
  //   Y[15:0] = in_3

  // Notes on the sheet:
  //   =
endmodule

module \_32位加法器  (
  input  [31:0] in_1,
  input  in_2,
  input  [31:0] in_3,
  output out_4,
  output [31:0] out_5,
  output out_6,
  output out_7,
  output out_8,
  output out_9
);

  wire and_1_out, and_2_out, and_3_out, \n16位两级先行进位加法器实验_1_out_5 , \n16位两级先行进位加法器实验_1_out_6 ,
       \n16位两级先行进位加法器实验_2_out_5 , \n16位两级先行进位加法器实验_2_out_6 , not_1_out, not_2_out, not_3_out, or_1_out;

  \_16位两级先行进位加法器实验  \u_16位两级先行进位加法器实验_1  (
    .in_2(in_3[31:16]), .in_3(in_1[31:16]), .in_1(or_1_out), .out_7(out_5[31:16]), .out_4(out_9),
    .out_5(\n16位两级先行进位加法器实验_1_out_5 ), .out_6(\n16位两级先行进位加法器实验_1_out_6 ));
  \_16位两级先行进位加法器实验  \u_16位两级先行进位加法器实验_2  (
    .in_2(in_3[15:0]), .in_3(in_1[15:0]), .in_1(in_2), .out_7(out_5[15:0]),
    .out_5(\n16位两级先行进位加法器实验_2_out_5 ), .out_6(\n16位两级先行进位加法器实验_2_out_6 ));  // open: out_4
  or or_1 (or_1_out, and_1_out, \n16位两级先行进位加法器实验_2_out_6 );
  and and_1 (and_1_out, \n16位两级先行进位加法器实验_2_out_5 , in_2);
  // Probe on in_1
  // Probe on in_3
  // Probe on out_5
  xor xor_1 (out_6, in_2, out_9);
  Comparator #(.width(32)) comparator_1 (.a(out_5), .b({32{1'b0}}), .eq(out_7));  // open: gt, lt
  not not_1 (not_1_out, in_1[31]);
  not not_2 (not_2_out, in_3[31]);
  not not_3 (not_3_out, out_5[31]);
  and and_2 (and_2_out, not_1_out, not_2_out, out_5[31]);
  or or_2 (out_4, and_2_out, and_3_out);
  and and_3 (and_3_out, in_1[31], in_3[31], not_3_out);

  assign out_8 = out_5[31];

  // Other names for the same wires on the sheet: CF = out_6; Cin = in_2; Cout = out_9; OF = out_4; S[31:0] = out_5;
  //   S1_32[15:0] = out_5[15:0]; S2_32[15:0] = out_5[31:16]; SF = out_5[31]; X[31:0] = in_1; Y[31:0] = in_3;
  //   ZF = out_7
endmodule

module \_32位ALU  (
  input  [3:0] in_1,
  input  [31:0] in_2,
  input  [31:0] in_3,
  output [31:0] out_4,
  output out_5
);

  wire CF, multiplexer_2_out, OF, SF, xor_1_out, xor_2_out, \操作控制部件_1_out_2 , \操作控制部件_1_out_3 ,
       \操作控制部件_1_out_4 , \操作控制部件_1_out_5 ;
  wire [2:0] \操作控制部件_1_out_6 ;
  wire [31:0] bit_extender_1_out, bit_extender_2_out, \n32位加法器_1_out_5 , \n32位桶形移位器_1_out_5 , \与门阵列_1_out_3 ,
       \异或门阵列_1_out_3 , \异或门阵列_2_out_3 , \或门阵列_1_out_3 ;

  assign bit_extender_1_out = {{31{\操作控制部件_1_out_2 }}, \操作控制部件_1_out_2 };  // Bit_Extender bit_extender_1
  \或门阵列  \u_或门阵列_1  (.in_1(in_2), .in_2(in_3), .out_3(\或门阵列_1_out_3 ));
  \与门阵列  \u_与门阵列_1  (.in_1(in_2), .in_2(in_3), .out_3(\与门阵列_1_out_3 ));
  \异或门阵列  \u_异或门阵列_1  (.in_1(in_2), .in_2(in_3), .out_3(\异或门阵列_1_out_3 ));
  \_32位桶形移位器  \u_32位桶形移位器_1  (
    .in_1(in_2), .out_5(\n32位桶形移位器_1_out_5 ), .in_2(\操作控制部件_1_out_3 ), .in_3(\操作控制部件_1_out_5 ),
    .in_4(in_3[4:0]));
  \异或门阵列  \u_异或门阵列_2  (.in_1(in_3), .in_2(bit_extender_1_out), .out_3(\异或门阵列_2_out_3 ));
  \_32位加法器  \u_32位加法器_1  (
    .out_4(OF), .in_1(in_2), .out_5(\n32位加法器_1_out_5 ), .out_6(CF), .out_7(out_5), .in_2(\操作控制部件_1_out_2 ),
    .out_8(SF), .in_3(\异或门阵列_2_out_3 ));  // open: out_9
  Multiplexer #(.select(3), .width(32), .enable("false")) multiplexer_1 (
    .in0(\n32位加法器_1_out_5 ), .in1(\或门阵列_1_out_3 ), .in2(\与门阵列_1_out_3 ), .in3(\异或门阵列_1_out_3 ),
    .in4(\n32位桶形移位器_1_out_5 ), .in5(in_3), .in6(bit_extender_2_out), .out(out_4), .sel(\操作控制部件_1_out_6 ));  // open: in7
  \操作控制部件  \u_操作控制部件_1  (
    .out_2(\操作控制部件_1_out_2 ), .out_3(\操作控制部件_1_out_3 ), .out_4(\操作控制部件_1_out_4 ), .out_5(\操作控制部件_1_out_5 ),
    .out_6(\操作控制部件_1_out_6 ), .in_1(in_1));
  xor xor_1 (xor_1_out, \操作控制部件_1_out_2 , CF);
  xor xor_2 (xor_2_out, OF, SF);
  // Probe on in_2
  // Probe on in_3
  // Probe on out_4
  Multiplexer #(.enable("false")) multiplexer_2 (
    .in0(xor_1_out), .in1(xor_2_out), .out(multiplexer_2_out), .sel(\操作控制部件_1_out_4 ));
  assign bit_extender_2_out = {{31{1'b0}}, multiplexer_2_out};  // Bit_Extender bit_extender_2

  // Other names for the same wires on the sheet: A[31:0] = in_2; ALUctr[3:0] = in_1; B[31:0] = in_3;
  //   Result[31:0] = out_4; Zero = out_5

  // Notes on the sheet:
  //                   输入引脚区
endmodule

module \操作控制部件  (
  input  [3:0] in_1,
  output out_2,
  output out_3,
  output out_4,
  output out_5,
  output [2:0] out_6
);

  wire and_1_out, and_2_out, and_6_out, and_7_out, and_8_out, and_9_out, and_10_out, and_11_out, and_12_out;

  and and_1 (and_1_out, in_1[3], ~in_1[2], ~in_1[1], ~in_1[0]);  // AND_Gate
  or or_1 (out_2, and_1_out, and_2_out);
  and and_2 (and_2_out, ~in_1[3], ~in_1[2], in_1[1]);  // AND_Gate
  and and_3 (out_4, ~in_1[3], ~in_1[2], in_1[1], ~in_1[0]);  // AND_Gate
  and and_4 (out_5, in_1[3], in_1[2], ~in_1[1], in_1[0]);  // AND_Gate
  and and_5 (out_3, ~in_1[3], ~in_1[2], ~in_1[1], in_1[0]);  // AND_Gate
  and and_6 (and_6_out, ~in_1[3], ~in_1[1], in_1[0]);  // AND_Gate
  and and_7 (and_7_out, in_1[3], in_1[2], in_1[0]);
  and and_8 (and_8_out, ~in_1[3], ~in_1[2], in_1[1]);  // AND_Gate
  and and_9 (and_9_out, ~in_1[3], ~in_1[2], in_1[1]);  // AND_Gate
  and and_10 (and_10_out, ~in_1[3], in_1[2], ~in_1[0]);  // AND_Gate
  and and_11 (and_11_out, ~in_1[3], in_1[2], ~in_1[1], ~in_1[0]);  // AND_Gate
  and and_12 (and_12_out, in_1[2], in_1[1], in_1[0]);
  or or_2 (out_6[2], and_6_out, and_7_out, and_8_out);
  or or_3 (out_6[1], and_9_out, and_10_out);
  or or_4 (out_6[0], and_11_out, and_12_out);

  // Other names for the same wires on the sheet: ALctr = out_5; ALUctr[3:0] = in_1; D = in_1[0]; C = in_1[1];
  //   B = in_1[2]; A = in_1[3]; OPctr[2:0] = out_6; SFTctr = out_3; SIGctr = out_4; SUBctr = out_2

  // Notes on the sheet:
  //   op2
  //   op1
endmodule

module \_32位桶形移位器  (
  input  [31:0] in_1,
  input  in_2,
  input  in_3,
  input  [4:0] in_4,
  output [31:0] out_5
);

  wire [31:0] l1_1_out_2, l2_1_out_2, l4_1_out_2, l8_1_out_2, l16_1_out_2, multiplexer_1_out,
       multiplexer_2_out, multiplexer_3_out, multiplexer_4_out, r1_1_out_3, r2_1_out_3, r4_1_out_3,
       r8_1_out_3, r16_1_out_3;

  R1 r1_1 (.in_1(in_1), .in_2(in_3), .out_3(r1_1_out_3));
  L1 l1_1 (.in_1(in_1), .out_2(l1_1_out_2));
  Multiplexer #(.select(2), .width(32), .enable("false")) multiplexer_1 (
    .in0(in_1), .in1(in_1), .in2(r1_1_out_3), .in3(l1_1_out_2), .out(multiplexer_1_out), .sel({in_4[0], in_2}));
  R2 r2_1 (.in_1(multiplexer_1_out), .in_2(in_3), .out_3(r2_1_out_3));
  L2 l2_1 (.in_1(multiplexer_1_out), .out_2(l2_1_out_2));
  Multiplexer #(.select(2), .width(32), .enable("false")) multiplexer_2 (
    .in0(multiplexer_1_out), .in1(multiplexer_1_out), .in2(r2_1_out_3), .in3(l2_1_out_2),
    .out(multiplexer_2_out), .sel({in_4[1], in_2}));
  R4 r4_1 (.in_1(multiplexer_2_out), .in_2(in_3), .out_3(r4_1_out_3));
  L4 l4_1 (.in_1(multiplexer_2_out), .out_2(l4_1_out_2));
  Multiplexer #(.select(2), .width(32), .enable("false")) multiplexer_3 (
    .in0(multiplexer_2_out), .in1(multiplexer_2_out), .in2(r4_1_out_3), .in3(l4_1_out_2),
    .out(multiplexer_3_out), .sel({in_4[2], in_2}));
  R8 r8_1 (.in_1(multiplexer_3_out), .in_2(in_3), .out_3(r8_1_out_3));
  L8 l8_1 (.in_1(multiplexer_3_out), .out_2(l8_1_out_2));
  Multiplexer #(.select(2), .width(32), .enable("false")) multiplexer_4 (
    .in0(multiplexer_3_out), .in1(multiplexer_3_out), .in2(r8_1_out_3), .in3(l8_1_out_2),
    .out(multiplexer_4_out), .sel({in_4[3], in_2}));
  R16 r16_1 (.in_1(multiplexer_4_out), .in_2(in_3), .out_3(r16_1_out_3));
  L16 l16_1 (.in_1(multiplexer_4_out), .out_2(l16_1_out_2));
  Multiplexer #(.select(2), .width(32), .enable("false")) multiplexer_5 (
    .in0(multiplexer_4_out), .in1(multiplexer_4_out), .in2(r16_1_out_3), .in3(l16_1_out_2), .out(out_5),
    .sel({in_4[4], in_2}));

  // Other names for the same wires on the sheet: SHAMT[4:0] = in_4; L_R = in_2; A_L = in_3; INPUT[31:0] = in_1;
  //   OUTPUT[31:0] = out_5

  // Notes on the sheet:
  //                  1 左移
  //   1算数右移
endmodule

module \异或门阵列  (
  input  [31:0] in_1,
  input  [31:0] in_2,
  output [31:0] out_3
);

  xor xor_1 (out_3[0], in_2[0], in_1[0]);
  xor xor_2 (out_3[1], in_2[1], in_1[1]);
  xor xor_3 (out_3[2], in_2[2], in_1[2]);
  xor xor_4 (out_3[3], in_2[3], in_1[3]);
  xor xor_5 (out_3[4], in_2[4], in_1[4]);
  xor xor_6 (out_3[5], in_2[5], in_1[5]);
  xor xor_7 (out_3[6], in_2[6], in_1[6]);
  xor xor_8 (out_3[7], in_2[7], in_1[7]);
  xor xor_9 (out_3[8], in_2[8], in_1[8]);
  xor xor_10 (out_3[9], in_2[9], in_1[9]);
  xor xor_11 (out_3[10], in_2[10], in_1[10]);
  xor xor_12 (out_3[11], in_2[11], in_1[11]);
  xor xor_13 (out_3[12], in_2[12], in_1[12]);
  xor xor_14 (out_3[13], in_2[13], in_1[13]);
  xor xor_15 (out_3[14], in_2[14], in_1[14]);
  xor xor_16 (out_3[15], in_2[15], in_1[15]);
  xor xor_17 (out_3[16], in_2[16], in_1[16]);
  xor xor_18 (out_3[17], in_2[17], in_1[17]);
  xor xor_19 (out_3[18], in_2[18], in_1[18]);
  xor xor_20 (out_3[19], in_2[19], in_1[19]);
  xor xor_21 (out_3[20], in_2[20], in_1[20]);
  xor xor_22 (out_3[21], in_2[21], in_1[21]);
  xor xor_23 (out_3[22], in_2[22], in_1[22]);
  xor xor_24 (out_3[23], in_2[23], in_1[23]);
  xor xor_25 (out_3[24], in_2[24], in_1[24]);
  xor xor_26 (out_3[25], in_2[25], in_1[25]);
  xor xor_27 (out_3[26], in_2[26], in_1[26]);
  xor xor_28 (out_3[27], in_2[27], in_1[27]);
  xor xor_29 (out_3[28], in_2[28], in_1[28]);
  xor xor_30 (out_3[29], in_2[29], in_1[29]);
  xor xor_31 (out_3[30], in_2[30], in_1[30]);
  xor xor_32 (out_3[31], in_2[31], in_1[31]);

  // Other names for the same wires on the sheet: A[31:0] = in_1; A0 = in_1[0]; A1 = in_1[1]; A2 = in_1[2];
  //   A3 = in_1[3]; A4 = in_1[4]; A5 = in_1[5]; A6 = in_1[6]; A7 = in_1[7]; A8 = in_1[8]; A9 = in_1[9];
  //   A10 = in_1[10]; A11 = in_1[11]; A12 = in_1[12]; A13 = in_1[13]; A14 = in_1[14]; A15 = in_1[15]; A16 = in_1[16];
  //   A17 = in_1[17]; A18 = in_1[18]; A19 = in_1[19]; A20 = in_1[20]; A21 = in_1[21]; A22 = in_1[22]; A23 = in_1[23];
  //   A24 = in_1[24]; A25 = in_1[25]; A26 = in_1[26]; A27 = in_1[27]; A28 = in_1[28]; A29 = in_1[29]; A30 = in_1[30];
  //   A31 = in_1[31]; B[31:0] = in_2; B0 = in_2[0]; B1 = in_2[1]; B2 = in_2[2]; B3 = in_2[3]; B4 = in_2[4];
  //   B5 = in_2[5]; B6 = in_2[6]; B7 = in_2[7]; B8 = in_2[8]; B9 = in_2[9]; B10 = in_2[10]; B11 = in_2[11];
  //   B12 = in_2[12]; B13 = in_2[13]; B14 = in_2[14]; B15 = in_2[15]; B16 = in_2[16]; B17 = in_2[17]; B18 = in_2[18];
  //   B19 = in_2[19]; B20 = in_2[20]; B21 = in_2[21]; B22 = in_2[22]; B23 = in_2[23]; B24 = in_2[24]; B25 = in_2[25];
  //   B26 = in_2[26]; B27 = in_2[27]; B28 = in_2[28]; B29 = in_2[29]; B30 = in_2[30]; B31 = in_2[31];
  //   OUTPUT[31:0] = out_3
endmodule

module \与门阵列  (
  input  [31:0] in_1,
  input  [31:0] in_2,
  output [31:0] out_3
);

  and and_1 (out_3[0], in_2[0], in_1[0]);
  and and_2 (out_3[1], in_2[1], in_1[1]);
  and and_3 (out_3[2], in_2[2], in_1[2]);
  and and_4 (out_3[3], in_2[3], in_1[3]);
  and and_5 (out_3[4], in_2[4], in_1[4]);
  and and_6 (out_3[5], in_2[5], in_1[5]);
  and and_7 (out_3[6], in_2[6], in_1[6]);
  and and_8 (out_3[7], in_2[7], in_1[7]);
  and and_9 (out_3[8], in_2[8], in_1[8]);
  and and_10 (out_3[9], in_2[9], in_1[9]);
  and and_11 (out_3[10], in_2[10], in_1[10]);
  and and_12 (out_3[11], in_2[11], in_1[11]);
  and and_13 (out_3[12], in_2[12], in_1[12]);
  and and_14 (out_3[13], in_2[13], in_1[13]);
  and and_15 (out_3[14], in_2[14], in_1[14]);
  and and_16 (out_3[15], in_2[15], in_1[15]);
  and and_17 (out_3[16], in_2[16], in_1[16]);
  and and_18 (out_3[17], in_2[17], in_1[17]);
  and and_19 (out_3[18], in_2[18], in_1[18]);
  and and_20 (out_3[19], in_2[19], in_1[19]);
  and and_21 (out_3[20], in_2[20], in_1[20]);
  and and_22 (out_3[21], in_2[21], in_1[21]);
  and and_23 (out_3[22], in_2[22], in_1[22]);
  and and_24 (out_3[23], in_2[23], in_1[23]);
  and and_25 (out_3[24], in_2[24], in_1[24]);
  and and_26 (out_3[25], in_2[25], in_1[25]);
  and and_27 (out_3[26], in_2[26], in_1[26]);
  and and_28 (out_3[27], in_2[27], in_1[27]);
  and and_29 (out_3[28], in_2[28], in_1[28]);
  and and_30 (out_3[29], in_2[29], in_1[29]);
  and and_31 (out_3[30], in_2[30], in_1[30]);
  and and_32 (out_3[31], in_2[31], in_1[31]);

  // Other names for the same wires on the sheet: A[31:0] = in_1; A0 = in_1[0]; A1 = in_1[1]; A2 = in_1[2];
  //   A3 = in_1[3]; A4 = in_1[4]; A5 = in_1[5]; A6 = in_1[6]; A7 = in_1[7]; A8 = in_1[8]; A9 = in_1[9];
  //   A10 = in_1[10]; A11 = in_1[11]; A12 = in_1[12]; A13 = in_1[13]; A14 = in_1[14]; A15 = in_1[15]; A16 = in_1[16];
  //   A17 = in_1[17]; A18 = in_1[18]; A19 = in_1[19]; A20 = in_1[20]; A21 = in_1[21]; A22 = in_1[22]; A23 = in_1[23];
  //   A24 = in_1[24]; A25 = in_1[25]; A26 = in_1[26]; A27 = in_1[27]; A28 = in_1[28]; A29 = in_1[29]; A30 = in_1[30];
  //   A31 = in_1[31]; B[31:0] = in_2; B0 = in_2[0]; B1 = in_2[1]; B2 = in_2[2]; B3 = in_2[3]; B4 = in_2[4];
  //   B5 = in_2[5]; B6 = in_2[6]; B7 = in_2[7]; B8 = in_2[8]; B9 = in_2[9]; B10 = in_2[10]; B11 = in_2[11];
  //   B12 = in_2[12]; B13 = in_2[13]; B14 = in_2[14]; B15 = in_2[15]; B16 = in_2[16]; B17 = in_2[17]; B18 = in_2[18];
  //   B19 = in_2[19]; B20 = in_2[20]; B21 = in_2[21]; B22 = in_2[22]; B23 = in_2[23]; B24 = in_2[24]; B25 = in_2[25];
  //   B26 = in_2[26]; B27 = in_2[27]; B28 = in_2[28]; B29 = in_2[29]; B30 = in_2[30]; B31 = in_2[31];
  //   OUTPUT[31:0] = out_3
endmodule

module \或门阵列  (
  input  [31:0] in_1,
  input  [31:0] in_2,
  output [31:0] out_3
);

  or or_1 (out_3[0], in_2[0], in_1[0]);
  or or_2 (out_3[1], in_2[1], in_1[1]);
  or or_3 (out_3[2], in_2[2], in_1[2]);
  or or_4 (out_3[3], in_2[3], in_1[3]);
  or or_5 (out_3[4], in_2[4], in_1[4]);
  or or_6 (out_3[5], in_2[5], in_1[5]);
  or or_7 (out_3[6], in_2[6], in_1[6]);
  or or_8 (out_3[7], in_2[7], in_1[7]);
  or or_9 (out_3[8], in_2[8], in_1[8]);
  or or_10 (out_3[9], in_2[9], in_1[9]);
  or or_11 (out_3[10], in_2[10], in_1[10]);
  or or_12 (out_3[11], in_2[11], in_1[11]);
  or or_13 (out_3[12], in_2[12], in_1[12]);
  or or_14 (out_3[13], in_2[13], in_1[13]);
  or or_15 (out_3[14], in_2[14], in_1[14]);
  or or_16 (out_3[15], in_2[15], in_1[15]);
  or or_17 (out_3[16], in_2[16], in_1[16]);
  or or_18 (out_3[17], in_2[17], in_1[17]);
  or or_19 (out_3[18], in_2[18], in_1[18]);
  or or_20 (out_3[19], in_2[19], in_1[19]);
  or or_21 (out_3[20], in_2[20], in_1[20]);
  or or_22 (out_3[21], in_2[21], in_1[21]);
  or or_23 (out_3[22], in_2[22], in_1[22]);
  or or_24 (out_3[23], in_2[23], in_1[23]);
  or or_25 (out_3[24], in_2[24], in_1[24]);
  or or_26 (out_3[25], in_2[25], in_1[25]);
  or or_27 (out_3[26], in_2[26], in_1[26]);
  or or_28 (out_3[27], in_2[27], in_1[27]);
  or or_29 (out_3[28], in_2[28], in_1[28]);
  or or_30 (out_3[29], in_2[29], in_1[29]);
  or or_31 (out_3[30], in_2[30], in_1[30]);
  or or_32 (out_3[31], in_2[31], in_1[31]);

  // Other names for the same wires on the sheet: A[31:0] = in_1; A0 = in_1[0]; A1 = in_1[1]; A2 = in_1[2];
  //   A3 = in_1[3]; A4 = in_1[4]; A5 = in_1[5]; A6 = in_1[6]; A7 = in_1[7]; A8 = in_1[8]; A9 = in_1[9];
  //   A10 = in_1[10]; A11 = in_1[11]; A12 = in_1[12]; A13 = in_1[13]; A14 = in_1[14]; A15 = in_1[15]; A16 = in_1[16];
  //   A17 = in_1[17]; A18 = in_1[18]; A19 = in_1[19]; A20 = in_1[20]; A21 = in_1[21]; A22 = in_1[22]; A23 = in_1[23];
  //   A24 = in_1[24]; A25 = in_1[25]; A26 = in_1[26]; A27 = in_1[27]; A28 = in_1[28]; A29 = in_1[29]; A30 = in_1[30];
  //   A31 = in_1[31]; B[31:0] = in_2; B0 = in_2[0]; B1 = in_2[1]; B2 = in_2[2]; B3 = in_2[3]; B4 = in_2[4];
  //   B5 = in_2[5]; B6 = in_2[6]; B7 = in_2[7]; B8 = in_2[8]; B9 = in_2[9]; B10 = in_2[10]; B11 = in_2[11];
  //   B12 = in_2[12]; B13 = in_2[13]; B14 = in_2[14]; B15 = in_2[15]; B16 = in_2[16]; B17 = in_2[17]; B18 = in_2[18];
  //   B19 = in_2[19]; B20 = in_2[20]; B21 = in_2[21]; B22 = in_2[22]; B23 = in_2[23]; B24 = in_2[24]; B25 = in_2[25];
  //   B26 = in_2[26]; B27 = in_2[27]; B28 = in_2[28]; B29 = in_2[29]; B30 = in_2[30]; B31 = in_2[31];
  //   OUTPUT[31:0] = out_3
endmodule
