// Logisim project 实验5.circ as structural Verilog: 9 circuits, main circuit 数据存储器实验
module \数据存储器实验  (
  input  [15:0] in_1,
  input  [31:0] in_2,
  input  in_3,
  input  in_4,
  input  in_5,
  input  in_6,
  input  [2:0] in_7,
  output [31:0] out_8
);

  wire [3:0] multiplexer_1_out;
  wire [7:0] Dout1, Dout2, Dout3, Dout4;
  wire [31:0] bit_extender_1_out, bit_extender_2_out, bit_extender_3_out, bit_extender_4_out;

  Multiplexer #(.select(3), .width(4), .enable("false")) multiplexer_1 (
    .in0({4{in_5}}), .in1({4{in_5}}), .in2({4{in_5}}), .in3({4{in_5}}), .in4({4{in_5}}),
    .in5({3'b000, in_5}), .in6({2'b00, {2{in_5}}}), .in7({4{in_5}}), .out(multiplexer_1_out), .sel(in_7));
  RAM #(.addrWidth(16), .bus("separate"), .Select("high")) ram_1 (
    .addr(in_1), .din(in_2[7:0]), .data(Dout1), .str(multiplexer_1_out[0]), .sel(in_6), .clk(in_3),
    .ld(1'b1), .clr(in_4));
  // Probe on out_8[7:0]
  // Probe on out_8[15:8]
  // Probe on out_8[23:16]
  // Probe on out_8[31:24]
  RAM #(.addrWidth(16), .bus("separate"), .Select("high")) ram_2 (
    .addr(in_1), .din(in_2[15:8]), .data(Dout2), .str(multiplexer_1_out[1]), .sel(in_6), .clk(in_3),
    .ld(1'b1), .clr(in_4));
  RAM #(.addrWidth(16), .bus("separate"), .Select("high")) ram_3 (
    .addr(in_1), .din(in_2[23:16]), .data(Dout3), .str(multiplexer_1_out[2]), .sel(in_6), .clk(in_3),
    .ld(1'b1), .clr(in_4));
  RAM #(.addrWidth(16), .bus("separate"), .Select("high")) ram_4 (
    .addr(in_1), .din(in_2[31:24]), .data(Dout4), .str(multiplexer_1_out[3]), .sel(in_6), .clk(in_3),
    .ld(1'b1), .clr(in_4));
  assign bit_extender_1_out = {{24{1'b0}}, Dout1};  // Bit_Extender bit_extender_1
  assign bit_extender_2_out = {{16{1'b0}}, {Dout2, Dout1}};  // Bit_Extender bit_extender_2
  assign bit_extender_3_out = {{24{Dout1[7]}}, Dout1};  // Bit_Extender bit_extender_3
  assign bit_extender_4_out = {{16{Dout2[7]}}, {Dout2, Dout1}};  // Bit_Extender bit_extender_4
  Multiplexer #(.select(3), .width(32), .enable("false")) multiplexer_2 (
    .in0({Dout4, Dout3, Dout2, Dout1}), .in1(bit_extender_1_out), .in2(bit_extender_2_out),
    .in5(bit_extender_3_out), .in6(bit_extender_4_out), .out(out_8), .sel(in_7));  // open: in3, in4, in7

  // Other names for the same wires on the sheet: WE = in_5; Addr[15:0] = in_1; CLK = in_3; CLR = in_4;
  //   Din[31:0] = in_2; Dout[31:0] = out_8; MemOp[2:0] = in_7; SEL = in_6
endmodule

module \ASCII码显示实验  (
  input  [7:0] in_1,
  input  in_2,
  output [7:0] out_3,
  output [7:0] out_4,
  output [7:0] out_5,
  output [7:0] out_6,
  output [7:0] out_7,
  output [7:0] out_8,
  output [7:0] out_9,
  output [7:0] out_10,
  output [7:0] out_11,
  output [7:0] out_12,
  output [7:0] out_13,
  output [7:0] out_14,
  output [7:0] out_15,
  output [7:0] out_16,
  output [7:0] out_17,
  output [7:0] out_18
);

  wire [15:0] adder_1_out, adder_2_out, adder_3_out, adder_4_out, adder_5_out, adder_6_out, adder_7_out,
       adder_8_out, adder_9_out, adder_10_out, adder_11_out, adder_12_out, adder_13_out, adder_14_out,
       adder_15_out;

  // Probe on in_1
  // Probe on {4'b0000, in_1, 4'b0000}
  Adder #(.width(16)) adder_1 (.a({4'b0000, in_1, 4'b0000}), .b(16'h1), .out(adder_1_out));  // open: cin, cout
  Adder #(.width(16)) adder_2 (.a({4'b0000, in_1, 4'b0000}), .b(16'h2), .out(adder_2_out));  // open: cin, cout
  Adder #(.width(16)) adder_3 (.a({4'b0000, in_1, 4'b0000}), .b(16'h3), .out(adder_3_out));  // open: cin, cout
  Adder #(.width(16)) adder_4 (.a({4'b0000, in_1, 4'b0000}), .b(16'h4), .out(adder_4_out));  // open: cin, cout
  Adder #(.width(16)) adder_5 (.a({4'b0000, in_1, 4'b0000}), .b(16'h5), .out(adder_5_out));  // open: cin, cout
  Adder #(.width(16)) adder_6 (.a({4'b0000, in_1, 4'b0000}), .b(16'h6), .out(adder_6_out));  // open: cin, cout
  Adder #(.width(16)) adder_7 (.a({4'b0000, in_1, 4'b0000}), .b(16'h7), .out(adder_7_out));  // open: cin, cout
  // Probe on {4'b0000, in_1, 4'b0000}
  // Probe on adder_1_out
  DotMatrix #(.inputtype("row"), .matrixcols(8), .matrixrows(16)) dotmatrix_1 (
    .row0(out_3), .row1(out_4), .row2(out_5), .row3(out_6), .row4(out_7), .row5(out_8), .row6(out_9),
    .row7(out_10), .row8(out_11), .row9(out_12), .row10(out_13), .row11(out_14), .row12(out_15),
    .row13(out_16), .row14(out_17), .row15(out_18));
  ROM #(.addrWidth(16), .Select("high")) rom_1 (.addr({4'b0000, in_1, 4'b0000}), .data(out_3), .sel(in_2));
  ROM #(.addrWidth(16), .Select("high")) rom_2 (.addr(adder_1_out), .data(out_4), .sel(in_2));
  ROM #(.addrWidth(16), .Select("high")) rom_3 (.addr(adder_2_out), .data(out_5), .sel(in_2));
  ROM #(.addrWidth(16), .Select("high")) rom_4 (.addr(adder_3_out), .data(out_6), .sel(in_2));
  ROM #(.addrWidth(16), .Select("high")) rom_5 (.addr(adder_4_out), .data(out_7), .sel(in_2));
  ROM #(.addrWidth(16), .Select("high")) rom_6 (.addr(adder_5_out), .data(out_8), .sel(in_2));
  ROM #(.addrWidth(16), .Select("high")) rom_7 (.addr(adder_6_out), .data(out_9), .sel(in_2));
  ROM #(.addrWidth(16), .Select("high")) rom_8 (.addr(adder_7_out), .data(out_10), .sel(in_2));
  Adder #(.width(16)) adder_8 (.a({4'b0000, in_1, 4'b0000}), .b(16'h8), .out(adder_8_out));  // open: cin, cout
  Adder #(.width(16)) adder_9 (.a({4'b0000, in_1, 4'b0000}), .b(16'h9), .out(adder_9_out));  // open: cin, cout
  Adder #(.width(16)) adder_10 (.a({4'b0000, in_1, 4'b0000}), .b(16'ha), .out(adder_10_out));  // open: cin, cout
  Adder #(.width(16)) adder_11 (.a({4'b0000, in_1, 4'b0000}), .b(16'hb), .out(adder_11_out));  // open: cin, cout
  Adder #(.width(16)) adder_12 (.a({4'b0000, in_1, 4'b0000}), .b(16'hc), .out(adder_12_out));  // open: cin, cout
  Adder #(.width(16)) adder_13 (.a({4'b0000, in_1, 4'b0000}), .b(16'hd), .out(adder_13_out));  // open: cin, cout
  Adder #(.width(16)) adder_14 (.a({4'b0000, in_1, 4'b0000}), .b(16'he), .out(adder_14_out));  // open: cin, cout
  Adder #(.width(16)) adder_15 (.a({4'b0000, in_1, 4'b0000}), .b(16'hf), .out(adder_15_out));  // open: cin, cout
  ROM #(.addrWidth(16), .Select("high")) rom_9 (.addr(adder_8_out), .data(out_11), .sel(in_2));
  ROM #(.addrWidth(16), .Select("high")) rom_10 (.addr(adder_9_out), .data(out_12), .sel(in_2));
  ROM #(.addrWidth(16), .Select("high")) rom_11 (.addr(adder_10_out), .data(out_13), .sel(in_2));
  ROM #(.addrWidth(16), .Select("high")) rom_12 (.addr(adder_11_out), .data(out_14), .sel(in_2));
  ROM #(.addrWidth(16), .Select("high")) rom_13 (.addr(adder_12_out), .data(out_15), .sel(in_2));
  ROM #(.addrWidth(16), .Select("high")) rom_14 (.addr(adder_13_out), .data(out_16), .sel(in_2));
  ROM #(.addrWidth(16), .Select("high")) rom_15 (.addr(adder_14_out), .data(out_17), .sel(in_2));
  ROM #(.addrWidth(16), .Select("high")) rom_16 (.addr(adder_15_out), .data(out_18), .sel(in_2));

  // Other names for the same wires on the sheet: Code[7:0] = in_1; row1[7:0] = out_3; row2[7:0] = out_4;
  //   row3[7:0] = out_5; row4[7:0] = out_6; row5[7:0] = out_7; row6[7:0] = out_8; row7[7:0] = out_9;
  //   row8[7:0] = out_10; row9[7:0] = out_11; row10[7:0] = out_12; row11[7:0] = out_13; row12[7:0] = out_14;
  //   row13[7:0] = out_15; row14[7:0] = out_16; row15[7:0] = out_17; row16[7:0] = out_18; Sel = in_2

  // Notes on the sheet:
  //   contents of rom_1 (hex, n*v repeats v):
  //   18*0 18 3c 3c 3c 18 18 18 0 18 18 5*0 63 63 63 22 14*0 36 36 7f 36 36 36 7f 36 36 4*0 c c 3e 63 61
  //   60 3e 3 3 43 63 3e c c 7*0 61 63 6 c 18 33 63 7*0 1c 36 36 1c 3b 6e 66 66 3b 5*0 30 30 30 60 13*0 c
  //   18 18 4*30 18 18 c 6*0 18 c c 4*6 c c 18 8*0 42 66 3c ff 3c 66 42 9*0 18 18 18 ff 18 18 18 15*0 18
  //   18 18 30 9*0 ff 18*0 18 18 6*0 1 3 7 e 1c 38 70 e0 c0 80 6*0 3e 63 63 63 6b 6b 63 63 63 3e 6*0 c 1c
  //   3c 6*c 3f 6*0 3e 63 3 6 c 18 30 61 63 7f 6*0 3e 63 3 3 1e 3 3 3 63 3e 6*0 6 e 1e 36 66 66 7f 6 6 f
  //   6*0 7f 60 60 60 7e 3 3 63 73 3e 6*0 1c 30 60 60 7e 4*63 3e 6*0 7f 63 3 6 6 c c 18 18 18 6*0 3e 63 63
  //   63 3e 4*63 3e 6*0 3e 4*63 3f 3 3 6 3c 9*0 18 18 0 0 0 18 18 9*0 18 18 0 0 0 18 18 18 30 5*0 6 c 18
  //   30 60 30 18 c 6 10*0 7e 0 0 7e 9*0 60 30 18 c 6 c 18 30 60 6*0 3e 63 63 6 c c c 0 c c 6*0 3e 63 63
  //   6f 6b 6b 6e 60 60 3e 6*0 8 1c 36 63 63 63 7f 63 63 63 6*0 7e 33 33 33 3e 4*33 7e 6*0 1e 33 61 4*60
  //   61 33 1e 6*0 7c 36 6*33 36 7c 6*0 7f 33 31 34 3c 34 30 31 33 7f 6*0 7f 33 31 34 3c 34 30 30 30 78
  //   6*0 1e 33 61 60 60 6f 63 63 37 1d 6*0 4*63 7f 5*63 6*0 3c 8*18 3c 6*0 f 6*6 66 66 3c 6*0 73 33 36 36
  //   3c 36 36 33 33 73 6*0 78 6*30 31 33 7f 6*0 63 77 7f 6b 6*63 6*0 63 63 73 7b 7f 6f 67 63 63 63 6*0 1c
  //   36 6*63 36 1c 6*0 7e 33 33 33 3e 4*30 78 6*0 3e 6*63 6b 6f 3e 6 7 4*0 7e 33 33 33 3e 36 36 33 33 73
  //   6*0 3e 63 63 30 1c 6 3 63 63 3e 6*0 ff db 99 6*18 3c 6*0 9*63 3e 6*0 7*63 36 1c 8 6*0 5*63 6b 6b 7f
  //   36 36 6*0 c3 c3 66 3c 18 18 3c 66 c3 c3 6*0 c3 c3 c3 66 3c 4*18 3c 6*0 7f 63 43 6 c 18 30 61 63 7f
  //   6*0 3c 8*30 3c 6*0 80 c0 e0 70 38 1c e 7 3 1 6*0 3c 8*c 3c 4*0 8 1c 36 63 24*0 ff 0 0 0 18 18 c 18*0
  //   3c 46 6 3e 66 66 3b 6*0 70 30 30 3c 36 4*33 6e 9*0 3e 63 60 60 60 63 3e 6*0 e 6 6 1e 36 4*66 3b 9*0
  //   3e 63 63 7e 60 63 3e 6*0 1c 36 32 30 7c 4*30 78 9*0 3b 4*66 3e 6 66 3c 4*0 70 30 30 36 3b 4*33 73
  //   6*0 c c 0 1c 5*c 1e 6*0 6 6 0 e 5*6 66 66 3c 4*0 70 30 30 33 33 36 3c 36 33 73 6*0 1c 8*c 1e 9*0 6e
  //   7f 5*6b 9*0 6e 6*33 9*0 3e 5*63 3e 9*0 6e 4*33 3e 30 30 78 7*0 3b 4*66 3e 6 6 f 7*0 6e 3b 33 30 30
  //   30 78 9*0 3e 63 38 e 3 63 3e 6*0 8 18 18 7e 4*18 1b e 9*0 6*66 3b 9*0 63 63 36 36 1c 1c 8 9*0 63 63
  //   63 6b 6b 7f 36 9*0 63 36 1c 1c 1c 36 63 9*0 5*63 3f 3 6 3c 7*0 7f 66 c 18 30 63 7f 6*0 e 18 18 18 70
  //   4*18 e 6*0 5*18 0 5*18 5*0 70 18 18 18 e 4*18 70 6*0 3b 6e 13*0 70 d8 d8 70
  //   contents of rom_2 (hex, n*v repeats v):
  //   18*0 18 3c 3c 3c 18 18 18 0 18 18 5*0 63 63 63 22 14*0 36 36 7f 36 36 36 7f 36 36 4*0 c c 3e 63 61
  //   60 3e 3 3 43 63 3e c c 7*0 61 63 6 c 18 33 63 7*0 1c 36 36 1c 3b 6e 66 66 3b 5*0 30 30 30 60 13*0 c
  //   18 18 4*30 18 18 c 6*0 18 c c 4*6 c c 18 8*0 42 66 3c ff 3c 66 42 9*0 18 18 18 ff 18 18 18 15*0 18
  //   18 18 30 9*0 ff 18*0 18 18 6*0 1 3 7 e 1c 38 70 e0 c0 80 6*0 3e 63 63 63 6b 6b 63 63 63 3e 6*0 c 1c
  //   3c 6*c 3f 6*0 3e 63 3 6 c 18 30 61 63 7f 6*0 3e 63 3 3 1e 3 3 3 63 3e 6*0 6 e 1e 36 66 66 7f 6 6 f
  //   6*0 7f 60 60 60 7e 3 3 63 73 3e 6*0 1c 30 60 60 7e 4*63 3e 6*0 7f 63 3 6 6 c c 18 18 18 6*0 3e 63 63
  //   63 3e 4*63 3e 6*0 3e 4*63 3f 3 3 6 3c 9*0 18 18 0 0 0 18 18 9*0 18 18 0 0 0 18 18 18 30 5*0 6 c 18
  //   30 60 30 18 c 6 10*0 7e 0 0 7e 9*0 60 30 18 c 6 c 18 30 60 6*0 3e 63 63 6 c c c 0 c c 6*0 3e 63 63
  //   6f 6b 6b 6e 60 60 3e 6*0 8 1c 36 63 63 63 7f 63 63 63 6*0 7e 33 33 33 3e 4*33 7e 6*0 1e 33 61 4*60
  //   61 33 1e 6*0 7c 36 6*33 36 7c 6*0 7f 33 31 34 3c 34 30 31 33 7f 6*0 7f 33 31 34 3c 34 30 30 30 78
  //   6*0 1e 33 61 60 60 6f 63 63 37 1d 6*0 4*63 7f 5*63 6*0 3c 8*18 3c 6*0 f 6*6 66 66 3c 6*0 73 33 36 36
  //   3c 36 36 33 33 73 6*0 78 6*30 31 33 7f 6*0 63 77 7f 6b 6*63 6*0 63 63 73 7b 7f 6f 67 63 63 63 6*0 1c
  //   36 6*63 36 1c 6*0 7e 33 33 33 3e 4*30 78 6*0 3e 6*63 6b 6f 3e 6 7 4*0 7e 33 33 33 3e 36 36 33 33 73
  //   6*0 3e 63 63 30 1c 6 3 63 63 3e 6*0 ff db 99 6*18 3c 6*0 9*63 3e 6*0 7*63 36 1c 8 6*0 5*63 6b 6b 7f
  //   36 36 6*0 c3 c3 66 3c 18 18 3c 66 c3 c3 6*0 c3 c3 c3 66 3c 4*18 3c 6*0 7f 63 43 6 c 18 30 61 63 7f
  //   6*0 3c 8*30 3c 6*0 80 c0 e0 70 38 1c e 7 3 1 6*0 3c 8*c 3c 4*0 8 1c 36 63 24*0 ff 0 0 0 18 18 c 18*0
  //   3c 46 6 3e 66 66 3b 6*0 70 30 30 3c 36 4*33 6e 9*0 3e 63 60 60 60 63 3e 6*0 e 6 6 1e 36 4*66 3b 9*0
  //   3e 63 63 7e 60 63 3e 6*0 1c 36 32 30 7c 4*30 78 9*0 3b 4*66 3e 6 66 3c 4*0 70 30 30 36 3b 4*33 73
  //   6*0 c c 0 1c 5*c 1e 6*0 6 6 0 e 5*6 66 66 3c 4*0 70 30 30 33 33 36 3c 36 33 73 6*0 1c 8*c 1e 9*0 6e
  //   7f 5*6b 9*0 6e 6*33 9*0 3e 5*63 3e 9*0 6e 4*33 3e 30 30 78 7*0 3b 4*66 3e 6 6 f 7*0 6e 3b 33 30 30
  //   30 78 9*0 3e 63 38 e 3 63 3e 6*0 8 18 18 7e 4*18 1b e 9*0 6*66 3b 9*0 63 63 36 36 1c 1c 8 9*0 63 63
  //   63 6b 6b 7f 36 9*0 63 36 1c 1c 1c 36 63 9*0 5*63 3f 3 6 3c 7*0 7f 66 c 18 30 63 7f 6*0 e 18 18 18 70
  //   4*18 e 6*0 5*18 0 5*18 5*0 70 18 18 18 e 4*18 70 6*0 3b 6e 13*0 70 d8 d8 70
  //   contents of rom_3 (hex, n*v repeats v):
  //   18*0 18 3c 3c 3c 18 18 18 0 18 18 5*0 63 63 63 22 14*0 36 36 7f 36 36 36 7f 36 36 4*0 c c 3e 63 61
  //   60 3e 3 3 43 63 3e c c 7*0 61 63 6 c 18 33 63 7*0 1c 36 36 1c 3b 6e 66 66 3b 5*0 30 30 30 60 13*0 c
  //   18 18 4*30 18 18 c 6*0 18 c c 4*6 c c 18 8*0 42 66 3c ff 3c 66 42 9*0 18 18 18 ff 18 18 18 15*0 18
  //   18 18 30 9*0 ff 18*0 18 18 6*0 1 3 7 e 1c 38 70 e0 c0 80 6*0 3e 63 63 63 6b 6b 63 63 63 3e 6*0 c 1c
  //   3c 6*c 3f 6*0 3e 63 3 6 c 18 30 61 63 7f 6*0 3e 63 3 3 1e 3 3 3 63 3e 6*0 6 e 1e 36 66 66 7f 6 6 f
  //   6*0 7f 60 60 60 7e 3 3 63 73 3e 6*0 1c 30 60 60 7e 4*63 3e 6*0 7f 63 3 6 6 c c 18 18 18 6*0 3e 63 63
  //   63 3e 4*63 3e 6*0 3e 4*63 3f 3 3 6 3c 9*0 18 18 0 0 0 18 18 9*0 18 18 0 0 0 18 18 18 30 5*0 6 c 18
  //   30 60 30 18 c 6 10*0 7e 0 0 7e 9*0 60 30 18 c 6 c 18 30 60 6*0 3e 63 63 6 c c c 0 c c 6*0 3e 63 63
  //   6f 6b 6b 6e 60 60 3e 6*0 8 1c 36 63 63 63 7f 63 63 63 6*0 7e 33 33 33 3e 4*33 7e 6*0 1e 33 61 4*60
  //   61 33 1e 6*0 7c 36 6*33 36 7c 6*0 7f 33 31 34 3c 34 30 31 33 7f 6*0 7f 33 31 34 3c 34 30 30 30 78
  //   6*0 1e 33 61 60 60 6f 63 63 37 1d 6*0 4*63 7f 5*63 6*0 3c 8*18 3c 6*0 f 6*6 66 66 3c 6*0 73 33 36 36
  //   3c 36 36 33 33 73 6*0 78 6*30 31 33 7f 6*0 63 77 7f 6b 6*63 6*0 63 63 73 7b 7f 6f 67 63 63 63 6*0 1c
  //   36 6*63 36 1c 6*0 7e 33 33 33 3e 4*30 78 6*0 3e 6*63 6b 6f 3e 6 7 4*0 7e 33 33 33 3e 36 36 33 33 73
  //   6*0 3e 63 63 30 1c 6 3 63 63 3e 6*0 ff db 99 6*18 3c 6*0 9*63 3e 6*0 7*63 36 1c 8 6*0 5*63 6b 6b 7f
  //   36 36 6*0 c3 c3 66 3c 18 18 3c 66 c3 c3 6*0 c3 c3 c3 66 3c 4*18 3c 6*0 7f 63 43 6 c 18 30 61 63 7f
  //   6*0 3c 8*30 3c 6*0 80 c0 e0 70 38 1c e 7 3 1 6*0 3c 8*c 3c 4*0 8 1c 36 63 24*0 ff 0 0 0 18 18 c 18*0
  //   3c 46 6 3e 66 66 3b 6*0 70 30 30 3c 36 4*33 6e 9*0 3e 63 60 60 60 63 3e 6*0 e 6 6 1e 36 4*66 3b 9*0
  //   3e 63 63 7e 60 63 3e 6*0 1c 36 32 30 7c 4*30 78 9*0 3b 4*66 3e 6 66 3c 4*0 70 30 30 36 3b 4*33 73
  //   6*0 c c 0 1c 5*c 1e 6*0 6 6 0 e 5*6 66 66 3c 4*0 70 30 30 33 33 36 3c 36 33 73 6*0 1c 8*c 1e 9*0 6e
  //   7f 5*6b 9*0 6e 6*33 9*0 3e 5*63 3e 9*0 6e 4*33 3e 30 30 78 7*0 3b 4*66 3e 6 6 f 7*0 6e 3b 33 30 30
  //   30 78 9*0 3e 63 38 e 3 63 3e 6*0 8 18 18 7e 4*18 1b e 9*0 6*66 3b 9*0 63 63 36 36 1c 1c 8 9*0 63 63
  //   63 6b 6b 7f 36 9*0 63 36 1c 1c 1c 36 63 9*0 5*63 3f 3 6 3c 7*0 7f 66 c 18 30 63 7f 6*0 e 18 18 18 70
  //   4*18 e 6*0 5*18 0 5*18 5*0 70 18 18 18 e 4*18 70 6*0 3b 6e 13*0 70 d8 d8 70
  //   contents of rom_4 (hex, n*v repeats v):
  //   18*0 18 3c 3c 3c 18 18 18 0 18 18 5*0 63 63 63 22 14*0 36 36 7f 36 36 36 7f 36 36 4*0 c c 3e 63 61
  //   60 3e 3 3 43 63 3e c c 7*0 61 63 6 c 18 33 63 7*0 1c 36 36 1c 3b 6e 66 66 3b 5*0 30 30 30 60 13*0 c
  //   18 18 4*30 18 18 c 6*0 18 c c 4*6 c c 18 8*0 42 66 3c ff 3c 66 42 9*0 18 18 18 ff 18 18 18 15*0 18
  //   18 18 30 9*0 ff 18*0 18 18 6*0 1 3 7 e 1c 38 70 e0 c0 80 6*0 3e 63 63 63 6b 6b 63 63 63 3e 6*0 c 1c
  //   3c 6*c 3f 6*0 3e 63 3 6 c 18 30 61 63 7f 6*0 3e 63 3 3 1e 3 3 3 63 3e 6*0 6 e 1e 36 66 66 7f 6 6 f
  //   6*0 7f 60 60 60 7e 3 3 63 73 3e 6*0 1c 30 60 60 7e 4*63 3e 6*0 7f 63 3 6 6 c c 18 18 18 6*0 3e 63 63
  //   63 3e 4*63 3e 6*0 3e 4*63 3f 3 3 6 3c 9*0 18 18 0 0 0 18 18 9*0 18 18 0 0 0 18 18 18 30 5*0 6 c 18
  //   30 60 30 18 c 6 10*0 7e 0 0 7e 9*0 60 30 18 c 6 c 18 30 60 6*0 3e 63 63 6 c c c 0 c c 6*0 3e 63 63
  //   6f 6b 6b 6e 60 60 3e 6*0 8 1c 36 63 63 63 7f 63 63 63 6*0 7e 33 33 33 3e 4*33 7e 6*0 1e 33 61 4*60
  //   61 33 1e 6*0 7c 36 6*33 36 7c 6*0 7f 33 31 34 3c 34 30 31 33 7f 6*0 7f 33 31 34 3c 34 30 30 30 78
  //   6*0 1e 33 61 60 60 6f 63 63 37 1d 6*0 4*63 7f 5*63 6*0 3c 8*18 3c 6*0 f 6*6 66 66 3c 6*0 73 33 36 36
  //   3c 36 36 33 33 73 6*0 78 6*30 31 33 7f 6*0 63 77 7f 6b 6*63 6*0 63 63 73 7b 7f 6f 67 63 63 63 6*0 1c
  //   36 6*63 36 1c 6*0 7e 33 33 33 3e 4*30 78 6*0 3e 6*63 6b 6f 3e 6 7 4*0 7e 33 33 33 3e 36 36 33 33 73
  //   6*0 3e 63 63 30 1c 6 3 63 63 3e 6*0 ff db 99 6*18 3c 6*0 9*63 3e 6*0 7*63 36 1c 8 6*0 5*63 6b 6b 7f
  //   36 36 6*0 c3 c3 66 3c 18 18 3c 66 c3 c3 6*0 c3 c3 c3 66 3c 4*18 3c 6*0 7f 63 43 6 c 18 30 61 63 7f
  //   6*0 3c 8*30 3c 6*0 80 c0 e0 70 38 1c e 7 3 1 6*0 3c 8*c 3c 4*0 8 1c 36 63 24*0 ff 0 0 0 18 18 c 18*0
  //   3c 46 6 3e 66 66 3b 6*0 70 30 30 3c 36 4*33 6e 9*0 3e 63 60 60 60 63 3e 6*0 e 6 6 1e 36 4*66 3b 9*0
  //   3e 63 63 7e 60 63 3e 6*0 1c 36 32 30 7c 4*30 78 9*0 3b 4*66 3e 6 66 3c 4*0 70 30 30 36 3b 4*33 73
  //   6*0 c c 0 1c 5*c 1e 6*0 6 6 0 e 5*6 66 66 3c 4*0 70 30 30 33 33 36 3c 36 33 73 6*0 1c 8*c 1e 9*0 6e
  //   7f 5*6b 9*0 6e 6*33 9*0 3e 5*63 3e 9*0 6e 4*33 3e 30 30 78 7*0 3b 4*66 3e 6 6 f 7*0 6e 3b 33 30 30
  //   30 78 9*0 3e 63 38 e 3 63 3e 6*0 8 18 18 7e 4*18 1b e 9*0 6*66 3b 9*0 63 63 36 36 1c 1c 8 9*0 63 63
  //   63 6b 6b 7f 36 9*0 63 36 1c 1c 1c 36 63 9*0 5*63 3f 3 6 3c 7*0 7f 66 c 18 30 63 7f 6*0 e 18 18 18 70
  //   4*18 e 6*0 5*18 0 5*18 5*0 70 18 18 18 e 4*18 70 6*0 3b 6e 13*0 70 d8 d8 70
  //   contents of rom_5 (hex, n*v repeats v):
  //   18*0 18 3c 3c 3c 18 18 18 0 18 18 5*0 63 63 63 22 14*0 36 36 7f 36 36 36 7f 36 36 4*0 c c 3e 63 61
  //   60 3e 3 3 43 63 3e c c 7*0 61 63 6 c 18 33 63 7*0 1c 36 36 1c 3b 6e 66 66 3b 5*0 30 30 30 60 13*0 c
  //   18 18 4*30 18 18 c 6*0 18 c c 4*6 c c 18 8*0 42 66 3c ff 3c 66 42 9*0 18 18 18 ff 18 18 18 15*0 18
  //   18 18 30 9*0 ff 18*0 18 18 6*0 1 3 7 e 1c 38 70 e0 c0 80 6*0 3e 63 63 63 6b 6b 63 63 63 3e 6*0 c 1c
  //   3c 6*c 3f 6*0 3e 63 3 6 c 18 30 61 63 7f 6*0 3e 63 3 3 1e 3 3 3 63 3e 6*0 6 e 1e 36 66 66 7f 6 6 f
  //   6*0 7f 60 60 60 7e 3 3 63 73 3e 6*0 1c 30 60 60 7e 4*63 3e 6*0 7f 63 3 6 6 c c 18 18 18 6*0 3e 63 63
  //   63 3e 4*63 3e 6*0 3e 4*63 3f 3 3 6 3c 9*0 18 18 0 0 0 18 18 9*0 18 18 0 0 0 18 18 18 30 5*0 6 c 18
  //   30 60 30 18 c 6 10*0 7e 0 0 7e 9*0 60 30 18 c 6 c 18 30 60 6*0 3e 63 63 6 c c c 0 c c 6*0 3e 63 63
  //   6f 6b 6b 6e 60 60 3e 6*0 8 1c 36 63 63 63 7f 63 63 63 6*0 7e 33 33 33 3e 4*33 7e 6*0 1e 33 61 4*60
  //   61 33 1e 6*0 7c 36 6*33 36 7c 6*0 7f 33 31 34 3c 34 30 31 33 7f 6*0 7f 33 31 34 3c 34 30 30 30 78
  //   6*0 1e 33 61 60 60 6f 63 63 37 1d 6*0 4*63 7f 5*63 6*0 3c 8*18 3c 6*0 f 6*6 66 66 3c 6*0 73 33 36 36
  //   3c 36 36 33 33 73 6*0 78 6*30 31 33 7f 6*0 63 77 7f 6b 6*63 6*0 63 63 73 7b 7f 6f 67 63 63 63 6*0 1c
  //   36 6*63 36 1c 6*0 7e 33 33 33 3e 4*30 78 6*0 3e 6*63 6b 6f 3e 6 7 4*0 7e 33 33 33 3e 36 36 33 33 73
  //   6*0 3e 63 63 30 1c 6 3 63 63 3e 6*0 ff db 99 6*18 3c 6*0 9*63 3e 6*0 7*63 36 1c 8 6*0 5*63 6b 6b 7f
  //   36 36 6*0 c3 c3 66 3c 18 18 3c 66 c3 c3 6*0 c3 c3 c3 66 3c 4*18 3c 6*0 7f 63 43 6 c 18 30 61 63 7f
  //   6*0 3c 8*30 3c 6*0 80 c0 e0 70 38 1c e 7 3 1 6*0 3c 8*c 3c 4*0 8 1c 36 63 24*0 ff 0 0 0 18 18 c 18*0
  //   3c 46 6 3e 66 66 3b 6*0 70 30 30 3c 36 4*33 6e 9*0 3e 63 60 60 60 63 3e 6*0 e 6 6 1e 36 4*66 3b 9*0
  //   3e 63 63 7e 60 63 3e 6*0 1c 36 32 30 7c 4*30 78 9*0 3b 4*66 3e 6 66 3c 4*0 70 30 30 36 3b 4*33 73
  //   6*0 c c 0 1c 5*c 1e 6*0 6 6 0 e 5*6 66 66 3c 4*0 70 30 30 33 33 36 3c 36 33 73 6*0 1c 8*c 1e 9*0 6e
  //   7f 5*6b 9*0 6e 6*33 9*0 3e 5*63 3e 9*0 6e 4*33 3e 30 30 78 7*0 3b 4*66 3e 6 6 f 7*0 6e 3b 33 30 30
  //   30 78 9*0 3e 63 38 e 3 63 3e 6*0 8 18 18 7e 4*18 1b e 9*0 6*66 3b 9*0 63 63 36 36 1c 1c 8 9*0 63 63
  //   63 6b 6b 7f 36 9*0 63 36 1c 1c 1c 36 63 9*0 5*63 3f 3 6 3c 7*0 7f 66 c 18 30 63 7f 6*0 e 18 18 18 70
  //   4*18 e 6*0 5*18 0 5*18 5*0 70 18 18 18 e 4*18 70 6*0 3b 6e 13*0 70 d8 d8 70
  //   contents of rom_6 (hex, n*v repeats v):
  //   18*0 18 3c 3c 3c 18 18 18 0 18 18 5*0 63 63 63 22 14*0 36 36 7f 36 36 36 7f 36 36 4*0 c c 3e 63 61
  //   60 3e 3 3 43 63 3e c c 7*0 61 63 6 c 18 33 63 7*0 1c 36 36 1c 3b 6e 66 66 3b 5*0 30 30 30 60 13*0 c
  //   18 18 4*30 18 18 c 6*0 18 c c 4*6 c c 18 8*0 42 66 3c ff 3c 66 42 9*0 18 18 18 ff 18 18 18 15*0 18
  //   18 18 30 9*0 ff 18*0 18 18 6*0 1 3 7 e 1c 38 70 e0 c0 80 6*0 3e 63 63 63 6b 6b 63 63 63 3e 6*0 c 1c
  //   3c 6*c 3f 6*0 3e 63 3 6 c 18 30 61 63 7f 6*0 3e 63 3 3 1e 3 3 3 63 3e 6*0 6 e 1e 36 66 66 7f 6 6 f
  //   6*0 7f 60 60 60 7e 3 3 63 73 3e 6*0 1c 30 60 60 7e 4*63 3e 6*0 7f 63 3 6 6 c c 18 18 18 6*0 3e 63 63
  //   63 3e 4*63 3e 6*0 3e 4*63 3f 3 3 6 3c 9*0 18 18 0 0 0 18 18 9*0 18 18 0 0 0 18 18 18 30 5*0 6 c 18
  //   30 60 30 18 c 6 10*0 7e 0 0 7e 9*0 60 30 18 c 6 c 18 30 60 6*0 3e 63 63 6 c c c 0 c c 6*0 3e 63 63
  //   6f 6b 6b 6e 60 60 3e 6*0 8 1c 36 63 63 63 7f 63 63 63 6*0 7e 33 33 33 3e 4*33 7e 6*0 1e 33 61 4*60
  //   61 33 1e 6*0 7c 36 6*33 36 7c 6*0 7f 33 31 34 3c 34 30 31 33 7f 6*0 7f 33 31 34 3c 34 30 30 30 78
  //   6*0 1e 33 61 60 60 6f 63 63 37 1d 6*0 4*63 7f 5*63 6*0 3c 8*18 3c 6*0 f 6*6 66 66 3c 6*0 73 33 36 36
  //   3c 36 36 33 33 73 6*0 78 6*30 31 33 7f 6*0 63 77 7f 6b 6*63 6*0 63 63 73 7b 7f 6f 67 63 63 63 6*0 1c
  //   36 6*63 36 1c 6*0 7e 33 33 33 3e 4*30 78 6*0 3e 6*63 6b 6f 3e 6 7 4*0 7e 33 33 33 3e 36 36 33 33 73
  //   6*0 3e 63 63 30 1c 6 3 63 63 3e 6*0 ff db 99 6*18 3c 6*0 9*63 3e 6*0 7*63 36 1c 8 6*0 5*63 6b 6b 7f
  //   36 36 6*0 c3 c3 66 3c 18 18 3c 66 c3 c3 6*0 c3 c3 c3 66 3c 4*18 3c 6*0 7f 63 43 6 c 18 30 61 63 7f
  //   6*0 3c 8*30 3c 6*0 80 c0 e0 70 38 1c e 7 3 1 6*0 3c 8*c 3c 4*0 8 1c 36 63 24*0 ff 0 0 0 18 18 c 18*0
  //   3c 46 6 3e 66 66 3b 6*0 70 30 30 3c 36 4*33 6e 9*0 3e 63 60 60 60 63 3e 6*0 e 6 6 1e 36 4*66 3b 9*0
  //   3e 63 63 7e 60 63 3e 6*0 1c 36 32 30 7c 4*30 78 9*0 3b 4*66 3e 6 66 3c 4*0 70 30 30 36 3b 4*33 73
  //   6*0 c c 0 1c 5*c 1e 6*0 6 6 0 e 5*6 66 66 3c 4*0 70 30 30 33 33 36 3c 36 33 73 6*0 1c 8*c 1e 9*0 6e
  //   7f 5*6b 9*0 6e 6*33 9*0 3e 5*63 3e 9*0 6e 4*33 3e 30 30 78 7*0 3b 4*66 3e 6 6 f 7*0 6e 3b 33 30 30
  //   30 78 9*0 3e 63 38 e 3 63 3e 6*0 8 18 18 7e 4*18 1b e 9*0 6*66 3b 9*0 63 63 36 36 1c 1c 8 9*0 63 63
  //   63 6b 6b 7f 36 9*0 63 36 1c 1c 1c 36 63 9*0 5*63 3f 3 6 3c 7*0 7f 66 c 18 30 63 7f 6*0 e 18 18 18 70
  //   4*18 e 6*0 5*18 0 5*18 5*0 70 18 18 18 e 4*18 70 6*0 3b 6e 13*0 70 d8 d8 70
  //   contents of rom_7 (hex, n*v repeats v):
  //   18*0 18 3c 3c 3c 18 18 18 0 18 18 5*0 63 63 63 22 14*0 36 36 7f 36 36 36 7f 36 36 4*0 c c 3e 63 61
  //   60 3e 3 3 43 63 3e c c 7*0 61 63 6 c 18 33 63 7*0 1c 36 36 1c 3b 6e 66 66 3b 5*0 30 30 30 60 13*0 c
  //   18 18 4*30 18 18 c 6*0 18 c c 4*6 c c 18 8*0 42 66 3c ff 3c 66 42 9*0 18 18 18 ff 18 18 18 15*0 18
  //   18 18 30 9*0 ff 18*0 18 18 6*0 1 3 7 e 1c 38 70 e0 c0 80 6*0 3e 63 63 63 6b 6b 63 63 63 3e 6*0 c 1c
  //   3c 6*c 3f 6*0 3e 63 3 6 c 18 30 61 63 7f 6*0 3e 63 3 3 1e 3 3 3 63 3e 6*0 6 e 1e 36 66 66 7f 6 6 f
  //   6*0 7f 60 60 60 7e 3 3 63 73 3e 6*0 1c 30 60 60 7e 4*63 3e 6*0 7f 63 3 6 6 c c 18 18 18 6*0 3e 63 63
  //   63 3e 4*63 3e 6*0 3e 4*63 3f 3 3 6 3c 9*0 18 18 0 0 0 18 18 9*0 18 18 0 0 0 18 18 18 30 5*0 6 c 18
  //   30 60 30 18 c 6 10*0 7e 0 0 7e 9*0 60 30 18 c 6 c 18 30 60 6*0 3e 63 63 6 c c c 0 c c 6*0 3e 63 63
  //   6f 6b 6b 6e 60 60 3e 6*0 8 1c 36 63 63 63 7f 63 63 63 6*0 7e 33 33 33 3e 4*33 7e 6*0 1e 33 61 4*60
  //   61 33 1e 6*0 7c 36 6*33 36 7c 6*0 7f 33 31 34 3c 34 30 31 33 7f 6*0 7f 33 31 34 3c 34 30 30 30 78
  //   6*0 1e 33 61 60 60 6f 63 63 37 1d 6*0 4*63 7f 5*63 6*0 3c 8*18 3c 6*0 f 6*6 66 66 3c 6*0 73 33 36 36
  //   3c 36 36 33 33 73 6*0 78 6*30 31 33 7f 6*0 63 77 7f 6b 6*63 6*0 63 63 73 7b 7f 6f 67 63 63 63 6*0 1c
  //   36 6*63 36 1c 6*0 7e 33 33 33 3e 4*30 78 6*0 3e 6*63 6b 6f 3e 6 7 4*0 7e 33 33 33 3e 36 36 33 33 73
  //   6*0 3e 63 63 30 1c 6 3 63 63 3e 6*0 ff db 99 6*18 3c 6*0 9*63 3e 6*0 7*63 36 1c 8 6*0 5*63 6b 6b 7f
  //   36 36 6*0 c3 c3 66 3c 18 18 3c 66 c3 c3 6*0 c3 c3 c3 66 3c 4*18 3c 6*0 7f 63 43 6 c 18 30 61 63 7f
  //   6*0 3c 8*30 3c 6*0 80 c0 e0 70 38 1c e 7 3 1 6*0 3c 8*c 3c 4*0 8 1c 36 63 24*0 ff 0 0 0 18 18 c 18*0
  //   3c 46 6 3e 66 66 3b 6*0 70 30 30 3c 36 4*33 6e 9*0 3e 63 60 60 60 63 3e 6*0 e 6 6 1e 36 4*66 3b 9*0
  //   3e 63 63 7e 60 63 3e 6*0 1c 36 32 30 7c 4*30 78 9*0 3b 4*66 3e 6 66 3c 4*0 70 30 30 36 3b 4*33 73
  //   6*0 c c 0 1c 5*c 1e 6*0 6 6 0 e 5*6 66 66 3c 4*0 70 30 30 33 33 36 3c 36 33 73 6*0 1c 8*c 1e 9*0 6e
  //   7f 5*6b 9*0 6e 6*33 9*0 3e 5*63 3e 9*0 6e 4*33 3e 30 30 78 7*0 3b 4*66 3e 6 6 f 7*0 6e 3b 33 30 30
  //   30 78 9*0 3e 63 38 e 3 63 3e 6*0 8 18 18 7e 4*18 1b e 9*0 6*66 3b 9*0 63 63 36 36 1c 1c 8 9*0 63 63
  //   63 6b 6b 7f 36 9*0 63 36 1c 1c 1c 36 63 9*0 5*63 3f 3 6 3c 7*0 7f 66 c 18 30 63 7f 6*0 e 18 18 18 70
  //   4*18 e 6*0 5*18 0 5*18 5*0 70 18 18 18 e 4*18 70 6*0 3b 6e 13*0 70 d8 d8 70
  //   contents of rom_8 (hex, n*v repeats v):
  //   18*0 18 3c 3c 3c 18 18 18 0 18 18 5*0 63 63 63 22 14*0 36 36 7f 36 36 36 7f 36 36 4*0 c c 3e 63 61
  //   60 3e 3 3 43 63 3e c c 7*0 61 63 6 c 18 33 63 7*0 1c 36 36 1c 3b 6e 66 66 3b 5*0 30 30 30 60 13*0 c
  //   18 18 4*30 18 18 c 6*0 18 c c 4*6 c c 18 8*0 42 66 3c ff 3c 66 42 9*0 18 18 18 ff 18 18 18 15*0 18
  //   18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
  //   contents of rom_9 (hex, n*v repeats v):
  //   18*0 18 3c 3c 3c 18 18 18 0 18 18 5*0 63 63 63 22 14*0 36 36 7f 36 36 36 7f 36 36 4*0 c c 3e 63 61
  //   60 3e 3 3 43 63 3e c c 7*0 61 63 6 c 18 33 63 7*0 1c 36 36 1c 3b 6e 66 66 3b 5*0 30 30 30 60 13*0 c
  //   18 18 4*30 18 18 c 6*0 18 c c 4*6 c c 18 8*0 42 66 3c ff 3c 66 42 9*0 18 18 18 ff 18 18 18 15*0 18
  //   18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
  //   contents of rom_10 (hex, n*v repeats v):
  //   18*0 18 3c 3c 3c 18 18 18 0 18 18 5*0 63 63 63 22 14*0 36 36 7f 36 36 36 7f 36 36 4*0 c c 3e 63 61
  //   60 3e 3 3 43 63 3e c c 7*0 61 63 6 c 18 33 63 7*0 1c 36 36 1c 3b 6e 66 66 3b 5*0 30 30 30 60 13*0 c
  //   18 18 4*30 18 18 c 6*0 18 c c 4*6 c c 18 8*0 42 66 3c ff 3c 66 42 9*0 18 18 18 ff 18 18 18 15*0 18
  //   18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
  //   contents of rom_11 (hex, n*v repeats v):
  //   18*0 18 3c 3c 3c 18 18 18 0 18 18 5*0 63 63 63 22 14*0 36 36 7f 36 36 36 7f 36 36 4*0 c c 3e 63 61
  //   60 3e 3 3 43 63 3e c c 7*0 61 63 6 c 18 33 63 7*0 1c 36 36 1c 3b 6e 66 66 3b 5*0 30 30 30 60 13*0 c
  //   18 18 4*30 18 18 c 6*0 18 c c 4*6 c c 18 8*0 42 66 3c ff 3c 66 42 9*0 18 18 18 ff 18 18 18 15*0 18
  //   18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
  //   contents of rom_12 (hex, n*v repeats v):
  //   18*0 18 3c 3c 3c 18 18 18 0 18 18 5*0 63 63 63 22 14*0 36 36 7f 36 36 36 7f 36 36 4*0 c c 3e 63 61
  //   60 3e 3 3 43 63 3e c c 7*0 61 63 6 c 18 33 63 7*0 1c 36 36 1c 3b 6e 66 66 3b 5*0 30 30 30 60 13*0 c
  //   18 18 4*30 18 18 c 6*0 18 c c 4*6 c c 18 8*0 42 66 3c ff 3c 66 42 9*0 18 18 18 ff 18 18 18 15*0 18
  //   18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
  //   contents of rom_13 (hex, n*v repeats v):
  //   18*0 18 3c 3c 3c 18 18 18 0 18 18 5*0 63 63 63 22 14*0 36 36 7f 36 36 36 7f 36 36 4*0 c c 3e 63 61
  //   60 3e 3 3 43 63 3e c c 7*0 61 63 6 c 18 33 63 7*0 1c 36 36 1c 3b 6e 66 66 3b 5*0 30 30 30 60 13*0 c
  //   18 18 4*30 18 18 c 6*0 18 c c 4*6 c c 18 8*0 42 66 3c ff 3c 66 42 9*0 18 18 18 ff 18 18 18 15*0 18
  //   18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
  //   contents of rom_14 (hex, n*v repeats v):
  //   18*0 18 3c 3c 3c 18 18 18 0 18 18 5*0 63 63 63 22 14*0 36 36 7f 36 36 36 7f 36 36 4*0 c c 3e 63 61
  //   60 3e 3 3 43 63 3e c c 7*0 61 63 6 c 18 33 63 7*0 1c 36 36 1c 3b 6e 66 66 3b 5*0 30 30 30 60 13*0 c
  //   18 18 4*30 18 18 c 6*0 18 c c 4*6 c c 18 8*0 42 66 3c ff 3c 66 42 9*0 18 18 18 ff 18 18 18 15*0 18
  //   18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
  //   contents of rom_15 (hex, n*v repeats v):
  //   18*0 18 3c 3c 3c 18 18 18 0 18 18 5*0 63 63 63 22 14*0 36 36 7f 36 36 36 7f 36 36 4*0 c c 3e 63 61
  //   60 3e 3 3 43 63 3e c c 7*0 61 63 6 c 18 33 63 7*0 1c 36 36 1c 3b 6e 66 66 3b 5*0 30 30 30 60 13*0 c
  //   18 18 4*30 18 18 c 6*0 18 c c 4*6 c c 18 8*0 42 66 3c ff 3c 66 42 9*0 18 18 18 ff 18 18 18 15*0 18
  //   18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
  //   contents of rom_16 (hex, n*v repeats v):
  //   18*0 18 3c 3c 3c 18 18 18 0 18 18 5*0 63 63 63 22 14*0 36 36 7f 36 36 36 7f 36 36 4*0 c c 3e 63 61
  //   60 3e 3 3 43 63 3e c c 7*0 61 63 6 c 18 33 63 7*0 1c 36 36 1c 3b 6e 66 66 3b 5*0 30 30 30 60 13*0 c
  //   18 18 4*30 18 18 c 6*0 18 c c 4*6 c c 18 8*0 42 66 3c ff 3c 66 42 9*0 18 18 18 ff 18 18 18 15*0 18
  //   18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
endmodule

module \IFU实验  (
  input  [31:0] in_1,
  input  [31:0] in_2,
  input  [31:0] in_3,
  input  in_4,
  input  in_5,
  input  in_6,
  input  in_7,
  input  in_8,
  output [31:0] out_9,
  output [31:0] out_10
);

  wire not_1_out;
  wire [31:0] adder_1_out, multiplexer_1_out, multiplexer_2_out, multiplexer_3_out;

  Multiplexer #(.width(32), .enable("false")) multiplexer_1 (
    .in0(adder_1_out), .in1(in_1), .out(multiplexer_1_out), .sel(in_5));
  not not_1 (not_1_out, in_6);
  Register #(.width(32), .Select("low")) PC (
    .D(multiplexer_1_out), .en(not_1_out), .Q(out_9), .clk(in_4));  // open: clr
  // Probe on out_9
  Multiplexer #(.width(32), .enable("false")) multiplexer_2 (
    .in0(out_9), .in1(in_3), .out(multiplexer_2_out), .sel(in_7));
  Multiplexer #(.width(32), .enable("false")) multiplexer_3 (
    .in0(32'h4), .in1(in_2), .out(multiplexer_3_out), .sel(in_8));
  Adder #(.width(32)) adder_1 (
    .a(multiplexer_2_out), .b(multiplexer_3_out), .out(adder_1_out), .cin(1'b0));  // open: cout
  // Probe on out_10
  ROM #(.addrWidth(16), .dataWidth(32), .Select("high")) \u_指令存储器_ROM  (.addr(out_9[17:2]), .data(out_10));

  // Other names for the same wires on the sheet: BusA[31:0] = in_3; CLK = in_4; Halt = in_6; Imm[31:0] = in_2;
  //   InitAddr[31:0] = in_1; IR[31:0] = out_10; NxtASrc = in_7; NxtBSrc = in_8; PC[31:0] = out_9; RESET = in_5

  // Notes on the sheet:
  //   contents of 指令存储器_ROM (hex, n*v repeats v):
  //   12312312 11111111 22222222 33333333
endmodule

module \立即数扩展器  (
  input  [31:0] in_1,
  input  [2:0] in_2,
  output [31:0] out_3
);

  wire [11:0] bit_extender_4_out;
  wire [19:0] bit_extender_3_out;
  wire [26:0] bit_extender_2_out;
  wire [31:0] bit_extender_1_out;

  assign bit_extender_1_out = {{20{in_1[31]}}, in_1[31:20]};  // Bit_Extender bit_extender_1
  assign bit_extender_2_out = {{20{in_1[31]}}, in_1[31:25]};  // Bit_Extender bit_extender_2
  assign bit_extender_3_out = {{19{in_1[31]}}, in_1[31]};  // Bit_Extender bit_extender_3
  assign bit_extender_4_out = {{11{in_1[31]}}, in_1[31]};  // Bit_Extender bit_extender_4
  Multiplexer #(.select(3), .width(32), .enable("false")) multiplexer_1 (
    .in0(bit_extender_1_out), .in1({in_1[31:12], {12{1'b0}}}), .in2({bit_extender_2_out, in_1[11:7]}),
    .in3({bit_extender_3_out, in_1[7], in_1[30:25], in_1[11:8], 1'b0}),
    .in4({bit_extender_4_out, in_1[19:12], in_1[20], in_1[30:21], 1'b0}), .out(out_3), .sel(in_2));  // open: in5, in6, in7

  // Other names for the same wires on the sheet: InStr[31:0] = in_1; ExtOp[2:0] = in_2; Imm[31:0] = out_3
endmodule

module Branch (
  input  [2:0] in_1,
  input  in_2,
  input  in_3,
  output out_4,
  output out_5
);

  wire not_1_out, not_2_out, or_1_out;

  not not_1 (not_1_out, in_2);
  or or_1 (or_1_out, in_2, not_2_out);
  not not_2 (not_2_out, in_3);
  and and_1 (out_4, ~in_1[0], in_1[1], ~in_1[2]);  // AND_Gate
  Multiplexer #(.select(3), .enable("false")) multiplexer_1 (
    .in0(1'b0), .in1(1'b1), .in2(1'b1), .in4(in_2), .in5(not_1_out), .in6(in_3), .in7(or_1_out), .out(out_5),
    .sel(in_1));  // open: in3

  // Other names for the same wires on the sheet: Branch[2:0] = in_1; NxtASrc = out_4; NxtBSrc = out_5; Result0 = in_3;
  //   Zero = in_2
endmodule

module \寄存器堆  (
  input  in_1,
  input  [4:0] in_2,
  input  [31:0] in_3,
  input  [4:0] in_4,
  input  [4:0] in_5,
  input  in_6,
  output [31:0] out_7,
  output [31:0] out_8
);

  wire and_1_out, and_2_out, and_3_out, and_4_out, and_5_out, and_6_out, and_7_out, and_8_out, and_9_out,
       and_10_out, and_11_out, and_12_out, and_13_out, and_14_out, and_15_out, and_16_out, and_17_out,
       and_18_out, and_19_out, and_20_out, and_21_out, and_22_out, and_23_out, and_24_out, and_25_out,
       and_26_out, and_27_out, and_28_out, and_29_out, and_30_out, and_31_out, and_32_out, decoder_1_out0,
       decoder_1_out1, decoder_1_out2, decoder_1_out3, decoder_1_out4, decoder_1_out5, decoder_1_out6,
       decoder_1_out7, decoder_1_out8, decoder_1_out9, decoder_1_out10, decoder_1_out11, decoder_1_out12,
       decoder_1_out13, decoder_1_out14, decoder_1_out15, decoder_1_out16, decoder_1_out17, decoder_1_out18,
       decoder_1_out19, decoder_1_out20, decoder_1_out21, decoder_1_out22, decoder_1_out23, decoder_1_out24,
       decoder_1_out25, decoder_1_out26, decoder_1_out27, decoder_1_out28, decoder_1_out29, decoder_1_out30,
       decoder_1_out31;
  wire [31:0] register_1_q, register_2_q, register_3_q, register_4_q, register_5_q, register_6_q,
       register_7_q, register_8_q, register_9_q, register_10_q, register_11_q, register_12_q, register_13_q,
       register_14_q, register_15_q, register_16_q, register_17_q, register_18_q, register_19_q,
       register_20_q, register_21_q, register_22_q, register_23_q, register_24_q, register_25_q,
       register_26_q, register_27_q, register_28_q, register_29_q, register_30_q, register_31_q,
       register_32_q;

  Decoder #(.select(5), .enable("false")) decoder_1 (
    .out0(decoder_1_out0), .out1(decoder_1_out1), .out2(decoder_1_out2), .out3(decoder_1_out3),
    .out4(decoder_1_out4), .out5(decoder_1_out5), .out6(decoder_1_out6), .out7(decoder_1_out7),
    .out8(decoder_1_out8), .out9(decoder_1_out9), .out10(decoder_1_out10), .out11(decoder_1_out11),
    .out12(decoder_1_out12), .out13(decoder_1_out13), .out14(decoder_1_out14), .out15(decoder_1_out15),
    .out16(decoder_1_out16), .out17(decoder_1_out17), .out18(decoder_1_out18), .out19(decoder_1_out19),
    .out20(decoder_1_out20), .out21(decoder_1_out21), .out22(decoder_1_out22), .out23(decoder_1_out23),
    .out24(decoder_1_out24), .out25(decoder_1_out25), .out26(decoder_1_out26), .out27(decoder_1_out27),
    .out28(decoder_1_out28), .out29(decoder_1_out29), .out30(decoder_1_out30), .out31(decoder_1_out31),
    .sel(in_5));
  and and_1 (and_1_out, decoder_1_out0, 1'b1, in_1);
  and and_2 (and_2_out, decoder_1_out1, 1'b1, in_1);
  and and_3 (and_3_out, decoder_1_out2, 1'b1, in_1);
  and and_4 (and_4_out, decoder_1_out3, 1'b1, in_1);
  and and_5 (and_5_out, decoder_1_out4, 1'b1, in_1);
  and and_6 (and_6_out, decoder_1_out5, 1'b1, in_1);
  and and_7 (and_7_out, decoder_1_out6, 1'b1, in_1);
  and and_8 (and_8_out, decoder_1_out7, 1'b1, in_1);
  and and_9 (and_9_out, decoder_1_out8, 1'b1, in_1);
  and and_10 (and_10_out, decoder_1_out9, 1'b1, in_1);
  and and_11 (and_11_out, decoder_1_out10, 1'b1, in_1);
  and and_12 (and_12_out, decoder_1_out11, 1'b1, in_1);
  and and_13 (and_13_out, decoder_1_out12, 1'b1, in_1);
  and and_14 (and_14_out, decoder_1_out13, 1'b1, in_1);
  and and_15 (and_15_out, decoder_1_out14, 1'b1, in_1);
  and and_16 (and_16_out, decoder_1_out15, 1'b1, in_1);
  and and_17 (and_17_out, decoder_1_out16, 1'b1, in_1);
  and and_18 (and_18_out, decoder_1_out17, 1'b1, in_1);
  and and_19 (and_19_out, decoder_1_out18, 1'b1, in_1);
  and and_20 (and_20_out, decoder_1_out19, 1'b1, in_1);
  and and_21 (and_21_out, decoder_1_out20, 1'b1, in_1);
  and and_22 (and_22_out, decoder_1_out21, 1'b1, in_1);
  and and_23 (and_23_out, decoder_1_out22, 1'b1, in_1);
  and and_24 (and_24_out, decoder_1_out23, 1'b1, in_1);
  and and_25 (and_25_out, decoder_1_out24, 1'b1, in_1);
  and and_26 (and_26_out, decoder_1_out25, 1'b1, in_1);
  and and_27 (and_27_out, decoder_1_out26, 1'b1, in_1);
  and and_28 (and_28_out, decoder_1_out27, 1'b1, in_1);
  and and_29 (and_29_out, decoder_1_out28, 1'b1, in_1);
  and and_30 (and_30_out, decoder_1_out29, 1'b1, in_1);
  and and_31 (and_31_out, decoder_1_out30, 1'b1, in_1);
  and and_32 (and_32_out, decoder_1_out31, 1'b1, in_1);
  Register #(.width(32), .Select("low")) register_1 (
    .D({32{1'b0}}), .en(and_1_out), .Q(register_1_q), .clk(in_6));  // open: clr
  Register #(.width(32), .Select("low")) register_2 (
    .D(in_3), .en(and_2_out), .Q(register_2_q), .clk(in_6));  // open: clr
  Register #(.width(32), .Select("low")) register_3 (
    .D(in_3), .en(and_3_out), .Q(register_3_q), .clk(in_6));  // open: clr
  Register #(.width(32), .Select("low")) register_4 (
    .D(in_3), .en(and_4_out), .Q(register_4_q), .clk(in_6));  // open: clr
  Register #(.width(32), .Select("low")) register_5 (
    .D(in_3), .en(and_5_out), .Q(register_5_q), .clk(in_6));  // open: clr
  Register #(.width(32), .Select("low")) register_6 (
    .D(in_3), .en(and_6_out), .Q(register_6_q), .clk(in_6));  // open: clr
  Register #(.width(32), .Select("low")) register_7 (
    .D(in_3), .en(and_7_out), .Q(register_7_q), .clk(in_6));  // open: clr
  Register #(.width(32), .Select("low")) register_8 (
    .D(in_3), .en(and_8_out), .Q(register_8_q), .clk(in_6));  // open: clr
  Register #(.width(32), .Select("low")) register_9 (
    .D(in_3), .en(and_9_out), .Q(register_9_q), .clk(in_6));  // open: clr
  Register #(.width(32), .Select("low")) register_10 (
    .D(in_3), .en(and_10_out), .Q(register_10_q), .clk(in_6));  // open: clr
  Register #(.width(32), .Select("low")) register_11 (
    .D(in_3), .en(and_11_out), .Q(register_11_q), .clk(in_6));  // open: clr
  Register #(.width(32), .Select("low")) register_12 (
    .D(in_3), .en(and_12_out), .Q(register_12_q), .clk(in_6));  // open: clr
  Register #(.width(32), .Select("low")) register_13 (
    .D(in_3), .en(and_13_out), .Q(register_13_q), .clk(in_6));  // open: clr
  Register #(.width(32), .Select("low")) register_14 (
    .D(in_3), .en(and_14_out), .Q(register_14_q), .clk(in_6));  // open: clr
  Register #(.width(32), .Select("low")) register_15 (
    .D(in_3), .en(and_15_out), .Q(register_15_q), .clk(in_6));  // open: clr
  Register #(.width(32), .Select("low")) register_16 (
    .D(in_3), .en(and_16_out), .Q(register_16_q), .clk(in_6));  // open: clr
  Register #(.width(32), .Select("low")) register_17 (
    .D(in_3), .en(and_17_out), .Q(register_17_q), .clk(in_6));  // open: clr
  Register #(.width(32), .Select("low")) register_18 (
    .D(in_3), .en(and_18_out), .Q(register_18_q), .clk(in_6));  // open: clr
  Register #(.width(32), .Select("low")) register_19 (
    .D(in_3), .en(and_19_out), .Q(register_19_q), .clk(in_6));  // open: clr
  Register #(.width(32), .Select("low")) register_20 (
    .D(in_3), .en(and_20_out), .Q(register_20_q), .clk(in_6));  // open: clr
  Register #(.width(32), .Select("low")) register_21 (
    .D(in_3), .en(and_21_out), .Q(register_21_q), .clk(in_6));  // open: clr
  Register #(.width(32), .Select("low")) register_22 (
    .D(in_3), .en(and_22_out), .Q(register_22_q), .clk(in_6));  // open: clr
  Register #(.width(32), .Select("low")) register_23 (
    .D(in_3), .en(and_23_out), .Q(register_23_q), .clk(in_6));  // open: clr
  Register #(.width(32), .Select("low")) register_24 (
    .D(in_3), .en(and_24_out), .Q(register_24_q), .clk(in_6));  // open: clr
  Register #(.width(32), .Select("low")) register_25 (
    .D(in_3), .en(and_25_out), .Q(register_25_q), .clk(in_6));  // open: clr
  Register #(.width(32), .Select("low")) register_26 (
    .D(in_3), .en(and_26_out), .Q(register_26_q), .clk(in_6));  // open: clr
  Register #(.width(32), .Select("low")) register_27 (
    .D(in_3), .en(and_27_out), .Q(register_27_q), .clk(in_6));  // open: clr
  Register #(.width(32), .Select("low")) register_28 (
    .D(in_3), .en(and_28_out), .Q(register_28_q), .clk(in_6));  // open: clr
  Register #(.width(32), .Select("low")) register_29 (
    .D(in_3), .en(and_29_out), .Q(register_29_q), .clk(in_6));  // open: clr
  Register #(.width(32), .Select("low")) register_30 (
    .D(in_3), .en(and_30_out), .Q(register_30_q), .clk(in_6));  // open: clr
  Register #(.width(32), .Select("low")) register_31 (
    .D(in_3), .en(and_31_out), .Q(register_31_q), .clk(in_6));  // open: clr
  Register #(.width(32), .Select("low")) register_32 (
    .D(in_3), .en(and_32_out), .Q(register_32_q), .clk(in_6));  // open: clr
  Multiplexer #(.select(5), .width(32), .enable("false")) multiplexer_1 (
    .in0(register_1_q), .in1(register_2_q), .in2(register_3_q), .in3(register_4_q), .in4(register_5_q),
    .in5(register_6_q), .in6(register_7_q), .in7(register_8_q), .in8(register_9_q), .in9(register_10_q),
    .in10(register_11_q), .in11(register_12_q), .in12(register_13_q), .in13(register_14_q),
    .in14(register_15_q), .in15(register_16_q), .in16(register_17_q), .in17(register_18_q),
    .in18(register_19_q), .in19(register_20_q), .in20(register_21_q), .in21(register_22_q),
    .in22(register_23_q), .in23(register_24_q), .in24(register_25_q), .in25(register_26_q),
    .in26(register_27_q), .in27(register_28_q), .in28(register_29_q), .in29(register_30_q),
    .in30(register_31_q), .in31(register_32_q), .out(out_8), .sel(in_4));
  Multiplexer #(.select(5), .width(32), .enable("false")) multiplexer_2 (
    .in0(register_1_q), .in1(register_2_q), .in2(register_3_q), .in3(register_4_q), .in4(register_5_q),
    .in5(register_6_q), .in6(register_7_q), .in7(register_8_q), .in8(register_9_q), .in9(register_10_q),
    .in10(register_11_q), .in11(register_12_q), .in12(register_13_q), .in13(register_14_q),
    .in14(register_15_q), .in15(register_16_q), .in16(register_17_q), .in17(register_18_q),
    .in18(register_19_q), .in19(register_20_q), .in20(register_21_q), .in21(register_22_q),
    .in22(register_23_q), .in23(register_24_q), .in24(register_25_q), .in25(register_26_q),
    .in26(register_27_q), .in27(register_28_q), .in28(register_29_q), .in29(register_30_q),
    .in30(register_31_q), .in31(register_32_q), .out(out_7), .sel(in_2));

  // Other names for the same wires on the sheet: BUSA[31:0] = out_7; BUSB[31:0] = out_8; CLK = in_6; RA[4:0] = in_2;
  //   RB[4:0] = in_4; RW[4:0] = in_5; WE = in_1; WRITE[31:0] = in_3
endmodule

module \IDU电路  (
  input  [31:0] in_1,
  input  [31:0] in_2,
  input  [31:0] in_3,
  input  [2:0] in_4,
  input  in_5,
  input  in_6,
  input  [1:0] in_7,
  output [31:0] out_8,
  output [31:0] out_9,
  output [31:0] out_10,
  output [6:0] out_11,
  output [6:0] out_12,
  output [2:0] out_13,
  output [31:0] out_14,
  output [31:0] out_15
);

  wire CLK, not_1_out;

  Clock clock_1 (.out(CLK));
  \立即数扩展器  \u_立即数扩展器_1  (.in_1(in_1), .out_3(out_15), .in_2(in_4));
  \寄存器堆  \u_寄存器堆_1  (
    .in_1(in_5), .in_2(in_1[19:15]), .in_3(in_2), .out_7(out_10), .out_8(out_14), .in_4(in_1[24:20]),
    .in_5(in_1[11:7]), .in_6(CLK));
  Multiplexer #(.width(32), .enable("false")) multiplexer_1 (.in0(in_3), .in1(out_10), .out(out_8), .sel(not_1_out));
  not not_1 (not_1_out, in_6);
  Multiplexer #(.select(2), .width(32), .enable("false")) multiplexer_2 (
    .in0(out_14), .in1(32'h4), .in2(out_15), .out(out_9), .sel(in_7));  // open: in3

  assign out_11 = in_1[6:0];
  assign out_12 = in_1[31:25];
  assign out_13 = in_1[14:12];

  // Other names for the same wires on the sheet: ALUASrc = in_6; ALUBSrc[1:0] = in_7; BusA[31:0] = out_10;
  //   BusW[31:0] = in_2; DataA[31:0] = out_8; DataB[31:0] = out_9; DataIn[31:0] = out_14; ExtOp[2:0] = in_4;
  //   imm[31:0] = out_15; IR[31:0] = in_1; OP[6:0] = in_1[6:0]; rd[4:0] = in_1[11:7]; func3[2:0] = in_1[14:12];
  //   rs1[4:0] = in_1[19:15]; rs2[4:0] = in_1[24:20]; func7[6:0] = in_1[31:25]; PC[31:0] = in_3; RegWr = in_5

  // Notes on the sheet:
  //                         也就是BusB,Din
endmodule

module DataPath (
  input  [2:0] in_1,
  input  [2:0] in_2,
  input  in_3,
  input  in_4,
  input  in_5,
  input  [1:0] in_6,
  input  [31:0] in_7,
  input  in_8,
  input  [3:0] in_9,
  input  in_10,
  input  [2:0] in_11,
  input  in_12,
  output [6:0] out_13,
  output [2:0] out_14,
  output [6:0] out_15
);

  wire branch_1_out_4, branch_1_out_5, CLK, \n32位alu_1_out_5 , not_1_out, not_2_out;
  wire [15:0] \ifu实验_1_out_9_2 ;
  wire [31:0] \idu电路_1_out_8 , \idu电路_1_out_9 , \idu电路_1_out_10 , \idu电路_1_out_14 , \idu电路_1_out_15 ,
       \ifu实验_1_out_9 , multiplexer_1_out, \n32位alu_1_out_4 , rom_1_data, \数据存储器实验_1_out_8 ;

  Clock clock_1 (.out(CLK));
  Button button_1 ();  // open: out
  \IFU实验  \ifu实验_1  (
    .in_4(CLK), .in_5(in_12), .in_6(in_10), .in_7(branch_1_out_4), .in_8(branch_1_out_5), .in_1(in_7),
    .in_2(\idu电路_1_out_15 ), .in_3(\idu电路_1_out_10 ),
    .out_9({\ifu实验_1_out_9 [31:18], \ifu实验_1_out_9_2 , \ifu实验_1_out_9 [1:0]}));  // open: out_10
  // Probe on {\ifu实验_1_out_9 [31:18], \ifu实验_1_out_9_2 , \ifu实验_1_out_9 [1:0]}
  not not_1 (not_1_out, in_12);
  ROM #(.addrWidth(16), .dataWidth(32), .Select("high")) rom_1 (
    .addr(\ifu实验_1_out_9_2 ), .data(rom_1_data), .sel(not_1_out));
  // Probe on multiplexer_1_out
  // Probe on \idu电路_1_out_15 
  // Probe on \idu电路_1_out_8 
  \IDU电路  \idu电路_1  (
    .in_4(in_1), .in_5(in_3), .out_11(out_13), .in_6(in_4), .in_7(in_6), .out_12(out_15), .out_13(out_14),
    .in_1(rom_1_data), .in_2(multiplexer_1_out),
    .in_3({\ifu实验_1_out_9 [31:18], \ifu实验_1_out_9_2 , \ifu实验_1_out_9 [1:0]}), .out_8(\idu电路_1_out_8 ),
    .out_14(\idu电路_1_out_14 ), .out_9(\idu电路_1_out_9 ), .out_15(\idu电路_1_out_15 ), .out_10(\idu电路_1_out_10 ));
  // Probe on \idu电路_1_out_9 
  \_32位ALU  \u_32位alu_1  (
    .in_2(\idu电路_1_out_8 ), .in_3(\idu电路_1_out_9 ), .out_4(\n32位alu_1_out_4 ), .out_5(\n32位alu_1_out_5 ),
    .in_1(in_9));
  not not_2 (not_2_out, in_12);
  // Probe on \n32位alu_1_out_4 
  Branch branch_1 (
    .in_1(in_11), .out_4(branch_1_out_4), .in_2(\n32位alu_1_out_5 ), .out_5(branch_1_out_5),
    .in_3(\n32位alu_1_out_4 [0]));
  \数据存储器实验  \u_数据存储器实验_1  (
    .in_1(\n32位alu_1_out_4 [17:2]), .in_2(\idu电路_1_out_14 ), .out_8(\数据存储器实验_1_out_8 ), .in_3(CLK),
    .in_5(in_5), .in_6(not_2_out), .in_7(in_2));  // open: in_4
  // Probe on \数据存储器实验_1_out_8 
  Multiplexer #(.width(32), .enable("false")) multiplexer_1 (
    .in0(\n32位alu_1_out_4 ), .in1(\数据存储器实验_1_out_8 ), .out(multiplexer_1_out), .sel(in_8));

  // Other names for the same wires on the sheet: ALUASrc = in_4; ALUBSrc[1:0] = in_6; ALUctr[3:0] = in_9;
  //   Branch[2:0] = in_11; ExtOp[2:0] = in_1; Func3[2:0] = out_14; Func7[6:0] = out_15; Halt = in_10;
  //   Init_Addr[31:0] = in_7; MemOp[2:0] = in_2; MemToReg = in_8; MemWr = in_5; Op[6:0] = out_13; RegWr = in_3;
  //   RESET = in_12

  // Notes on the sheet:
  //   PC
  //   contents of rom_1 (hex, n*v repeats v):
  //   fffff2b7 6428293 502023 4032d313 602223 401383 fff3c413 802423 7424b3 902623 fc049ce3 3000567 a02823
  //   64597
  //         BusW
  //        Imm
  //             数据存储器
endmodule

module \跑马灯  (
  input  [2:0] in_1,
  input  in_2,
  input  SEL
);

  wire comparator_1_eq;
  wire [2:0] adder_1_out, adder_2_out, Count;
  wire [7:0] \ascii码显示实验_1_out_3 , \ascii码显示实验_1_out_4 , \ascii码显示实验_1_out_5 , \ascii码显示实验_1_out_6 ,
       \ascii码显示实验_1_out_7 , \ascii码显示实验_1_out_8 , \ascii码显示实验_1_out_9 , \ascii码显示实验_1_out_10 ,
       \ascii码显示实验_1_out_11 , \ascii码显示实验_1_out_12 , \ascii码显示实验_1_out_13 , \ascii码显示实验_1_out_14 ,
       \ascii码显示实验_1_out_15 , \ascii码显示实验_1_out_16 , \ascii码显示实验_1_out_17 , \ascii码显示实验_1_out_18 ,
       \ascii码显示实验_2_out_3 , \ascii码显示实验_2_out_4 , \ascii码显示实验_2_out_5 , \ascii码显示实验_2_out_6 ,
       \ascii码显示实验_2_out_7 , \ascii码显示实验_2_out_8 , \ascii码显示实验_2_out_9 , \ascii码显示实验_2_out_10 ,
       \ascii码显示实验_2_out_11 , \ascii码显示实验_2_out_12 , \ascii码显示实验_2_out_13 , \ascii码显示实验_2_out_14 ,
       \ascii码显示实验_2_out_15 , \ascii码显示实验_2_out_16 , \ascii码显示实验_2_out_17 , \ascii码显示实验_2_out_18 ,
       \ascii码显示实验_3_out_3 , \ascii码显示实验_3_out_4 , \ascii码显示实验_3_out_5 , \ascii码显示实验_3_out_6 ,
       \ascii码显示实验_3_out_7 , \ascii码显示实验_3_out_8 , \ascii码显示实验_3_out_9 , \ascii码显示实验_3_out_10 ,
       \ascii码显示实验_3_out_11 , \ascii码显示实验_3_out_12 , \ascii码显示实验_3_out_13 , \ascii码显示实验_3_out_14 ,
       \ascii码显示实验_3_out_15 , \ascii码显示实验_3_out_16 , \ascii码显示实验_3_out_17 , \ascii码显示实验_3_out_18 ,
       multiplexer_1_out, multiplexer_2_out, multiplexer_3_out;

  Comparator #(.width(3)) comparator_1 (.a(Count), .b(3'b101), .eq(comparator_1_eq));  // open: gt, lt
  Counter #(.width(3), .max('h7)) counter_1 (
    .D(in_1), .Q(Count), .clk(in_2), .clr(comparator_1_eq));  // open: load, count, carry, preset, down
  \ASCII码显示实验  \ascii码显示实验_1  (
    .in_1(multiplexer_1_out), .in_2(SEL), .out_3(\ascii码显示实验_1_out_3 ), .out_4(\ascii码显示实验_1_out_4 ),
    .out_5(\ascii码显示实验_1_out_5 ), .out_6(\ascii码显示实验_1_out_6 ), .out_7(\ascii码显示实验_1_out_7 ),
    .out_8(\ascii码显示实验_1_out_8 ), .out_9(\ascii码显示实验_1_out_9 ), .out_10(\ascii码显示实验_1_out_10 ),
    .out_11(\ascii码显示实验_1_out_11 ), .out_12(\ascii码显示实验_1_out_12 ), .out_13(\ascii码显示实验_1_out_13 ),
    .out_14(\ascii码显示实验_1_out_14 ), .out_15(\ascii码显示实验_1_out_15 ), .out_16(\ascii码显示实验_1_out_16 ),
    .out_17(\ascii码显示实验_1_out_17 ), .out_18(\ascii码显示实验_1_out_18 ));
  Multiplexer #(.select(3), .width(8), .enable("false")) multiplexer_1 (
    .in0(8'h2e), .in1(8'h2a), .in2(8'h35), .in3(8'h23), .in4(8'h33), .in5(8'h2e), .in6(8'h2a), .in7(8'h35),
    .out(multiplexer_1_out), .sel(Count));
  DotMatrix #(.inputtype("row"), .matrixcols(8), .matrixrows(16)) dotmatrix_1 (
    .row0(\ascii码显示实验_1_out_3 ), .row1(\ascii码显示实验_1_out_4 ), .row2(\ascii码显示实验_1_out_5 ),
    .row3(\ascii码显示实验_1_out_6 ), .row4(\ascii码显示实验_1_out_7 ), .row5(\ascii码显示实验_1_out_8 ),
    .row6(\ascii码显示实验_1_out_9 ), .row7(\ascii码显示实验_1_out_10 ), .row8(\ascii码显示实验_1_out_11 ),
    .row9(\ascii码显示实验_1_out_12 ), .row10(\ascii码显示实验_1_out_13 ), .row11(\ascii码显示实验_1_out_14 ),
    .row12(\ascii码显示实验_1_out_15 ), .row13(\ascii码显示实验_1_out_16 ), .row14(\ascii码显示实验_1_out_17 ),
    .row15(\ascii码显示实验_1_out_18 ));
  Adder #(.width(3)) adder_1 (.a(Count), .b(3'b001), .out(adder_1_out));  // open: cin, cout
  DotMatrix #(.inputtype("row"), .matrixcols(8), .matrixrows(16)) dotmatrix_2 (
    .row0(\ascii码显示实验_2_out_3 ), .row1(\ascii码显示实验_2_out_4 ), .row2(\ascii码显示实验_2_out_5 ),
    .row3(\ascii码显示实验_2_out_6 ), .row4(\ascii码显示实验_2_out_7 ), .row5(\ascii码显示实验_2_out_8 ),
    .row6(\ascii码显示实验_2_out_9 ), .row7(\ascii码显示实验_2_out_10 ), .row8(\ascii码显示实验_2_out_11 ),
    .row9(\ascii码显示实验_2_out_12 ), .row10(\ascii码显示实验_2_out_13 ), .row11(\ascii码显示实验_2_out_14 ),
    .row12(\ascii码显示实验_2_out_15 ), .row13(\ascii码显示实验_2_out_16 ), .row14(\ascii码显示实验_2_out_17 ),
    .row15(\ascii码显示实验_2_out_18 ));
  \ASCII码显示实验  \ascii码显示实验_2  (
    .in_1(multiplexer_2_out), .in_2(SEL), .out_3(\ascii码显示实验_2_out_3 ), .out_4(\ascii码显示实验_2_out_4 ),
    .out_5(\ascii码显示实验_2_out_5 ), .out_6(\ascii码显示实验_2_out_6 ), .out_7(\ascii码显示实验_2_out_7 ),
    .out_8(\ascii码显示实验_2_out_8 ), .out_9(\ascii码显示实验_2_out_9 ), .out_10(\ascii码显示实验_2_out_10 ),
    .out_11(\ascii码显示实验_2_out_11 ), .out_12(\ascii码显示实验_2_out_12 ), .out_13(\ascii码显示实验_2_out_13 ),
    .out_14(\ascii码显示实验_2_out_14 ), .out_15(\ascii码显示实验_2_out_15 ), .out_16(\ascii码显示实验_2_out_16 ),
    .out_17(\ascii码显示实验_2_out_17 ), .out_18(\ascii码显示实验_2_out_18 ));
  Multiplexer #(.select(3), .width(8), .enable("false")) multiplexer_2 (
    .in0(8'h2e), .in1(8'h2a), .in2(8'h35), .in3(8'h23), .in4(8'h33), .in5(8'h2e), .in6(8'h2a), .in7(8'h35),
    .out(multiplexer_2_out), .sel(adder_1_out));
  Adder #(.width(3)) adder_2 (.a(Count), .b(3'b010), .out(adder_2_out));  // open: cin, cout
  DotMatrix #(.inputtype("row"), .matrixcols(8), .matrixrows(16)) dotmatrix_3 (
    .row0(\ascii码显示实验_3_out_3 ), .row1(\ascii码显示实验_3_out_4 ), .row2(\ascii码显示实验_3_out_5 ),
    .row3(\ascii码显示实验_3_out_6 ), .row4(\ascii码显示实验_3_out_7 ), .row5(\ascii码显示实验_3_out_8 ),
    .row6(\ascii码显示实验_3_out_9 ), .row7(\ascii码显示实验_3_out_10 ), .row8(\ascii码显示实验_3_out_11 ),
    .row9(\ascii码显示实验_3_out_12 ), .row10(\ascii码显示实验_3_out_13 ), .row11(\ascii码显示实验_3_out_14 ),
    .row12(\ascii码显示实验_3_out_15 ), .row13(\ascii码显示实验_3_out_16 ), .row14(\ascii码显示实验_3_out_17 ),
    .row15(\ascii码显示实验_3_out_18 ));
  \ASCII码显示实验  \ascii码显示实验_3  (
    .in_1(multiplexer_3_out), .in_2(SEL), .out_3(\ascii码显示实验_3_out_3 ), .out_4(\ascii码显示实验_3_out_4 ),
    .out_5(\ascii码显示实验_3_out_5 ), .out_6(\ascii码显示实验_3_out_6 ), .out_7(\ascii码显示实验_3_out_7 ),
    .out_8(\ascii码显示实验_3_out_8 ), .out_9(\ascii码显示实验_3_out_9 ), .out_10(\ascii码显示实验_3_out_10 ),
    .out_11(\ascii码显示实验_3_out_11 ), .out_12(\ascii码显示实验_3_out_12 ), .out_13(\ascii码显示实验_3_out_13 ),
    .out_14(\ascii码显示实验_3_out_14 ), .out_15(\ascii码显示实验_3_out_15 ), .out_16(\ascii码显示实验_3_out_16 ),
    .out_17(\ascii码显示实验_3_out_17 ), .out_18(\ascii码显示实验_3_out_18 ));
  Multiplexer #(.select(3), .width(8), .enable("false")) multiplexer_3 (
    .in0(8'h2e), .in1(8'h2a), .in2(8'h35), .in3(8'h23), .in4(8'h33), .in5(8'h2e), .in6(8'h2a), .in7(8'h35),
    .out(multiplexer_3_out), .sel(adder_2_out));
endmodule
