// Logisim project 实验6.circ as structural Verilog: 2 circuits, main circuit 控制器
module \控制器  (
  input  [6:0] in_1,
  input  [2:0] in_2,
  input  [6:0] in_3,
  output [2:0] out_4,
  output out_5,
  output out_6,
  output [1:0] out_7,
  output [3:0] out_8,
  output [2:0] out_9,
  output out_10,
  output [2:0] out_11,
  output out_12,
  output out_13
);

  wire and_1_out, and_2_out, and_3_out, and_4_out, and_5_out, and_6_out, and_7_out, and_8_out, and_9_out,
       and_12_out, and_13_out, comparator_7_eq, comparator_8_eq, comparator_13_eq, comparator_14_eq,
       comparator_15_lt, comparator_16_eq, I_Arith, J_jalr, or_3_out, or_7_out, or_8_out, or_9_out,
       or_10_out, or_15_out, or_16_out, or_17_out, R_Arith, U_auipc, U_lui;

  or or_1 (out_4[0], U_lui, U_auipc, out_9[2]);
  or or_2 (out_4[1], out_9[2], out_12);
  or or_3 (or_3_out, out_9[2], out_12);
  or or_4 (out_7[0], out_4[2], J_jalr);
  Comparator #(.width(7)) comparator_1 (.a(in_1), .b(7'b0110111), .eq(U_lui));  // open: gt, lt
  Comparator #(.width(7)) comparator_2 (.a(in_1), .b(7'b1100111), .eq(J_jalr));  // open: gt, lt
  not not_1 (out_5, or_3_out);
  or or_5 (out_6, U_auipc, out_4[2], J_jalr);
  or or_6 (out_7[1], U_lui, U_auipc, I_Arith, out_10, out_12);
  Comparator #(.width(7)) comparator_3 (.a(in_1), .b(7'b0010111), .eq(U_auipc));  // open: gt, lt
  Comparator #(.width(7)) comparator_4 (.a(in_1), .b(7'b1100011), .eq(out_9[2]));  // open: gt, lt
  Comparator #(.width(7)) comparator_5 (.a(in_1), .b(7'b0010011), .eq(I_Arith));  // open: gt, lt
  Comparator #(.width(7)) comparator_6 (.a(in_1), .b(7'b0000011), .eq(out_10));  // open: gt, lt
  and and_1 (and_1_out, I_Arith, comparator_7_eq);
  Comparator #(.width(3)) comparator_7 (.a(in_2), .b(3'b101), .eq(comparator_7_eq));  // open: gt, lt
  or or_7 (or_7_out, I_Arith, R_Arith);
  and and_2 (and_2_out, or_7_out, in_2[2]);
  or or_8 (or_8_out, I_Arith, R_Arith);
  and and_3 (and_3_out, or_8_out, in_2[1]);
  or or_9 (or_9_out, I_Arith, R_Arith);
  and and_4 (and_4_out, or_9_out, in_2[0]);
  and and_5 (and_5_out, out_9[2], comparator_8_eq);
  Comparator #(.width(2)) comparator_8 (.a(in_2[2:1]), .b(2'b11), .eq(comparator_8_eq));  // open: gt, lt
  or or_10 (or_10_out, and_1_out, R_Arith);
  Comparator #(.width(7)) comparator_9 (.a(in_1), .b(7'b0110011), .eq(R_Arith));  // open: gt, lt
  Comparator #(.width(7)) comparator_10 (.a(in_1), .b(7'b0100011), .eq(out_12));  // open: gt, lt
  or or_11 (out_8[3], U_lui, and_6_out);
  and and_6 (and_6_out, or_10_out, in_3[5]);
  or or_12 (out_8[2], U_lui, and_2_out);
  or or_13 (out_8[1], U_lui, and_3_out, out_9[2]);
  or or_14 (out_8[0], U_lui, and_4_out, and_5_out);
  Comparator #(.width(7)) comparator_11 (.a(in_1), .b(7'b1101111), .eq(out_4[2]));  // open: gt, lt
  Comparator #(.width(7)) comparator_12 (.a(in_1), .b({7{1'b0}}), .eq(out_13));  // open: gt, lt
  Comparator #(.width(3), .mode("unsigned")) comparator_13 (
    .a(in_2), .b(3'b000), .eq(comparator_13_eq));  // open: gt, lt
  Comparator #(.width(3), .mode("unsigned")) comparator_14 (
    .a(in_2), .b(3'b100), .eq(comparator_14_eq));  // open: gt, lt
  and and_7 (and_7_out, out_9[2], in_2[2]);
  and and_8 (and_8_out, out_9[2], in_2[0]);
  or or_15 (or_15_out, out_10, out_12);
  Comparator #(.width(3), .mode("unsigned")) comparator_15 (
    .a(in_2), .b(3'b010), .lt(comparator_15_lt));  // open: gt, eq
  or or_16 (or_16_out, out_10, out_12);
  and and_9 (and_9_out, in_2[0], 1'b1);
  or or_17 (or_17_out, comparator_13_eq, comparator_14_eq);
  Comparator #(.width(3), .mode("unsigned")) comparator_16 (
    .a(in_2), .b(3'b000), .eq(comparator_16_eq));  // open: gt, lt
  or or_18 (out_9[1], and_7_out, J_jalr);
  or or_19 (out_9[0], and_8_out, out_4[2]);
  and and_10 (out_11[2], or_15_out, comparator_15_lt);
  and and_11 (out_11[1], or_16_out, and_9_out);
  and and_12 (and_12_out, out_10, or_17_out);
  or or_20 (out_11[0], and_12_out, and_13_out);
  and and_13 (and_13_out, out_12, comparator_16_eq);

  // Other names for the same wires on the sheet: ALUASrc = out_6; ALUBSrc[1:0] = out_7; ALUctr[3:0] = out_8;
  //   Branch[2:0] = out_9; B_Instr = out_9[2]; ExtOp[2:0] = out_4; J_jal = out_4[2]; funct3[2:0] = in_2;
  //   funct7[6:0] = in_3; halt = out_13; MemOp[2:0] = out_11; I_load = out_10; MemToReg = out_10; Opcode[6:0] = in_1;
  //   RegWr = out_5; MemWr = out_12; S_Instr = out_12

  // Notes on the sheet:
  //   ExtOp[2]:仅有jal是1
  //   ExtOp[1]:B或S是1
  //   ExtOp[0]:lui auipc B是1
  //   RegWr：B或S才是0
  //   ALUASrc:只有auipc jal jalr是1
  //   ALUBSrc[1]:U I S-->1
  //   ALUBSrc[0]: jal jalr是1
  //   ALUctr[3]: lui   (I+func3=101或R)&func75=1
  //   ALUctr：
  //   ALUctr[2] lui 或IArith RArith中func3[2]==1的
  //   ALUctr[1] lui 或IArith RArith中func3[1]==1 或 B
  //   ALUctr[0] lui 或IArith RArith中func3[0]==1 或 Band func3[2:1]==11
  //   Branch
  //   Branch[2]: B
  //   MemToReg：I-load
  //   MemWr: S
  //   MemOp
  //   MemOp[2] (I or S) and func3<2
  //   MemOp[1]   (I or S) and func3[0]==1
  //   Branch[1]:B and func3[2]=1  or  jalr
  //   Branch[0]:B and func3[0]=1  or  jal
  //   MemOp[0]   (I and (func3=000 or func3=100)) or (S and func3==000)
endmodule

module \单周期CPU  (
  input  [31:0] in_1,
  output out_2
);

  wire branch_1_out_4, branch_1_out_5, CLK, clock_2_out, comparator_1_eq, \n32位alu_1_out_5 , not_1_out,
       not_2_out, or_1_out, RESET, \控制器_1_out_5 , \控制器_1_out_6 , \控制器_1_out_10 , \控制器_1_out_12 ;
  wire [1:0] \控制器_1_out_7 ;
  wire [2:0] \idu电路_1_out_13 , \控制器_1_out_4 , \控制器_1_out_9 , \控制器_1_out_11 ;
  wire [3:0] \控制器_1_out_8 ;
  wire [6:0] \idu电路_1_out_11 , \idu电路_1_out_12 ;
  wire [15:0] counter_1_q;
  wire [31:0] \idu电路_1_out_8 , \idu电路_1_out_9 , \idu电路_1_out_10 , \idu电路_1_out_14 , \idu电路_1_out_15 ,
       \ifu实验_1_out_9 , IR, multiplexer_1_out, \n32位alu_1_out_4 , \数据存储器实验_1_out_8 ;

  // Probe on \idu电路_1_out_15 
  Clock clock_1 (.out(CLK));
  Button button_1 (.out(RESET));
  \IFU实验  \ifu实验_1  (
    .in_4(CLK), .in_5(RESET), .in_6(out_2), .in_7(branch_1_out_4), .in_8(branch_1_out_5), .in_1(in_1),
    .in_2(\idu电路_1_out_15 ), .in_3(\idu电路_1_out_10 ), .out_9(\ifu实验_1_out_9 ));  // open: out_10
  not not_1 (not_1_out, RESET);
  ROM #(.addrWidth(16), .dataWidth(32), .Select("high")) rom_1 (
    .addr(\ifu实验_1_out_9 [17:2]), .data(IR), .sel(not_1_out));
  \控制器  \u_控制器_1  (
    .in_1(\idu电路_1_out_11 ), .out_4(\控制器_1_out_4 ), .out_5(\控制器_1_out_5 ), .in_2(\idu电路_1_out_13 ),
    .out_6(\控制器_1_out_6 ), .out_7(\控制器_1_out_7 ), .in_3(\idu电路_1_out_12 ), .out_8(\控制器_1_out_8 ),
    .out_9(\控制器_1_out_9 ), .out_10(\控制器_1_out_10 ), .out_11(\控制器_1_out_11 ), .out_12(\控制器_1_out_12 ),
    .out_13(out_2));
  Comparator #(.width(32)) comparator_1 (.a(IR), .b(32'h6f), .eq(comparator_1_eq));  // open: gt, lt
  // Probe on \idu电路_1_out_8 
  \IDU电路  \idu电路_1  (
    .in_4(\控制器_1_out_4 ), .in_5(\控制器_1_out_5 ), .out_11(\idu电路_1_out_11 ), .in_6(\控制器_1_out_6 ),
    .in_7(\控制器_1_out_7 ), .out_12(\idu电路_1_out_12 ), .out_13(\idu电路_1_out_13 ), .in_1(IR),
    .in_2(multiplexer_1_out), .in_3(\ifu实验_1_out_9 ), .out_8(\idu电路_1_out_8 ), .out_14(\idu电路_1_out_14 ),
    .out_9(\idu电路_1_out_9 ), .out_15(\idu电路_1_out_15 ), .out_10(\idu电路_1_out_10 ));
  // Probe on \idu电路_1_out_9 
  not not_2 (not_2_out, or_1_out);
  or or_1 (or_1_out, out_2, comparator_1_eq);
  \_32位ALU  \u_32位alu_1  (
    .in_2(\idu电路_1_out_8 ), .in_3(\idu电路_1_out_9 ), .out_4(\n32位alu_1_out_4 ), .out_5(\n32位alu_1_out_5 ),
    .in_1(\控制器_1_out_8 ));
  // Probe on counter_1_q
  Counter #(.width(16), .max('hffff), .behavior("old")) counter_1 (
    .count(not_2_out), .Q(counter_1_q), .clk(clock_2_out));  // open: load, D, carry, clr, preset
  Clock clock_2 (.out(clock_2_out));
  Branch branch_1 (
    .in_1(\控制器_1_out_9 ), .out_4(branch_1_out_4), .in_2(\n32位alu_1_out_5 ), .out_5(branch_1_out_5),
    .in_3(\n32位alu_1_out_4 [0]));
  // Probe on \n32位alu_1_out_4 
  \数据存储器实验  \u_数据存储器实验_1  (
    .in_1(\n32位alu_1_out_4 [17:2]), .in_2(\idu电路_1_out_14 ), .out_8(\数据存储器实验_1_out_8 ), .in_3(CLK),
    .in_5(\控制器_1_out_12 ), .in_6(not_1_out), .in_7(\控制器_1_out_11 ));  // open: in_4
  Multiplexer #(.width(32), .enable("false")) multiplexer_1 (
    .in0(\n32位alu_1_out_4 ), .in1(\数据存储器实验_1_out_8 ), .out(multiplexer_1_out), .sel(\控制器_1_out_10 ));
  // Probe on multiplexer_1_out
  // Probe on \数据存储器实验_1_out_8 

  // Other names for the same wires on the sheet: Halt = out_2; Init_Addr[31:0] = in_1

  // Notes on the sheet:
  //   imm
  //   contents of rom_1 (hex, n*v repeats v):
  //   2503 100613 6b3 c686b3 a60663 160613 ff5ff06f d02423 6f
  //   busw
endmodule
